// Logisim project MipsOnBusCpu-1.circ as structural Verilog: 15 circuits, main circuit ◇指令译码器
module \单总线CPU_微程序  (
  output [21:0] \控制总线 
);

  wire and_1_out, CLK, comparator_1_eq, comparator_2_eq, equal, mips_alu_1_equal, not_1_out;
  wire [4:0] registerfile_1_p4, registerfile_1_p5, \微地址_状态 ;
  wire [11:0] Clks, \指令数 ;
  wire [31:0] AR_q, bit_extender_1_out, controlled_buffer_1_out, controlled_buffer_3_out, DR_q, IR,
       mips_alu_1_result, PC_q, ram_1_data, registerfile_1_p6, shifter_1_out, X_q, Z_q, \内部总线 ;

  // Probe on Clks
  Register #(.width(32), .trigger("rising"), .Select("low")) AR (
    .D(\内部总线 ), .en(\控制总线 [13]), .Q(AR_q), .clk(CLK));  // open: clr
  // Probe on controlled_buffer_3_out
  // Mips_Probe mips_probe_1: pin names not known; wires that end beside it: IR
  Register #(.width(32), .trigger("rising"), .Select("low")) X (
    .D(\内部总线 ), .en(\控制总线 [10]), .Q(X_q), .clk(CLK));  // open: clr
  // Probe on \指令数 
  RAM #(.addrWidth(10), .dataWidth(32), .bus("separate"), .Select("high")) ram_1 (
    .addr(AR_q[11:2]), .din(controlled_buffer_3_out), .data(ram_1_data), .str(\控制总线 [0]), .clk(CLK),
    .ld(\控制总线 [1]));  // open: sel, clr
  MIPS_ALU mips_alu_1 (
    .X(X_q), .Y(\内部总线 ), .Equal(mips_alu_1_equal), .Result(mips_alu_1_result), .ADD(\控制总线 [4]),
    .ADD4(\控制总线 [3]), .SLT(\控制总线 [2]));  // open: SUB
  assign controlled_buffer_1_out = \控制总线 [11] ? \内部总线  : 32'bz;  // Controlled_Buffer controlled_buffer_1
  assign controlled_buffer_1_out = \控制总线 [12] ? ram_1_data : 32'bz;  // Controlled_Buffer controlled_buffer_2
  assign controlled_buffer_3_out = \控制总线 [15] ? DR_q : 32'bz;  // Controlled_Buffer controlled_buffer_3
  // Probe on \内部总线 
  Register #(.width(32), .trigger("rising"), .Select("low")) PC (
    .D(\内部总线 ), .en(\控制总线 [14]), .Q(PC_q), .clk(CLK));  // open: clr
  Register #(.width(32), .trigger("rising"), .Select("low")) DR (
    .D(controlled_buffer_1_out), .Q(DR_q), .clk(CLK));  // open: en, clr
  Register #(.width(1), .trigger("rising"), .Select("low")) PSW (
    .D(mips_alu_1_equal), .en(\控制总线 [7]), .Q(equal), .clk(CLK));  // open: clr
  Register #(.width(32), .trigger("rising"), .Select("low")) Z (
    .D(mips_alu_1_result), .Q(Z_q), .clk(CLK));  // open: en, clr
  assign \内部总线  = \控制总线 [21] ? PC_q : 32'bz;  // Controlled_Buffer controlled_buffer_4
  assign \内部总线  = \控制总线 [20] ? DR_q : 32'bz;  // Controlled_Buffer controlled_buffer_5
  assign \内部总线  = \控制总线 [19] ? Z_q : 32'bz;  // Controlled_Buffer controlled_buffer_6
  assign \内部总线  = \控制总线 [17] ? bit_extender_1_out : 32'bz;  // Controlled_Buffer controlled_buffer_7
  assign \内部总线  = \控制总线 [16] ? shifter_1_out : 32'bz;  // Controlled_Buffer controlled_buffer_8
  Register #(.width(32), .trigger("rising"), .Select("low")) u_IR (
    .D(\内部总线 ), .en(\控制总线 [8]), .Q(IR), .clk(CLK));  // open: clr
  Comparator #(.width(32), .mode("twosComplement")) comparator_1 (
    .a(IR), .b(32'h1000ffff), .eq(comparator_1_eq));  // open: gt, lt
  Clock #(.highDuration(1), .lowDuration(1)) clock_1 (.out(CLK));
  \微程序控制器  \u_微程序控制器_1  (.CLK(CLK), .EQUAL(equal), .mAddr(\微地址_状态 ), .ControlBus(\控制总线 ), .\指令字 (IR));
  // Probe on \微地址_状态 
  // RegisterFile registerfile_1: pin names not known; wires that end beside it: \内部总线 , CLK, \控制总线 [9], registerfile_1_p4, registerfile_1_p5, registerfile_1_p6
  not not_1 (not_1_out, comparator_1_eq);
  Counter #(.width(12), .max('hfff), .ongoal("wrap"), .trigger("rising"), .behavior("new")) counter_1 (
    .count(not_1_out), .Q(Clks), .clk(CLK));  // open: load, D, carry, clr, preset, down
  assign bit_extender_1_out = {{16{IR[15]}}, IR[15:0]};  // Bit_Extender bit_extender_1
  assign \内部总线  = \控制总线 [18] ? registerfile_1_p6 : 32'bz;  // Controlled_Buffer controlled_buffer_9
  Multiplexer #(.select(1), .width(5), .disabled("Z"), .enable("false")) multiplexer_1 (
    .in0(IR[25:21]), .in1(IR[20:16]), .out(registerfile_1_p5), .sel(\控制总线 [6]));
  Multiplexer #(.select(1), .width(5), .disabled("Z"), .enable("false")) multiplexer_2 (
    .in0(IR[20:16]), .in1(IR[15:11]), .out(registerfile_1_p4), .sel(\控制总线 [5]));
  and and_1 (and_1_out, not_1_out, comparator_2_eq);
  Comparator #(.width(5), .mode("twosComplement")) comparator_2 (
    .a(5'b00011), .b(\微地址_状态 ), .eq(comparator_2_eq));  // open: gt, lt
  Shifter #(.width(32), .shift("ll")) shifter_1 (.in(bit_extender_1_out), .\dist (5'b00010), .out(shifter_1_out));
  Counter #(.width(12), .max('hfff), .ongoal("wrap"), .trigger("rising"), .behavior("old")) counter_2 (
    .count(and_1_out), .Q(\指令数 ), .clk(CLK));  // open: load, D, carry, clr, preset

  // Other names for the same wires on the sheet: rd[4:0] = IR[15:11]; rt[4:0] = IR[20:16]; rs[4:0] = IR[25:21];
  //   Write = \控制总线 [0]; READ = \控制总线 [1]; Slt = \控制总线 [2]; Add4 = \控制总线 [3]; Add = \控制总线 [4]; RegDst = \控制总线 [5];
  //   RegTgt = \控制总线 [6]; PSWin = \控制总线 [7]; IRin = \控制总线 [8]; Rin = \控制总线 [9]; Xin = \控制总线 [10]; DRin = \控制总线 [11];
  //   DREin = \控制总线 [12]; ARin = \控制总线 [13]; PCin = \控制总线 [14]; DREout = \控制总线 [15]; IR_A_out = \控制总线 [16];
  //   IR_I_out = \控制总线 [17]; Rout = \控制总线 [18]; Zout = \控制总线 [19]; DRout = \控制总线 [20]; PCout = \控制总线 [21]

  // Notes on the sheet:
  //   单总线结构 MIPS CPU
  //   MEM
  //   外部总线
  //   内部总线
  //   微程序控制器
  //   Immediate32
  //   AddressOffset32
endmodule

// Decoder
module \指令译码器  (
  input  [31:0] IR,
  output LW,
  output SW,
  output BEQ,
  output ADDI,
  output SLT,
  output OtherInstr
);

  wire comparator_5_eq, comparator_6_eq;

  Comparator #(.width(6), .mode("twosComplement")) comparator_1 (
    .a(IR[31:26]), .b(6'b100011), .eq(LW));  // open: gt, lt
  Comparator #(.width(6), .mode("twosComplement")) comparator_2 (
    .a(IR[31:26]), .b(6'b101011), .eq(SW));  // open: gt, lt
  Comparator #(.width(6), .mode("twosComplement")) comparator_3 (
    .a(IR[31:26]), .b(6'b001000), .eq(ADDI));  // open: gt, lt
  Comparator #(.width(6), .mode("twosComplement")) comparator_4 (
    .a(IR[31:26]), .b(6'b000100), .eq(BEQ));  // open: gt, lt
  Comparator #(.width(6), .mode("twosComplement")) comparator_5 (
    .a(IR[31:26]), .b({6{1'b0}}), .eq(comparator_5_eq));  // open: gt, lt
  Comparator #(.width(6), .mode("twosComplement")) comparator_6 (
    .a(IR[5:0]), .b(6'b101010), .eq(comparator_6_eq));  // open: gt, lt
  and and_1 (SLT, comparator_5_eq, comparator_6_eq);
  nor nor_1 (OtherInstr, BEQ, SW, LW, ADDI, SLT);

  // Other names for the same wires on the sheet: FUNCT[5:0] = IR[5:0]; OP[5:0] = IR[31:26]

  // Notes on the sheet:
  //   常用常量
endmodule

// 控制器
module \微程序控制器  (
  input  EQUAL,
  input  [31:0] \指令字 ,
  input  CLK,
  output [4:0] mAddr,
  output [21:0] ControlBus
);

  wire ADDI, BEQ, LW, Other, P0, P1, P2, SLT, SW;
  wire [1:0] \条件判别测试逻辑_1_s0 ;
  wire [4:0] multiplexer_1_out, rom_1_data, \微程序入口查找逻辑_1_s0 ;

  \微程序入口查找逻辑  \u_微程序入口查找逻辑_1  (
    .LW(LW), .SW(SW), .BEQ(BEQ), .SLT(SLT), .ADDI(ADDI), .S4(\微程序入口查找逻辑_1_s0 [4]), .S3(\微程序入口查找逻辑_1_s0 [3]),
    .S2(\微程序入口查找逻辑_1_s0 [2]), .S1(\微程序入口查找逻辑_1_s0 [1]), .S0(\微程序入口查找逻辑_1_s0 [0]));
  // Probe on \微程序入口查找逻辑_1_s0 
  \条件判别测试逻辑  \u_条件判别测试逻辑_1  (.P0(P0), .P1(P1), .equal(EQUAL), .S1(\条件判别测试逻辑_1_s0 [1]), .S0(\条件判别测试逻辑_1_s0 [0]));
  Multiplexer #(.select(2), .width(5), .disabled("Z"), .enable("false")) multiplexer_1 (
    .in0(rom_1_data), .in1(\微程序入口查找逻辑_1_s0 ), .in2(5'b10000), .out(multiplexer_1_out), .sel(\条件判别测试逻辑_1_s0 ));  // open: in3
  Register #(.width(5), .trigger("falling"), .Select("low")) register_1 (
    .D(multiplexer_1_out), .Q(mAddr), .clk(CLK));  // open: en, clr
  // Probe on mAddr
  \指令译码器  \u_指令译码器_1  (.IR(\指令字 ), .LW(LW), .SW(SW), .BEQ(BEQ), .ADDI(ADDI), .SLT(SLT), .OtherInstr(Other));
  ROM #(.addrWidth(5), .dataWidth(30), .Select("high")) rom_1 (
    .addr(mAddr), .data({ControlBus, P0, P1, P2, rom_1_data}));

  // Notes on the sheet:
  //   不要改变此引脚区域内容，也不要改变封装形式
  //   微程序入口查找逻辑
  //   判别测试逻辑
  //   微程序入口
  //   下址字段
  //   beq分支
  //   输入输出引脚
  //   μAR
  //   时钟是上跳沿还是下跳沿有效？
  //   微程序控制器（下址字段法）
  //   微地址
  //   控制存储器
  //   指令译码器
  //   contents of rom_1 (hex, n*v repeats v):
  //   20240001 802 8500203 10010080 4040005 2001006 8200007 100208 10020000 404000a 200100b 820000c
  //   408400d 800100 404000f 400c040 20040011 1001012 8400000 4040014 4004415 8022000 4040017 2001018
  //   8020000
  //   控制字段
  //   指令译码信号
  //   微指令
  //   指令译码逻辑ID
  //   判断逻辑
endmodule

module \微程序入口查找逻辑  (
  input  LW,
  input  SW,
  input  BEQ,
  input  SLT,
  input  ADDI,
  output S4,
  output S3,
  output S2,
  output S1,
  output S0
);

  or or_1 (S4, SLT, ADDI);
  or or_2 (S3, SW, BEQ);
  or or_3 (S2, LW, BEQ, ADDI);
  or or_4 (S1, BEQ, SLT, ADDI);
  or or_5 (S0, SW, SLT);
endmodule

module \条件判别测试逻辑  (
  input  P0,
  input  P1,
  input  equal,
  output S1,
  output S0
);

  wire and_1_out, and_2_out;

  and and_1 (and_1_out, P0, ~P1, ~equal);  // AND_Gate
  and and_2 (and_2_out, P0, ~P1, equal);  // AND_Gate
  and and_3 (S1, ~P0, P1, equal);  // AND_Gate
  or or_1 (S0, and_1_out, and_2_out);
endmodule

// 硬布线
module \硬布线控制器  (
  input  EQUAL,
  input  [31:0] \指令字 ,
  input  CLK,
  output [4:0] statu,
  output [21:0] ControlBus
);

  wire ADDI, BEQ, LW, Other, SLT, SW;
  wire [4:0] undriven;
  wire [7:0] rom_1_data;

  \硬布线状态机  \u_硬布线状态机_1  ();  // open: S4, S3, S2, S1, S0, LW, SW, BEQ, SLT, ADDI, EQUAL, N4, N3, N2, N1, N0
  // Probe on undriven
  Register #(.width(5), .trigger("rising"), .Select("low")) register_1 (
    .D(undriven), .Q(statu), .clk(CLK));  // open: en, clr
  \指令译码器  \u_指令译码器_1  (.IR(\指令字 ), .LW(LW), .SW(SW), .BEQ(BEQ), .ADDI(ADDI), .SLT(SLT), .OtherInstr(Other));
  ROM #(.addrWidth(5), .dataWidth(30), .Select("high")) rom_1 (.addr(statu), .data({ControlBus, rom_1_data}));

  // Other names for the same wires on the sheet: Write = ControlBus[0]; READ = ControlBus[1]; Slt_t = ControlBus[2];
  //   Add4 = ControlBus[3]; Add = ControlBus[4]; RegDst = ControlBus[5]; RegTgt = ControlBus[6];
  //   PSWin = ControlBus[7]; IRin = ControlBus[8]; Rin = ControlBus[9]; Xin = ControlBus[10]; DRin = ControlBus[11];
  //   DREin = ControlBus[12]; ARin = ControlBus[13]; PCin = ControlBus[14]; DREout = ControlBus[15];
  //   IR_A_out = ControlBus[16]; IR_I_out = ControlBus[17]; Rout = ControlBus[18]; Zout = ControlBus[19];
  //   DRout = ControlBus[20]; PCout = ControlBus[21]

  // Notes on the sheet:
  //   不要改变此引脚区域内容，也不要改变封装形式
  //   输入输出引脚
  //   时钟是上跳沿还是下跳沿有效？
  //   状态寄存器
  //   指令译码器
  //   控制存储器
  //   指令译码信号
  //   控制字段
  //   微指令
  //   指令译码逻辑ID
endmodule

module \硬布线状态机  (
  input  S4,
  input  S3,
  input  S2,
  input  S1,
  input  S0,
  input  LW,
  input  SW,
  input  BEQ,
  input  SLT,
  input  ADDI,
  input  EQUAL,
  output N4,
  output N3,
  output N2,
  output N1,
  output N0
);
endmodule

module \单总线CPU_中断_微程序  (
  input  [1:0] EduInt,
  output [21:0] \EDU控制总线 ,
  output [4:0] \EDU中断信号 
);

  wire _1_out, _2_out, and_1_out, CLK, comparator_1_eq, comparator_2_eq, equal, mips_alu_1_equal, not_1_out,
       \中断控制器_1_ir1w , \中断控制器_1_ir2w , \中断请求 ;
  wire [4:0] registerfile_1_p4, registerfile_1_p5, \微地址_状态 ;
  wire [11:0] Clks, \指令数 ;
  wire [31:0] AR_q, bit_extender_1_out, controlled_buffer_1_out, controlled_buffer_3_out, DR_q, IR,
       mips_alu_1_result, PC_q, ram_1_data, registerfile_1_p6, shifter_1_out, X_q, Z_q, \内部总线 ;

  // Probe on Clks
  Register #(.width(32), .trigger("rising"), .Select("low")) AR (
    .D(\内部总线 ), .en(\EDU控制总线 [13]), .Q(AR_q), .clk(CLK));  // open: clr
  // Probe on controlled_buffer_3_out
  // Mips_Probe mips_probe_1: pin names not known; wires that end beside it: IR
  Register #(.width(32), .trigger("rising"), .Select("low")) X (
    .D(\内部总线 ), .en(\EDU控制总线 [10]), .Q(X_q), .clk(CLK));  // open: clr
  // Probe on \指令数 
  RAM #(.addrWidth(10), .dataWidth(32), .bus("separate"), .Select("high")) ram_1 (
    .addr(AR_q[11:2]), .din(controlled_buffer_3_out), .data(ram_1_data), .str(\EDU控制总线 [0]), .clk(CLK),
    .ld(\EDU控制总线 [1]));  // open: sel, clr
  MIPS_ALU mips_alu_1 (
    .X(X_q), .Y(\内部总线 ), .Equal(mips_alu_1_equal), .Result(mips_alu_1_result), .ADD(\EDU控制总线 [4]),
    .ADD4(\EDU控制总线 [3]), .SLT(\EDU控制总线 [2]));  // open: SUB
  assign controlled_buffer_1_out = \EDU控制总线 [11] ? \内部总线  : 32'bz;  // Controlled_Buffer controlled_buffer_1
  assign controlled_buffer_1_out = \EDU控制总线 [12] ? ram_1_data : 32'bz;  // Controlled_Buffer controlled_buffer_2
  assign controlled_buffer_3_out = \EDU控制总线 [15] ? DR_q : 32'bz;  // Controlled_Buffer controlled_buffer_3
  // Probe on \内部总线 
  Register #(.width(32), .trigger("rising"), .Select("low")) PC (
    .D(\内部总线 ), .en(\EDU控制总线 [14]), .Q(PC_q), .clk(CLK));  // open: clr
  Register #(.width(32), .trigger("rising"), .Select("low")) DR (
    .D(controlled_buffer_1_out), .Q(DR_q), .clk(CLK));  // open: en, clr
  Register #(.width(1), .trigger("rising"), .Select("low")) PSW (
    .D(mips_alu_1_equal), .en(\EDU控制总线 [7]), .Q(equal), .clk(CLK));  // open: clr
  Register #(.width(32), .trigger("rising"), .Select("low")) Z (
    .D(mips_alu_1_result), .Q(Z_q), .clk(CLK));  // open: en, clr
  assign \内部总线  = \EDU控制总线 [21] ? PC_q : 32'bz;  // Controlled_Buffer controlled_buffer_4
  // Probe on \内部总线 
  assign \内部总线  = \EDU控制总线 [20] ? DR_q : 32'bz;  // Controlled_Buffer controlled_buffer_5
  assign \内部总线  = \EDU控制总线 [19] ? Z_q : 32'bz;  // Controlled_Buffer controlled_buffer_6
  assign \内部总线  = \EDU控制总线 [17] ? bit_extender_1_out : 32'bz;  // Controlled_Buffer controlled_buffer_7
  assign \内部总线  = \EDU控制总线 [16] ? shifter_1_out : 32'bz;  // Controlled_Buffer controlled_buffer_8
  Register #(.width(32), .trigger("rising"), .Select("low")) u_IR (
    .D(\内部总线 ), .en(\EDU控制总线 [8]), .Q(IR), .clk(CLK));  // open: clr
  Comparator #(.width(32), .mode("twosComplement")) comparator_1 (
    .a(IR), .b(32'h1000ffff), .eq(comparator_1_eq));  // open: gt, lt
  Clock #(.highDuration(1), .lowDuration(1)) clock_1 (.out(CLK));
  \微程序控制器_中断  \u_微程序控制器_中断_1  (
    .EQUAL(equal), .\指令字 (IR), .IntR(\中断请求 ), .CLK(CLK), .mAddr(\微地址_状态 ), .ControlBus(\EDU控制总线 ),
    .IntSignals(\EDU中断信号 ));
  // Probe on \微地址_状态 
  // RegisterFile registerfile_1: pin names not known; wires that end beside it: \内部总线 , CLK, \EDU控制总线 [9], registerfile_1_p4, registerfile_1_p5, registerfile_1_p6
  not not_1 (not_1_out, comparator_1_eq);
  Counter #(.width(12), .max('hfff), .ongoal("wrap"), .trigger("rising"), .behavior("new")) counter_1 (
    .count(not_1_out), .Q(Clks), .clk(CLK));  // open: load, D, carry, clr, preset, down
  assign bit_extender_1_out = {{16{IR[15]}}, IR[15:0]};  // Bit_Extender bit_extender_1
  assign \内部总线  = \EDU控制总线 [18] ? registerfile_1_p6 : 32'bz;  // Controlled_Buffer controlled_buffer_9
  Multiplexer #(.select(1), .width(5), .disabled("Z"), .enable("false")) multiplexer_1 (
    .in0(IR[25:21]), .in1(IR[20:16]), .out(registerfile_1_p5), .sel(\EDU控制总线 [6]));
  Multiplexer #(.select(1), .width(5), .disabled("Z"), .enable("false")) multiplexer_2 (
    .in0(IR[20:16]), .in1(IR[15:11]), .out(registerfile_1_p4), .sel(\EDU控制总线 [5]));
  and and_1 (and_1_out, not_1_out, comparator_2_eq);
  Comparator #(.width(5), .mode("twosComplement")) comparator_2 (
    .a(5'b00011), .b(\微地址_状态 ), .eq(comparator_2_eq));  // open: gt, lt
  Shifter #(.width(32), .shift("ll")) shifter_1 (.in(bit_extender_1_out), .\dist (5'b00010), .out(shifter_1_out));
  Counter #(.width(12), .max('hfff), .ongoal("wrap"), .trigger("rising"), .behavior("old")) counter_2 (
    .count(and_1_out), .Q(\指令数 ), .clk(CLK));  // open: load, D, carry, clr, preset
  D_Flip_Flop #(.trigger("rising"), .Pre_Clr_Positions("LEGACY"), .NegatePresetClear("false"), .enable("true"), .NewFFLayout("false")) d_ff_1 (
    .preset(\EDU中断信号 [0]), .reset(\EDU中断信号 [1]));  // open: clk, D, Q, Qn, en
  Button _1 (.out(_1_out));
  Button _2 (.out(_2_out));
  Register #(.width(32), .trigger("rising"), .Select("low")) EPC (.clk(CLK));  // open: D, en, Q, clr
  LED #(.active("true")) _1_2 (.in(\中断控制器_1_ir1w ));
  LED #(.active("true")) _2_2 (.in(\中断控制器_1_ir2w ));
  \中断控制器  \u_中断控制器_1  (
    .CLK(CLK), .Key1(_1_out), .Key2(_2_out), .Clr(\EDU中断信号 [1]), .IR1W(\中断控制器_1_ir1w ),
    .IR2W(\中断控制器_1_ir2w ), .EDU_TEST(EduInt));  // open: IR3W, IntNo, IntR, Key3

  // Other names for the same wires on the sheet: rd[4:0] = IR[15:11]; rt[4:0] = IR[20:16]; rs[4:0] = IR[25:21];
  //   中断控制信号[4:0] = \EDU中断信号 ; 关中断 = \EDU中断信号 [0]; 开中断 = \EDU中断信号 [1]; Addrout = \EDU中断信号 [2]; EPCin = \EDU中断信号 [3];
  //   EPCout = \EDU中断信号 [4]; Write = \EDU控制总线 [0]; 控制总线[21:0] = \EDU控制总线 ; READ = \EDU控制总线 [1]; Slt = \EDU控制总线 [2];
  //   Add4 = \EDU控制总线 [3]; Add = \EDU控制总线 [4]; RegDst = \EDU控制总线 [5]; RegTgt = \EDU控制总线 [6]; PSWin = \EDU控制总线 [7];
  //   IRin = \EDU控制总线 [8]; Rin = \EDU控制总线 [9]; Xin = \EDU控制总线 [10]; DRin = \EDU控制总线 [11]; DREin = \EDU控制总线 [12];
  //   ARin = \EDU控制总线 [13]; PCin = \EDU控制总线 [14]; DREout = \EDU控制总线 [15]; IR_A_out = \EDU控制总线 [16];
  //   IR_I_out = \EDU控制总线 [17]; Rout = \EDU控制总线 [18]; Zout = \EDU控制总线 [19]; DRout = \EDU控制总线 [20];
  //   PCout = \EDU控制总线 [21]

  // Notes on the sheet:
  //   单总线结构 MIPS CPU
  //   MEM
  //   外部总线
  //   内部总线
  //   Immediate32
  //   AddressOffset32
  //   中断使能寄存器
  //   EPC用于保存断点
  //   执行ERET时开中断，同时清除中断源
  //   中断逻辑
endmodule

// 微程序
module \微程序控制器_中断  (
  input  EQUAL,
  input  [31:0] \指令字 ,
  input  IntR,
  input  CLK,
  output [4:0] mAddr,
  output [21:0] ControlBus,
  output [4:0] IntSignals
);

  wire ADDI, BEQ, ERET, LW, P0, P1, P2, SLT, SW;
  wire [4:0] adder_1_out, multiplexer_1_out, undriven, undriven_2, undriven_3, undriven_4,
       \微程序入口查找逻辑_中断_1_s0 ;

  \微程序入口查找逻辑_中断  \u_微程序入口查找逻辑_中断_1  (
    .LW(LW), .SW(SW), .BEQ(BEQ), .SLT(SLT), .ADDI(ADDI), .ERET(ERET), .S4(\微程序入口查找逻辑_中断_1_s0 [4]),
    .S3(\微程序入口查找逻辑_中断_1_s0 [3]), .S2(\微程序入口查找逻辑_中断_1_s0 [2]), .S1(\微程序入口查找逻辑_中断_1_s0 [1]),
    .S0(\微程序入口查找逻辑_中断_1_s0 [0]));
  // Probe on \微程序入口查找逻辑_中断_1_s0 
  \条件判别测试逻辑_中断  \u_条件判别测试逻辑_中断_1  (.P0(P0), .P1(P1), .P2(P2), .equal(EQUAL), .IntR(IntR));  // open: S2, S1, S0
  Multiplexer #(.select(3), .width(5), .disabled("Z"), .enable("false")) multiplexer_1 (
    .in0(undriven_3), .in1(undriven_4), .in2(undriven_2), .in3(undriven), .in4({5{1'b0}}),
    .out(multiplexer_1_out));  // open: in5, in6, in7, sel
  // Probe on multiplexer_1_out
  Register #(.width(5), .trigger("falling"), .Select("low")) register_1 (
    .D(multiplexer_1_out), .Q(mAddr), .clk(CLK));  // open: en, clr
  Adder #(.width(5)) adder_1 (.a(5'b00001), .b(mAddr), .out(adder_1_out));  // open: cin, cout
  \指令译码器  \u_指令译码器_1  (.IR(\指令字 ), .LW(LW), .SW(SW), .BEQ(BEQ), .ADDI(ADDI), .SLT(SLT), .OtherInstr(ERET));
  ROM #(.addrWidth(5), .dataWidth(30), .Select("high")) rom_1 (
    .addr(mAddr), .data({ControlBus, IntSignals, P0, P1, P2}));

  // Notes on the sheet:
  //   不要改变此引脚区域内容，也不要改变封装形式
  //   微程序入口查找逻辑
  //   beq分支
  //   中断响应入口
  //   入口地址
  //   取指微程序入口
  //   顺序地址
  //   判别测试逻辑
  //   μAR
  //   支持中断的微程序控制器（计数器法）
  //   微地址
  //   指令译码器
  //   mAddr++
  //   控制存储器
  //   指令译码信号
  //   控制字段
  //   微指令
  //   指令译码逻辑ID
  //   判断逻辑
endmodule

module \微程序入口查找逻辑_中断  (
  input  LW,
  input  SW,
  input  BEQ,
  input  SLT,
  input  ADDI,
  input  ERET,
  output S4,
  output S3,
  output S2,
  output S1,
  output S0
);
endmodule

module \条件判别测试逻辑_中断  (
  input  P0,
  input  P1,
  input  P2,
  input  equal,
  input  IntR,
  output S2,
  output S1,
  output S0
);
endmodule

// 硬布线
module \硬布线控制器_中断  (
  input  EQUAL,
  input  [31:0] \指令字 ,
  input  IntR,
  input  CLK,
  output [4:0] statu,
  output [21:0] ControlBus,
  output [4:0] IntSignals
);

  wire ADDI, BEQ, ERET, LW, P1, P2, P3, SLT, SW;
  wire [4:0] undriven;

  \硬布线状态机_中断  \u_硬布线状态机_中断_1  ();  // open: S4, S3, S2, S1, S0, LW, SW, BEQ, SLT, ADDI, ERET, IR, EQUAL, N4, N3, N2, N1, N0
  // Probe on undriven
  Register #(.width(5), .trigger("falling"), .Select("low")) register_1 (
    .D(undriven), .Q(statu), .clk(CLK));  // open: en, clr
  // Probe on statu
  \指令译码器  \u_指令译码器_1  (.IR(\指令字 ), .LW(LW), .SW(SW), .BEQ(BEQ), .ADDI(ADDI), .SLT(SLT), .OtherInstr(ERET));
  ROM #(.addrWidth(5), .dataWidth(30), .Select("high")) rom_1 (
    .addr(statu), .data({ControlBus, IntSignals, P1, P2, P3}));

  // Notes on the sheet:
  //   不要改变此引脚区域内容，也不要改变封装形式
  //   硬布线控制器状态机
  //   状态寄存器
  //   支持中断的硬布线控制器
  //   指令译码器
  //   控制存储器
  //   指令译码信号
  //   控制字段
  //   微指令
  //   指令译码逻辑ID
  //   判断逻辑
endmodule

module \硬布线状态机_中断  (
  input  S4,
  input  S3,
  input  S2,
  input  S1,
  input  S0,
  input  LW,
  input  SW,
  input  BEQ,
  input  SLT,
  input  ADDI,
  input  ERET,
  input  IR,
  input  EQUAL,
  output N4,
  output N3,
  output N2,
  output N1,
  output N0
);
endmodule

// ALU
module MIPS_ALU (
  input  ADD,
  input  ADD4,
  input  [31:0] X,
  input  [31:0] Y,
  input  SUB,
  input  SLT,
  output Equal,
  output [31:0] Result
);

  wire [0:0] comparator_1_lt;
  wire [1:0] priority_encoder_1_out;
  wire [31:0] adder_1_out, adder_2_out, subtractor_1_out;

  Pull_Resistor #(.pull(0)) pull_resistor_1 (.node(Y));
  Adder #(.width(32)) adder_1 (.a(X), .b(Y), .out(adder_1_out));  // open: cin, cout
  Adder #(.width(32)) adder_2 (.a(X), .b(32'h4), .out(adder_2_out));  // open: cin, cout
  Subtractor #(.width(32)) subtractor_1 (.a(X), .b(Y), .out(subtractor_1_out));  // open: bin, bout
  Comparator #(.width(32), .mode("twosComplement")) comparator_1 (
    .a(X), .b(Y), .eq(Equal), .lt(comparator_1_lt[0]));  // open: gt
  Priority_Encoder #(.select(2), .disabled("Z")) priority_encoder_1 (
    .in0(ADD), .in1(ADD4), .in2(SUB), .in3(SLT), .out(priority_encoder_1_out));  // open: gs, en_out, en_in
  Pull_Resistor #(.pull(0)) pull_resistor_2 (.node(priority_encoder_1_out));
  Multiplexer #(.select(2), .width(32), .disabled("Z"), .enable("false")) multiplexer_1 (
    .in0(adder_1_out), .in1(adder_2_out), .in2(subtractor_1_out), .in3({{31{1'b0}}, comparator_1_lt[0]}),
    .out(Result), .sel(priority_encoder_1_out));

  // Notes on the sheet:
  //   不要改变此引脚区域内容，也不要改变ALU封装形式
  //   输入引脚
  //   输出引脚
endmodule

// 中断控制器
module \中断控制器  (
  input  CLK,
  input  Key1,
  input  Key2,
  input  Key3,
  input  Clr,
  input  [1:0] EDU_TEST,
  output IR1W,
  output IR2W,
  output IR3W,
  output [1:0] IntNo,
  output IntR
);

  wire and_1_out, and_2_out, and_3_out, Clr0, Clr1, Clr2, Clr3, d_ff_1_q, d_ff_2_q, d_ff_3_q, IR1_q, IR2_q,
       IR3_q, or_1_out, or_3_out, or_6_out, or_7_out, or_8_out;

  or or_1 (or_1_out, Key1, EDU_TEST[0]);
  or or_2 (IR1W, IR1_q, d_ff_2_q);
  or or_3 (or_3_out, Key2, EDU_TEST[1]);
  or or_4 (IR2W, IR2_q, d_ff_3_q);
  D_Flip_Flop #(.trigger("rising"), .Pre_Clr_Positions("LEGACY"), .NegatePresetClear("false"), .enable("true"), .NewFFLayout("false")) d_ff_1 (
    .clk(Key3), .D(1'b1), .Q(d_ff_1_q), .reset(IR3_q));  // open: Qn, preset, en
  or or_5 (IR3W, IR3_q, d_ff_1_q);
  D_Flip_Flop #(.trigger("rising"), .Pre_Clr_Positions("LEGACY"), .NegatePresetClear("false"), .enable("true"), .NewFFLayout("false")) d_ff_2 (
    .clk(or_1_out), .D(1'b1), .Q(d_ff_2_q), .reset(IR1_q));  // open: Qn, preset, en
  D_Flip_Flop #(.trigger("rising"), .Pre_Clr_Positions("LEGACY"), .NegatePresetClear("false"), .enable("true"), .NewFFLayout("false")) d_ff_3 (
    .clk(or_3_out), .D(1'b1), .Q(d_ff_3_q), .reset(IR2_q));  // open: Qn, preset, en
  or or_6 (or_6_out, d_ff_2_q, IR1_q);
  and and_1 (and_1_out, or_6_out, ~Clr1);  // AND_Gate
  or or_7 (or_7_out, d_ff_3_q, IR2_q);
  and and_2 (and_2_out, or_7_out, ~Clr2);  // AND_Gate
  or or_8 (or_8_out, d_ff_1_q, IR3_q);
  and and_3 (and_3_out, or_8_out, ~Clr3);  // AND_Gate
  Pull_Resistor #(.pull(0)) pull_resistor_1 (.node(EDU_TEST));
  D_Flip_Flop #(.trigger("rising"), .Pre_Clr_Positions("LEGACY"), .NegatePresetClear("false"), .enable("true"), .NewFFLayout("false")) IR1 (
    .clk(CLK), .D(and_1_out), .Q(IR1_q));  // open: Qn, preset, en, reset
  D_Flip_Flop #(.trigger("rising"), .Pre_Clr_Positions("LEGACY"), .NegatePresetClear("false"), .enable("true"), .NewFFLayout("false")) IR2 (
    .clk(CLK), .D(and_2_out), .Q(IR2_q));  // open: Qn, preset, en, reset
  D_Flip_Flop #(.trigger("rising"), .Pre_Clr_Positions("LEGACY"), .NegatePresetClear("false"), .enable("true"), .NewFFLayout("false")) IR3 (
    .clk(CLK), .D(and_3_out), .Q(IR3_q));  // open: Qn, preset, en, reset
  Priority_Encoder #(.select(2), .disabled("Z")) priority_encoder_1 (
    .in1(IR1_q), .in2(IR2_q), .in3(IR3_q), .out(IntNo), .gs(IntR));  // open: in0, en_out, en_in
  Decoder #(.select(2), .tristate("false"), .disabled(0), .enable("true")) decoder_1 (
    .out0(Clr0), .out1(Clr1), .out2(Clr2), .out3(Clr3), .sel(IntNo), .en(Clr));

  // Other names for the same wires on the sheet: EDU_INT1 = EDU_TEST[0]; EDU_INT2 = EDU_TEST[1]

  // Notes on the sheet:
  //   中断等待
  //   中断等待
  //   中断等待
  //   中断信号采样参考电路
  //   Reset 
  //   Reset 
  //   Reset 
  //   中断优先编码器
endmodule
