// Logisim project cpu24.circ as structural Verilog: 31 circuits, main circuit ◇单周期MIPS
// 单周期硬布线控制器
module \单周期硬布线控制器  (
  input  [5:0] OP,
  input  [5:0] Func,
  output [3:0] ALU_OP,
  output MemToReg,
  output MemWrite,
  output ALU_SRC,
  output RegWrite,
  output SysCALL,
  output SignedExt,
  output RegDst,
  output Beq,
  output Bne,
  output JR,
  output JMP,
  output JAL,
  output ERET
);

  \运算控制器自动生成  \u_运算控制器自动生成_1  (
    .OP0(OP[0]), .OP1(OP[1]), .OP2(OP[2]), .OP3(OP[3]), .OP4(OP[4]), .OP5(OP[5]), .F0(Func[0]), .F1(Func[1]),
    .F2(Func[2]), .F3(Func[3]), .F4(Func[4]), .F5(Func[5]), .S0(ALU_OP[0]), .S1(ALU_OP[1]), .S2(ALU_OP[2]),
    .S3(ALU_OP[3]));
  \控制信号自动生成  \u_控制信号自动生成_1  (
    .OP0(OP[0]), .OP1(OP[1]), .OP2(OP[2]), .OP3(OP[3]), .OP4(OP[4]), .OP5(OP[5]), .F0(Func[0]), .F1(Func[1]),
    .F2(Func[2]), .F3(Func[3]), .F4(Func[4]), .F5(Func[5]), .MemToReg(MemToReg), .MemWrite(MemWrite),
    .ALU_SRC(ALU_SRC), .RegWrite(RegWrite), .SysCALL(SysCALL), .SignedExt(SignedExt), .RegDst(RegDst),
    .BEQ(Beq), .BNE(Bne), .JR(JR), .JUMP(JMP), .JAL(JAL), .ERET(ERET));

  // Other names for the same wires on the sheet: OP_CODE[5:0] = OP

  // Notes on the sheet:
  //   运算器控制器，根据指令生成运算器功能选择信号
  //   控制信号生成，产生数据通路需要的其他控制信号
endmodule

module \单周期MIPS  (
  input  IR1,
  input  IR2,
  input  IR3,
  output RegWrite,
  output MemWrite,
  output [31:0] PC,
  output [31:0] IR,
  output [31:0] RDin,
  output [31:0] MDin,
  output [31:0] LedData
);

  wire alu_srcb, and_3_out, and_4_out, beq, bne, CLK, clock_2_out, comparator_1_eq, comparator_1_lt,
       comparator_2_eq, d_ff_1_q, equal, Go, halt, IR1_t, IR2_t, IR3_t, IRA, IRB, IRC, jal, jmp, jmp_if, jr,
       led_en, mem_to_reg, nand_1_out, not_1_out, not_2_out, reg_dst, rst, signed_ext, syscall, W1, W2, W3;
  wire [3:0] alu_op;
  wire [4:0] multiplexer_4_out, multiplexer_5_out, multiplexer_6_out, multiplexer_7_out;
  wire [12:0] CNT_num;
  wire [15:0] \总周期数 ;
  wire [31:0] bit_extender_1_out, bit_extender_2_out, mips_alu_1_result, multiplexer_1_out,
       multiplexer_2_out, multiplexer_3_out, multiplexer_8_out, multiplexer_9_out, multiplexer_10_out, pc_4,
       pc_imm, pc_jr, ram_1_data, shifter_1_out;

  Clock #(.highDuration(1), .lowDuration(1)) clock_1 ();  // open: out
  Button _1 (.out(IRA));
  Button _2 (.out(IRB));
  Button _3 (.out(IRC));
  Button \u_继续运行  (.out(Go));
  LED #(.active("true")) led_1 (.in(W1));
  LED #(.active("true")) led_2 (.in(W2));
  LED #(.active("true")) led_3 (.in(W3));
  Button button_1 (.out(rst));
  Multiplexer #(.select(1), .width(32), .disabled("Z"), .enable("false")) multiplexer_1 (
    .in0(pc_4), .in1(pc_imm), .out(multiplexer_1_out), .sel(jmp_if));
  Multiplexer #(.select(1), .width(32), .disabled("Z"), .enable("false")) multiplexer_2 (
    .in0(multiplexer_1_out), .in1({pc_4[31:28], IR[25:0], 2'b00}), .out(multiplexer_2_out), .sel(jmp));
  Multiplexer #(.select(1), .width(32), .disabled("Z"), .enable("false")) multiplexer_3 (
    .in0(multiplexer_2_out), .in1(pc_jr), .out(multiplexer_3_out), .sel(jr));
  not not_1 (not_1_out, halt);
  // Mips_Probe mips_probe_1: pin names not known; wires that end beside it: {pc_4[31:28], IR[25:0], 2'b00}
  Hex_Digit_Display hex_digit_display_1 (.value(LedData[31:28]));  // open: dp
  D_Flip_Flop #(.trigger("high"), .Pre_Clr_Positions("LEGACY"), .NegatePresetClear("false"), .enable("true"), .NewFFLayout("false")) d_ff_1 (.Q(d_ff_1_q));  // open: clk, D, Qn, preset, en, reset
  Hex_Digit_Display hex_digit_display_2 (.value(LedData[23:20]));  // open: dp
  Hex_Digit_Display hex_digit_display_3 (.value(LedData[27:24]));  // open: dp
  Register #(.width(32), .trigger("rising"), .Select("low")) u_PC (
    .D(multiplexer_3_out), .en(not_1_out), .Q(PC), .clk(CLK), .clr(rst));
  // Probe on PC
  // Probe on 13'hc
  Clock #(.highDuration(1), .lowDuration(1)) clock_2 (.out(clock_2_out));
  Hex_Digit_Display hex_digit_display_4 (.value(LedData[15:12]));  // open: dp
  Hex_Digit_Display hex_digit_display_5 (.value(LedData[19:16]));  // open: dp
  \单周期硬布线控制器  \u_单周期硬布线控制器_1  (
    .Func(IR[5:0]), .OP(IR[31:26]), .ALU_OP(alu_op), .MemToReg(mem_to_reg), .MemWrite(MemWrite),
    .ALU_SRC(alu_srcb), .RegWrite(RegWrite), .SysCALL(syscall), .SignedExt(signed_ext), .RegDst(reg_dst),
    .JR(jr), .JMP(jmp), .Beq(beq), .JAL(jal), .Bne(bne));  // open: ERET
  Multiplexer #(.select(1), .width(5), .disabled("Z"), .enable("false")) multiplexer_4 (
    .in0(IR[20:16]), .in1(5'b00100), .out(multiplexer_4_out), .sel(syscall));
  Multiplexer #(.select(1), .width(5), .disabled("Z"), .enable("false")) multiplexer_5 (
    .in0(IR[20:16]), .in1(IR[15:11]), .out(multiplexer_5_out), .sel(reg_dst));
  // Probe on IR[15:0]
  Comparator #(.width(13), .mode("twosComplement")) comparator_1 (
    .a(CNT_num), .b(13'hc), .eq(comparator_1_eq), .lt(comparator_1_lt));  // open: gt
  Hex_Digit_Display hex_digit_display_6 (.value(LedData[11:8]));  // open: dp
  Hex_Digit_Display hex_digit_display_7 (.value(LedData[7:4]));  // open: dp
  // Probe on \总周期数 
  // Probe on multiplexer_6_out
  Multiplexer #(.select(1), .width(5), .disabled("Z"), .enable("false")) multiplexer_6 (
    .in0(IR[25:21]), .in1(5'b00010), .out(multiplexer_6_out), .sel(syscall));
  Multiplexer #(.select(1), .width(5), .disabled("Z"), .enable("false")) multiplexer_7 (
    .in0(multiplexer_5_out), .in1({5{1'b1}}), .out(multiplexer_7_out), .sel(jal));
  nand nand_1 (nand_1_out, d_ff_1_q, comparator_1_eq);
  Counter #(.width(13), .max('h1fff), .ongoal("stay"), .trigger("rising"), .behavior("old")) counter_1 (
    .count(comparator_1_lt), .Q(CNT_num), .clk(clock_2_out));  // open: load, D, carry, clr, preset
  Hex_Digit_Display hex_digit_display_8 (.value(LedData[3:0]));  // open: dp
  // Probe on multiplexer_4_out
  // Probe on multiplexer_7_out
  // Probe on bit_extender_1_out
  ROM #(.addrWidth(10), .dataWidth(32), .Select("high")) rom_1 (.addr(PC[11:2]), .data(IR));
  assign CLK = nand_1_out ? clock_2_out : 1'bz;  // Controlled_Buffer controlled_buffer_1
  Pull_Resistor #(.pull(1)) pull_resistor_1 (.node(CLK));
  or or_1 (IR1_t, IR1, IRA);
  MIPS_Regifile mips_regifile_1 (
    .Din(RDin), .Clk(CLK), .R1(pc_jr), .R2(MDin), .WE(RegWrite), .W_num(multiplexer_7_out),
    .R1_num(multiplexer_6_out), .R2_num(multiplexer_4_out));
  assign bit_extender_1_out = {{16{1'b0}}, IR[15:0]};  // Bit_Extender bit_extender_1
  assign bit_extender_2_out = {{16{IR[15]}}, IR[15:0]};  // Bit_Extender bit_extender_2
  // Mips_Probe mips_probe_2: pin names not known; wires that end beside it: IR
  or or_2 (IR2_t, IR2, IRB);
  Adder #(.width(32)) adder_1 (.a(PC), .b(32'h4), .out(pc_4));  // open: cin, cout
  Comparator #(.width(32), .mode("twosComplement")) comparator_2 (
    .a(pc_jr), .b(32'h22), .eq(comparator_2_eq));  // open: gt, lt
  // Probe on pc_jr
  Multiplexer #(.select(1), .width(32), .disabled("Z"), .enable("false")) multiplexer_8 (
    .in0(bit_extender_1_out), .in1(bit_extender_2_out), .out(multiplexer_8_out), .sel(signed_ext));
  Multiplexer #(.select(1), .width(32), .disabled("Z"), .enable("false")) multiplexer_9 (
    .in0(MDin), .in1(multiplexer_8_out), .out(multiplexer_9_out), .sel(alu_srcb));
  Shifter #(.width(32), .shift("ll")) shifter_1 (.in(bit_extender_2_out), .\dist (5'b00010), .out(shifter_1_out));
  and and_1 (led_en, syscall, comparator_2_eq);
  and and_2 (halt, syscall, ~comparator_2_eq);  // AND_Gate
  MIPS_ALU mips_alu_1 (
    .X(pc_jr), .Y(multiplexer_9_out), .AluOP(alu_op), .Equal(equal), .Result(mips_alu_1_result),
    .shamt(IR[10:6]));  // open: Result_2
  or or_3 (IR3_t, IR3, IRC);
  Adder #(.width(32)) adder_2 (.a(shifter_1_out), .b(pc_4), .out(pc_imm));  // open: cin, cout
  and and_3 (and_3_out, beq, equal);
  and and_4 (and_4_out, bne, ~equal);  // AND_Gate
  Register #(.width(32), .trigger("rising"), .Select("low")) register_1 (
    .D(MDin), .en(led_en), .Q(LedData), .clk(CLK), .clr(rst));
  or or_4 (jmp_if, and_3_out, and_4_out);
  not not_2 (not_2_out, halt);
  RAM #(.addrWidth(10), .dataWidth(32), .bus("separate"), .Select("high")) ram_1 (
    .addr(mips_alu_1_result[11:2]), .din(MDin), .data(ram_1_data), .str(MemWrite), .clk(CLK));  // open: sel, ld, clr
  Counter #(.width(16), .max('hffff), .ongoal("wrap"), .trigger("rising"), .behavior("old")) counter_2 (
    .count(not_2_out), .Q(\总周期数 ), .clk(CLK), .clr(rst));  // open: load, D, carry, preset
  Multiplexer #(.select(1), .width(32), .disabled("Z"), .enable("false")) multiplexer_10 (
    .in0(mips_alu_1_result), .in1(ram_1_data), .out(multiplexer_10_out), .sel(mem_to_reg));
  Multiplexer #(.select(1), .width(32), .disabled("Z"), .enable("false")) multiplexer_11 (
    .in0(multiplexer_10_out), .in1(pc_4), .out(RDin), .sel(jal));

  // Other names for the same wires on the sheet: a0[31:0] = MDin; addr[25:0] = IR[25:0]; imm[15:0] = IR[15:0];
  //   mem_write = MemWrite; reg_write = RegWrite

  // Notes on the sheet:
  //   中断源
  //   中断等待指示
  //   总复位信号应将除ROM以外所有存储组件全部清零
  //   OP
  //   rs
  //   rt
  //   rd
  //   shamt
  //   控制位
  //   暂停节拍，不能为0
  //   Func
  //   用这个时钟源需要去掉电路中的其他时钟源
  //   数码管输出
  //   戳工具置1进入计数暂停模式，ctrl+k时钟自动运行到对应节拍暂停
  //   ctrl+k关闭时钟连续运行，将控制位置零，进入单步调试模式调试
  //   数码管输出应该用寄存器锁存，否则显示数据只能一闪而过
  //   指令存储器
  //   contents of rom_1 (hex, n*v repeats v):
  //   20110001 8000c05 20110001 20120002 20130003 8000c09 20110001 20120002 20130003 8000c0d 20110001
  //   20120002 20130003 8000c11 20110001 20120002 20130003 c000cb8 20100001 20110001 118fc0 112020
  //   20020022 c 118882 12200001 8000c15 112020 20020022 c 20110001 118880 112020 20020022 c 12200001
  //   8000c1f 20110001 118fc0 112020 20020022 c 1188c3 112020 20020022 c 118903 112020 20020022 c 118903
  //   112020 20020022 c 118903 112020 20020022 c 118903 112020 20020022 c 118903 112020 20020022 c 118903
  //   112020 20020022 c 118903 112020 20020022 c 20100001 109fc0 139fc3 8021 2012000c 24160003 26100001
  //   3210000f 20080008 20090001 139900 2709825 132020 20020022 c 1094022 1500fff9 22100001 2018000f
  //   2188024 108700 20080008 20090001 139902 2709825 132021 20020022 c 1094022 1500fff9 108702 2c9b022
  //   12c00001 8000c50 4020 1084027 84400 3508ffff 82021 20020022 c 2010ffff 20110000 ae300000 22100001
  //   22310004 ae300000 22100001 22310004 ae300000 22100001 22310004 ae300000 22100001 22310004 ae300000
  //   22100001 22310004 ae300000 22100001 22310004 ae300000 22100001 22310004 ae300000 22100001 22310004
  //   ae300000 22100001 22310004 ae300000 22100001 22310004 ae300000 22100001 22310004 ae300000 22100001
  //   22310004 ae300000 22100001 22310004 ae300000 22100001 22310004 ae300000 22100001 22310004 ae300000
  //   22100001 22310004 22100001 8020 2011003c 8e130000 8e340000 274402a 11000002 ae330000 ae140000
  //   2231fffc 1611fff8 102020 20020022 c 22100004 2011003c 1611fff2 20020032 c 20100000 22100001 102020
  //   20020022 c 22100002 102020 20020022 c 22100003 102020 20020022 c 22100004 102020 20020022 c 22100005
  //   102020 20020022 c 22100006 102020 20020022 c 22100007 102020 20020022 c 22100008 102020 20020022
  //   20020022 c 3e00008
  //   可计数暂停的时钟源
  //   指令字
  //   为方便自动评测，需要输出PC，IR，寄存器堆写如数据RDin
  //   RAM写使能MemWrite、RAM写入数据MDin等信号
endmodule

// 运算器控制器
module \运算控制器自动生成  (
  input  OP0,
  input  OP1,
  input  OP2,
  input  OP3,
  input  OP4,
  input  OP5,
  input  F0,
  input  F1,
  input  F2,
  input  F3,
  input  F4,
  input  F5,
  output S0,
  output S1,
  output S2,
  output S3
);

  wire and_1_out, and_2_out, and_3_out, and_4_out, and_5_out, and_6_out, and_7_out, and_8_out, and_9_out,
       and_10_out, and_11_out, and_12_out, and_13_out, and_14_out, and_15_out, and_16_out, and_17_out,
       and_18_out, and_19_out, and_20_out, and_21_out, and_22_out, and_23_out, and_24_out, and_25_out,
       and_26_out, and_27_out, and_28_out, and_29_out, and_30_out, and_31_out, and_32_out, and_33_out,
       and_34_out, not_1_out, not_2_out, not_3_out, not_4_out, not_5_out, not_6_out, not_7_out, not_8_out,
       not_9_out, not_10_out, not_11_out, not_12_out, not_13_out, not_14_out, not_15_out, not_16_out,
       not_17_out, not_18_out, not_19_out, not_20_out, not_21_out, not_22_out, not_23_out, not_24_out,
       not_25_out, not_26_out, not_27_out, not_28_out, not_29_out, not_30_out, not_31_out, not_32_out,
       not_33_out, not_34_out, not_35_out, not_36_out, not_37_out, not_38_out, not_39_out, not_40_out,
       not_41_out, not_42_out, not_43_out, not_44_out, not_45_out, not_46_out, not_47_out, not_48_out,
       not_49_out, not_50_out, not_51_out, not_52_out, not_53_out, not_54_out, not_55_out, not_56_out,
       not_57_out, not_58_out, not_59_out, not_60_out, not_61_out, not_62_out, not_63_out, not_64_out,
       not_65_out, not_66_out, not_67_out, not_68_out, not_69_out, not_70_out, not_71_out, not_72_out,
       not_73_out, not_74_out, not_75_out, not_76_out, not_77_out, not_78_out, not_79_out, not_80_out,
       not_81_out, not_82_out, not_83_out, not_84_out, not_85_out, not_86_out, not_87_out, not_88_out,
       not_89_out, not_90_out, not_91_out, not_92_out, not_93_out, not_94_out, not_95_out, not_96_out,
       not_97_out, not_98_out, not_99_out, not_100_out, not_101_out, not_102_out, not_103_out, not_104_out,
       not_105_out, not_106_out, not_107_out, not_108_out, not_109_out, not_110_out, not_111_out,
       not_112_out, not_113_out, not_114_out, not_115_out, not_116_out, not_117_out, not_118_out,
       not_119_out, not_120_out, not_121_out, not_122_out, not_123_out, not_124_out, not_125_out,
       not_126_out, not_127_out, not_128_out, not_129_out, not_130_out, not_131_out, not_132_out,
       not_133_out, not_134_out, not_135_out, not_136_out, not_137_out, not_138_out, not_139_out,
       not_140_out, not_141_out, not_142_out, not_143_out, not_144_out, not_145_out, not_146_out,
       not_147_out, not_148_out, not_149_out, not_150_out, not_151_out, not_152_out, not_153_out,
       not_154_out, not_155_out, not_156_out, not_157_out, not_158_out, not_159_out, not_160_out,
       not_161_out, not_162_out, not_163_out, not_164_out, not_165_out, not_166_out, not_167_out,
       not_168_out, not_169_out, not_170_out, not_171_out, not_172_out, not_173_out, not_174_out,
       not_175_out, not_176_out, not_177_out, not_178_out, not_179_out, not_180_out, not_181_out,
       not_182_out, not_183_out, not_184_out, not_185_out, not_186_out, not_187_out, not_188_out,
       not_189_out, not_190_out, not_191_out, not_192_out, not_193_out, not_194_out, not_195_out,
       not_196_out, not_197_out, not_198_out, not_199_out, not_200_out, not_201_out, not_202_out,
       not_203_out, not_204_out, not_205_out, not_206_out, not_207_out, not_208_out, not_209_out,
       not_210_out, not_211_out, not_212_out, not_213_out, not_214_out, not_215_out, not_216_out,
       not_217_out, not_218_out, not_219_out, not_220_out, not_221_out, not_222_out, not_223_out,
       not_224_out, not_225_out, not_226_out, not_227_out, not_228_out, not_229_out, not_230_out,
       not_231_out, not_232_out, not_233_out, not_234_out, not_235_out, not_236_out;

  not not_1 (not_1_out, OP5);
  not not_2 (not_2_out, OP4);
  not not_3 (not_3_out, OP3);
  not not_4 (not_4_out, OP2);
  not not_5 (not_5_out, OP1);
  not not_6 (not_6_out, OP0);
  not not_7 (not_7_out, F5);
  not not_8 (not_8_out, F4);
  not not_9 (not_9_out, F3);
  not not_10 (not_10_out, F2);
  not not_11 (not_11_out, OP5);
  not not_12 (not_12_out, OP4);
  not not_13 (not_13_out, OP3);
  not not_14 (not_14_out, OP2);
  not not_15 (not_15_out, OP1);
  not not_16 (not_16_out, OP0);
  not not_17 (not_17_out, F4);
  not not_18 (not_18_out, F3);
  not not_19 (not_19_out, F2);
  not not_20 (not_20_out, F1);
  not not_21 (not_21_out, F0);
  not not_22 (not_22_out, OP5);
  not not_23 (not_23_out, OP4);
  not not_24 (not_24_out, OP3);
  not not_25 (not_25_out, OP2);
  not not_26 (not_26_out, OP1);
  not not_27 (not_27_out, OP0);
  not not_28 (not_28_out, F4);
  not not_29 (not_29_out, F3);
  not not_30 (not_30_out, F2);
  not not_31 (not_31_out, F1);
  not not_32 (not_32_out, OP5);
  not not_33 (not_33_out, OP4);
  not not_34 (not_34_out, OP3);
  not not_35 (not_35_out, OP2);
  not not_36 (not_36_out, OP1);
  not not_37 (not_37_out, OP0);
  not not_38 (not_38_out, F4);
  not not_39 (not_39_out, F3);
  not not_40 (not_40_out, F1);
  not not_41 (not_41_out, F0);
  not not_42 (not_42_out, OP5);
  not not_43 (not_43_out, OP4);
  not not_44 (not_44_out, OP3);
  not not_45 (not_45_out, OP2);
  not not_46 (not_46_out, OP1);
  not not_47 (not_47_out, OP0);
  not not_48 (not_48_out, F4);
  not not_49 (not_49_out, F2);
  not not_50 (not_50_out, F0);
  not not_51 (not_51_out, OP5);
  not not_52 (not_52_out, OP4);
  not not_53 (not_53_out, OP2);
  not not_54 (not_54_out, OP1);
  not not_55 (not_55_out, OP0);
  not not_56 (not_56_out, OP5);
  not not_57 (not_57_out, OP4);
  not not_58 (not_58_out, OP1);
  not not_59 (not_59_out, OP0);
  not not_60 (not_60_out, OP5);
  not not_61 (not_61_out, OP4);
  not not_62 (not_62_out, OP2);
  not not_63 (not_63_out, OP1);
  not not_64 (not_64_out, OP5);
  not not_65 (not_65_out, OP4);
  not not_66 (not_66_out, OP2);
  not not_67 (not_67_out, OP0);
  not not_68 (not_68_out, OP4);
  not not_69 (not_69_out, OP3);
  not not_70 (not_70_out, OP2);
  not not_71 (not_71_out, OP4);
  not not_72 (not_72_out, OP2);
  not not_73 (not_73_out, OP5);
  not not_74 (not_74_out, OP4);
  not not_75 (not_75_out, OP3);
  not not_76 (not_76_out, OP2);
  not not_77 (not_77_out, OP1);
  not not_78 (not_78_out, OP0);
  not not_79 (not_79_out, F5);
  not not_80 (not_80_out, F4);
  not not_81 (not_81_out, F3);
  not not_82 (not_82_out, F2);
  not not_83 (not_83_out, F0);
  not not_84 (not_84_out, OP5);
  not not_85 (not_85_out, OP4);
  not not_86 (not_86_out, OP3);
  not not_87 (not_87_out, OP2);
  not not_88 (not_88_out, OP1);
  not not_89 (not_89_out, OP0);
  not not_90 (not_90_out, F4);
  not not_91 (not_91_out, F3);
  not not_92 (not_92_out, F2);
  not not_93 (not_93_out, F0);
  not not_94 (not_94_out, OP5);
  not not_95 (not_95_out, OP4);
  not not_96 (not_96_out, OP3);
  not not_97 (not_97_out, OP2);
  not not_98 (not_98_out, OP1);
  not not_99 (not_99_out, OP0);
  not not_100 (not_100_out, F4);
  not not_101 (not_101_out, F3);
  not not_102 (not_102_out, F1);
  not not_103 (not_103_out, F0);
  not not_104 (not_104_out, OP5);
  not not_105 (not_105_out, OP4);
  not not_106 (not_106_out, OP3);
  not not_107 (not_107_out, OP2);
  not not_108 (not_108_out, OP1);
  not not_109 (not_109_out, OP0);
  not not_110 (not_110_out, F4);
  not not_111 (not_111_out, F3);
  not not_112 (not_112_out, OP5);
  not not_113 (not_113_out, OP4);
  not not_114 (not_114_out, OP3);
  not not_115 (not_115_out, OP2);
  not not_116 (not_116_out, OP1);
  not not_117 (not_117_out, OP0);
  not not_118 (not_118_out, F4);
  not not_119 (not_119_out, F2);
  not not_120 (not_120_out, F0);
  not not_121 (not_121_out, OP5);
  not not_122 (not_122_out, OP4);
  not not_123 (not_123_out, OP1);
  not not_124 (not_124_out, OP0);
  not not_125 (not_125_out, OP5);
  not not_126 (not_126_out, OP4);
  not not_127 (not_127_out, OP2);
  not not_128 (not_128_out, OP0);
  not not_129 (not_129_out, OP5);
  not not_130 (not_130_out, OP4);
  not not_131 (not_131_out, OP3);
  not not_132 (not_132_out, OP2);
  not not_133 (not_133_out, OP1);
  not not_134 (not_134_out, OP0);
  not not_135 (not_135_out, F4);
  not not_136 (not_136_out, F3);
  not not_137 (not_137_out, F2);
  not not_138 (not_138_out, F1);
  not not_139 (not_139_out, F0);
  not not_140 (not_140_out, OP5);
  not not_141 (not_141_out, OP4);
  not not_142 (not_142_out, OP3);
  not not_143 (not_143_out, OP2);
  not not_144 (not_144_out, OP1);
  not not_145 (not_145_out, OP0);
  not not_146 (not_146_out, F4);
  not not_147 (not_147_out, F3);
  not not_148 (not_148_out, F2);
  not not_149 (not_149_out, F1);
  not not_150 (not_150_out, OP5);
  not not_151 (not_151_out, OP4);
  not not_152 (not_152_out, OP3);
  not not_153 (not_153_out, OP2);
  not not_154 (not_154_out, OP1);
  not not_155 (not_155_out, OP0);
  not not_156 (not_156_out, F4);
  not not_157 (not_157_out, F3);
  not not_158 (not_158_out, F2);
  not not_159 (not_159_out, F0);
  not not_160 (not_160_out, OP5);
  not not_161 (not_161_out, OP4);
  not not_162 (not_162_out, OP3);
  not not_163 (not_163_out, OP2);
  not not_164 (not_164_out, OP1);
  not not_165 (not_165_out, OP0);
  not not_166 (not_166_out, F4);
  not not_167 (not_167_out, F3);
  not not_168 (not_168_out, F1);
  not not_169 (not_169_out, F0);
  not not_170 (not_170_out, OP5);
  not not_171 (not_171_out, OP4);
  not not_172 (not_172_out, OP3);
  not not_173 (not_173_out, OP2);
  not not_174 (not_174_out, OP1);
  not not_175 (not_175_out, OP0);
  not not_176 (not_176_out, F4);
  not not_177 (not_177_out, F2);
  not not_178 (not_178_out, OP5);
  not not_179 (not_179_out, OP4);
  not not_180 (not_180_out, OP2);
  not not_181 (not_181_out, OP1);
  not not_182 (not_182_out, OP0);
  not not_183 (not_183_out, OP5);
  not not_184 (not_184_out, OP4);
  not not_185 (not_185_out, OP1);
  not not_186 (not_186_out, OP0);
  not not_187 (not_187_out, OP5);
  not not_188 (not_188_out, OP4);
  not not_189 (not_189_out, OP2);
  not not_190 (not_190_out, OP1);
  not not_191 (not_191_out, OP4);
  not not_192 (not_192_out, OP3);
  not not_193 (not_193_out, OP2);
  not not_194 (not_194_out, OP4);
  not not_195 (not_195_out, OP2);
  not not_196 (not_196_out, OP5);
  not not_197 (not_197_out, OP4);
  not not_198 (not_198_out, OP3);
  not not_199 (not_199_out, OP2);
  not not_200 (not_200_out, OP1);
  not not_201 (not_201_out, OP0);
  not not_202 (not_202_out, F4);
  not not_203 (not_203_out, F3);
  not not_204 (not_204_out, F1);
  not not_205 (not_205_out, OP5);
  not not_206 (not_206_out, OP4);
  not not_207 (not_207_out, OP3);
  not not_208 (not_208_out, OP2);
  not not_209 (not_209_out, OP1);
  not not_210 (not_210_out, OP0);
  not not_211 (not_211_out, F4);
  not not_212 (not_212_out, F3);
  not not_213 (not_213_out, OP5);
  not not_214 (not_214_out, OP4);
  not not_215 (not_215_out, OP3);
  not not_216 (not_216_out, OP2);
  not not_217 (not_217_out, OP1);
  not not_218 (not_218_out, OP0);
  not not_219 (not_219_out, F4);
  not not_220 (not_220_out, F2);
  not not_221 (not_221_out, F0);
  not not_222 (not_222_out, OP5);
  not not_223 (not_223_out, OP4);
  not not_224 (not_224_out, OP3);
  not not_225 (not_225_out, OP2);
  not not_226 (not_226_out, OP1);
  not not_227 (not_227_out, OP0);
  not not_228 (not_228_out, F4);
  not not_229 (not_229_out, F2);
  not not_230 (not_230_out, OP5);
  not not_231 (not_231_out, OP4);
  not not_232 (not_232_out, OP2);
  not not_233 (not_233_out, OP0);
  not not_234 (not_234_out, OP5);
  not not_235 (not_235_out, OP4);
  not not_236 (not_236_out, OP1);
  and and_1 (and_1_out, not_1_out, not_2_out, not_3_out, not_4_out, not_5_out, not_6_out, not_7_out, not_8_out, not_9_out, not_10_out, F1, F0);
  and and_2 (and_2_out, not_11_out, not_12_out, not_13_out, not_14_out, not_15_out, not_16_out, F5, not_17_out, not_18_out, not_19_out, not_20_out, not_21_out);
  and and_3 (and_3_out, not_22_out, not_23_out, not_24_out, not_25_out, not_26_out, not_27_out, F5, not_28_out, not_29_out, not_30_out, not_31_out, F0);
  and and_4 (and_4_out, not_32_out, not_33_out, not_34_out, not_35_out, not_36_out, not_37_out, F5, not_38_out, not_39_out, F2, not_40_out, not_41_out);
  and and_5 (and_5_out, not_42_out, not_43_out, not_44_out, not_45_out, not_46_out, not_47_out, F5, not_48_out, F3, not_49_out, F1, not_50_out);
  and and_6 (and_6_out, not_51_out, not_52_out, OP3, not_53_out, not_54_out, not_55_out);
  and and_7 (and_7_out, not_56_out, not_57_out, OP3, OP2, not_58_out, not_59_out);
  and and_8 (and_8_out, not_60_out, not_61_out, OP3, not_62_out, not_63_out, OP0);
  and and_9 (and_9_out, not_64_out, not_65_out, OP3, not_66_out, OP1, not_67_out);
  and and_10 (and_10_out, OP5, not_68_out, not_69_out, not_70_out, OP1, OP0);
  and and_11 (and_11_out, OP5, not_71_out, OP3, not_72_out, OP1, OP0);
  and and_12 (and_12_out, not_73_out, not_74_out, not_75_out, not_76_out, not_77_out, not_78_out, not_79_out, not_80_out, not_81_out, not_82_out, F1, not_83_out);
  and and_13 (and_13_out, not_84_out, not_85_out, not_86_out, not_87_out, not_88_out, not_89_out, F5, not_90_out, not_91_out, not_92_out, F1, not_93_out);
  and and_14 (and_14_out, not_94_out, not_95_out, not_96_out, not_97_out, not_98_out, not_99_out, F5, not_100_out, not_101_out, F2, not_102_out, not_103_out);
  and and_15 (and_15_out, not_104_out, not_105_out, not_106_out, not_107_out, not_108_out, not_109_out, F5, not_110_out, not_111_out, F2, F1, F0);
  and and_16 (and_16_out, not_112_out, not_113_out, not_114_out, not_115_out, not_116_out, not_117_out, F5, not_118_out, F3, not_119_out, F1, not_120_out);
  and and_17 (and_17_out, not_121_out, not_122_out, OP3, OP2, not_123_out, not_124_out);
  and and_18 (and_18_out, not_125_out, not_126_out, OP3, not_127_out, OP1, not_128_out);
  and and_19 (and_19_out, not_129_out, not_130_out, not_131_out, not_132_out, not_133_out, not_134_out, F5, not_135_out, not_136_out, not_137_out, not_138_out, not_139_out);
  and and_20 (and_20_out, not_140_out, not_141_out, not_142_out, not_143_out, not_144_out, not_145_out, F5, not_146_out, not_147_out, not_148_out, not_149_out, F0);
  and and_21 (and_21_out, not_150_out, not_151_out, not_152_out, not_153_out, not_154_out, not_155_out, F5, not_156_out, not_157_out, not_158_out, F1, not_159_out);
  and and_22 (and_22_out, not_160_out, not_161_out, not_162_out, not_163_out, not_164_out, not_165_out, F5, not_166_out, not_167_out, F2, not_168_out, not_169_out);
  and and_23 (and_23_out, not_170_out, not_171_out, not_172_out, not_173_out, not_174_out, not_175_out, F5, not_176_out, F3, not_177_out, F1, F0);
  and and_24 (and_24_out, not_178_out, not_179_out, OP3, not_180_out, not_181_out, not_182_out);
  and and_25 (and_25_out, not_183_out, not_184_out, OP3, OP2, not_185_out, not_186_out);
  and and_26 (and_26_out, not_187_out, not_188_out, OP3, not_189_out, not_190_out, OP0);
  and and_27 (and_27_out, OP5, not_191_out, not_192_out, not_193_out, OP1, OP0);
  and and_28 (and_28_out, OP5, not_194_out, OP3, not_195_out, OP1, OP0);
  and and_29 (and_29_out, not_196_out, not_197_out, not_198_out, not_199_out, not_200_out, not_201_out, F5, not_202_out, not_203_out, F2, not_204_out, F0);
  and and_30 (and_30_out, not_205_out, not_206_out, not_207_out, not_208_out, not_209_out, not_210_out, F5, not_211_out, not_212_out, F2, F1, F0);
  and and_31 (and_31_out, not_213_out, not_214_out, not_215_out, not_216_out, not_217_out, not_218_out, F5, not_219_out, F3, not_220_out, F1, not_221_out);
  and and_32 (and_32_out, not_222_out, not_223_out, not_224_out, not_225_out, not_226_out, not_227_out, F5, not_228_out, F3, not_229_out, F1, F0);
  and and_33 (and_33_out, not_230_out, not_231_out, OP3, not_232_out, OP1, not_233_out);
  and and_34 (and_34_out, not_234_out, not_235_out, OP3, OP2, not_236_out, OP0);
  or or_1 (S0, and_1_out, and_2_out, and_3_out, and_4_out, and_5_out, and_6_out, and_7_out, and_8_out, and_9_out, and_10_out, and_11_out);
  or or_2 (S1, and_12_out, and_13_out, and_14_out, and_15_out, and_16_out, and_17_out, and_18_out);
  or or_3 (S2, and_19_out, and_20_out, and_21_out, and_22_out, and_23_out, and_24_out, and_25_out, and_26_out, and_27_out, and_28_out);
  or or_4 (S3, and_29_out, and_30_out, and_31_out, and_32_out, and_33_out, and_34_out);
endmodule

// 控制信号生成
module \控制信号自动生成  (
  input  OP0,
  input  OP1,
  input  OP2,
  input  OP3,
  input  OP4,
  input  OP5,
  input  F0,
  input  F1,
  input  F2,
  input  F3,
  input  F4,
  input  F5,
  output MemToReg,
  output MemWrite,
  output ALU_SRC,
  output RegWrite,
  output SysCALL,
  output SignedExt,
  output RegDst,
  output BEQ,
  output BNE,
  output JR,
  output JUMP,
  output JAL,
  output ERET
);

  wire and_3_out, and_4_out, and_5_out, and_6_out, and_7_out, and_8_out, and_9_out, and_10_out, and_11_out,
       and_12_out, and_13_out, and_15_out, and_16_out, and_17_out, and_18_out, and_19_out, and_20_out,
       and_21_out, and_22_out, and_23_out, and_27_out, and_28_out, not_1_out, not_2_out, not_3_out,
       not_4_out, not_5_out, not_6_out, not_7_out, not_8_out, not_9_out, not_10_out, not_11_out, not_12_out,
       not_13_out, not_14_out, not_15_out, not_16_out, not_17_out, not_18_out, not_19_out, not_20_out,
       not_21_out, not_22_out, not_23_out, not_24_out, not_25_out, not_26_out, not_27_out, not_28_out,
       not_29_out, not_30_out, not_31_out, not_32_out, not_33_out, not_34_out, not_35_out, not_36_out,
       not_37_out, not_38_out, not_39_out, not_40_out, not_41_out, not_42_out, not_43_out, not_44_out,
       not_45_out, not_46_out, not_47_out, not_48_out, not_49_out, not_50_out, not_51_out, not_52_out,
       not_53_out, not_54_out, not_55_out, not_56_out, not_57_out, not_58_out, not_59_out, not_60_out,
       not_61_out, not_62_out, not_63_out, not_64_out, not_65_out, not_66_out, not_67_out, not_68_out,
       not_69_out, not_70_out, not_71_out, not_72_out, not_73_out, not_74_out, not_75_out, not_76_out,
       not_77_out, not_78_out, not_79_out, not_80_out, not_81_out, not_82_out, not_83_out, not_84_out,
       not_85_out, not_86_out, not_87_out, not_88_out, not_89_out, not_90_out, not_91_out, not_92_out,
       not_93_out, not_94_out, not_95_out, not_96_out, not_97_out, not_98_out, not_99_out, not_100_out,
       not_101_out, not_102_out, not_103_out, not_104_out, not_105_out, not_106_out, not_107_out,
       not_108_out, not_109_out, not_110_out, not_111_out, not_112_out, not_113_out, not_114_out,
       not_115_out, not_116_out, not_117_out, not_118_out, not_119_out, not_120_out, not_121_out,
       not_122_out, not_123_out, not_124_out, not_125_out, not_126_out, not_127_out, not_128_out,
       not_129_out, not_130_out, not_131_out, not_132_out, not_133_out, not_134_out, not_135_out,
       not_136_out, not_137_out, not_138_out, not_139_out, not_140_out, not_141_out, not_142_out,
       not_143_out, not_144_out, not_145_out, not_146_out, not_147_out, not_148_out, not_149_out,
       not_150_out, not_151_out, not_152_out, not_153_out, not_154_out, not_155_out, not_156_out,
       not_157_out, not_158_out, not_159_out, not_160_out, not_161_out, not_162_out, not_163_out,
       not_164_out, not_165_out, not_166_out, not_167_out, not_168_out, not_169_out, not_170_out,
       not_171_out, not_172_out, not_173_out, not_174_out, not_175_out, not_176_out, not_177_out,
       not_178_out, not_179_out, not_180_out, not_181_out, not_182_out, not_183_out, not_184_out,
       not_185_out, not_186_out, not_187_out;

  not not_1 (not_1_out, OP2);
  not not_2 (not_2_out, OP3);
  not not_3 (not_3_out, OP4);
  not not_4 (not_4_out, OP2);
  not not_5 (not_5_out, OP4);
  not not_6 (not_6_out, OP0);
  not not_7 (not_7_out, OP2);
  not not_8 (not_8_out, OP4);
  not not_9 (not_9_out, OP5);
  not not_10 (not_10_out, OP1);
  not not_11 (not_11_out, OP4);
  not not_12 (not_12_out, OP5);
  not not_13 (not_13_out, OP2);
  not not_14 (not_14_out, OP4);
  not not_15 (not_15_out, OP0);
  not not_16 (not_16_out, OP1);
  not not_17 (not_17_out, OP2);
  not not_18 (not_18_out, OP4);
  not not_19 (not_19_out, OP5);
  not not_20 (not_20_out, F0);
  not not_21 (not_21_out, F2);
  not not_22 (not_22_out, F3);
  not not_23 (not_23_out, F4);
  not not_24 (not_24_out, OP0);
  not not_25 (not_25_out, OP1);
  not not_26 (not_26_out, OP2);
  not not_27 (not_27_out, OP4);
  not not_28 (not_28_out, OP5);
  not not_29 (not_29_out, F1);
  not not_30 (not_30_out, F3);
  not not_31 (not_31_out, F4);
  not not_32 (not_32_out, OP0);
  not not_33 (not_33_out, OP1);
  not not_34 (not_34_out, OP2);
  not not_35 (not_35_out, OP4);
  not not_36 (not_36_out, OP5);
  not not_37 (not_37_out, F2);
  not not_38 (not_38_out, F3);
  not not_39 (not_39_out, F4);
  not not_40 (not_40_out, F5);
  not not_41 (not_41_out, OP0);
  not not_42 (not_42_out, OP1);
  not not_43 (not_43_out, OP2);
  not not_44 (not_44_out, OP4);
  not not_45 (not_45_out, OP5);
  not not_46 (not_46_out, F2);
  not not_47 (not_47_out, F4);
  not not_48 (not_48_out, OP0);
  not not_49 (not_49_out, OP1);
  not not_50 (not_50_out, OP2);
  not not_51 (not_51_out, OP4);
  not not_52 (not_52_out, OP5);
  not not_53 (not_53_out, F3);
  not not_54 (not_54_out, F4);
  not not_55 (not_55_out, OP0);
  not not_56 (not_56_out, OP2);
  not not_57 (not_57_out, OP4);
  not not_58 (not_58_out, OP5);
  not not_59 (not_59_out, OP1);
  not not_60 (not_60_out, OP4);
  not not_61 (not_61_out, OP5);
  not not_62 (not_62_out, OP2);
  not not_63 (not_63_out, OP3);
  not not_64 (not_64_out, OP4);
  not not_65 (not_65_out, OP0);
  not not_66 (not_66_out, OP1);
  not not_67 (not_67_out, OP2);
  not not_68 (not_68_out, OP3);
  not not_69 (not_69_out, OP4);
  not not_70 (not_70_out, OP5);
  not not_71 (not_71_out, F0);
  not not_72 (not_72_out, F1);
  not not_73 (not_73_out, F4);
  not not_74 (not_74_out, F5);
  not not_75 (not_75_out, OP0);
  not not_76 (not_76_out, OP2);
  not not_77 (not_77_out, OP4);
  not not_78 (not_78_out, OP5);
  not not_79 (not_79_out, OP1);
  not not_80 (not_80_out, OP2);
  not not_81 (not_81_out, OP4);
  not not_82 (not_82_out, OP5);
  not not_83 (not_83_out, OP2);
  not not_84 (not_84_out, OP4);
  not not_85 (not_85_out, OP0);
  not not_86 (not_86_out, OP1);
  not not_87 (not_87_out, OP2);
  not not_88 (not_88_out, OP3);
  not not_89 (not_89_out, OP4);
  not not_90 (not_90_out, OP5);
  not not_91 (not_91_out, F0);
  not not_92 (not_92_out, F1);
  not not_93 (not_93_out, F2);
  not not_94 (not_94_out, F4);
  not not_95 (not_95_out, F5);
  not not_96 (not_96_out, OP0);
  not not_97 (not_97_out, OP1);
  not not_98 (not_98_out, OP2);
  not not_99 (not_99_out, OP3);
  not not_100 (not_100_out, OP4);
  not not_101 (not_101_out, OP5);
  not not_102 (not_102_out, F0);
  not not_103 (not_103_out, F2);
  not not_104 (not_104_out, F3);
  not not_105 (not_105_out, F4);
  not not_106 (not_106_out, OP0);
  not not_107 (not_107_out, OP1);
  not not_108 (not_108_out, OP2);
  not not_109 (not_109_out, OP3);
  not not_110 (not_110_out, OP4);
  not not_111 (not_111_out, OP5);
  not not_112 (not_112_out, F1);
  not not_113 (not_113_out, F3);
  not not_114 (not_114_out, F4);
  not not_115 (not_115_out, OP0);
  not not_116 (not_116_out, OP1);
  not not_117 (not_117_out, OP2);
  not not_118 (not_118_out, OP3);
  not not_119 (not_119_out, OP4);
  not not_120 (not_120_out, OP5);
  not not_121 (not_121_out, F2);
  not not_122 (not_122_out, F3);
  not not_123 (not_123_out, F4);
  not not_124 (not_124_out, F5);
  not not_125 (not_125_out, OP0);
  not not_126 (not_126_out, OP1);
  not not_127 (not_127_out, OP2);
  not not_128 (not_128_out, OP3);
  not not_129 (not_129_out, OP4);
  not not_130 (not_130_out, OP5);
  not not_131 (not_131_out, F2);
  not not_132 (not_132_out, F4);
  not not_133 (not_133_out, OP0);
  not not_134 (not_134_out, OP1);
  not not_135 (not_135_out, OP2);
  not not_136 (not_136_out, OP3);
  not not_137 (not_137_out, OP4);
  not not_138 (not_138_out, OP5);
  not not_139 (not_139_out, F3);
  not not_140 (not_140_out, F4);
  not not_141 (not_141_out, OP0);
  not not_142 (not_142_out, OP1);
  not not_143 (not_143_out, OP3);
  not not_144 (not_144_out, OP4);
  not not_145 (not_145_out, OP5);
  not not_146 (not_146_out, OP1);
  not not_147 (not_147_out, OP3);
  not not_148 (not_148_out, OP4);
  not not_149 (not_149_out, OP5);
  not not_150 (not_150_out, OP0);
  not not_151 (not_151_out, OP1);
  not not_152 (not_152_out, OP2);
  not not_153 (not_153_out, OP3);
  not not_154 (not_154_out, OP4);
  not not_155 (not_155_out, OP5);
  not not_156 (not_156_out, F0);
  not not_157 (not_157_out, F1);
  not not_158 (not_158_out, F2);
  not not_159 (not_159_out, F4);
  not not_160 (not_160_out, F5);
  not not_161 (not_161_out, OP0);
  not not_162 (not_162_out, OP2);
  not not_163 (not_163_out, OP3);
  not not_164 (not_164_out, OP4);
  not not_165 (not_165_out, OP5);
  not not_166 (not_166_out, F0);
  not not_167 (not_167_out, F1);
  not not_168 (not_168_out, F2);
  not not_169 (not_169_out, F4);
  not not_170 (not_170_out, F5);
  not not_171 (not_171_out, OP2);
  not not_172 (not_172_out, OP3);
  not not_173 (not_173_out, OP4);
  not not_174 (not_174_out, OP5);
  not not_175 (not_175_out, OP2);
  not not_176 (not_176_out, OP3);
  not not_177 (not_177_out, OP4);
  not not_178 (not_178_out, OP5);
  not not_179 (not_179_out, OP5);
  not not_180 (not_180_out, OP3);
  not not_181 (not_181_out, OP2);
  not not_182 (not_182_out, OP1);
  not not_183 (not_183_out, OP0);
  not not_184 (not_184_out, F5);
  not not_185 (not_185_out, F2);
  not not_186 (not_186_out, F1);
  not not_187 (not_187_out, F0);
  and and_1 (MemToReg, OP0, OP1, not_1_out, not_2_out, not_3_out, OP5);
  and and_2 (MemWrite, OP0, OP1, not_4_out, OP3, not_5_out, OP5);
  and and_3 (and_3_out, not_6_out, not_7_out, OP3, not_8_out, not_9_out);
  or or_1 (ALU_SRC, and_3_out, and_4_out, and_5_out);
  and and_4 (and_4_out, not_10_out, OP3, not_11_out, not_12_out);
  and and_5 (and_5_out, OP0, OP1, not_13_out, not_14_out, OP5);
  and and_6 (and_6_out, not_15_out, not_16_out, not_17_out, not_18_out, not_19_out, not_20_out, not_21_out, not_22_out, not_23_out);
  and and_7 (and_7_out, not_24_out, not_25_out, not_26_out, not_27_out, not_28_out, not_29_out, not_30_out, not_31_out, F5);
  and and_8 (and_8_out, not_32_out, not_33_out, not_34_out, not_35_out, not_36_out, F1, not_37_out, not_38_out, not_39_out, not_40_out);
  and and_9 (and_9_out, not_41_out, not_42_out, not_43_out, not_44_out, not_45_out, F1, not_46_out, F3, not_47_out, F5);
  and and_10 (and_10_out, not_48_out, not_49_out, not_50_out, not_51_out, not_52_out, F0, F2, not_53_out, not_54_out, F5);
  and and_11 (and_11_out, not_55_out, not_56_out, OP3, not_57_out, not_58_out);
  and and_12 (and_12_out, not_59_out, OP3, not_60_out, not_61_out);
  and and_13 (and_13_out, OP0, OP1, not_62_out, not_63_out, not_64_out);
  and and_14 (SysCALL, not_65_out, not_66_out, not_67_out, not_68_out, not_69_out, not_70_out, not_71_out, not_72_out, F2, F3, not_73_out, not_74_out);
  and and_15 (and_15_out, not_75_out, not_76_out, OP3, not_77_out, not_78_out);
  or or_2 (SignedExt, and_15_out, and_16_out, and_17_out);
  and and_16 (and_16_out, not_79_out, not_80_out, OP3, not_81_out, not_82_out);
  and and_17 (and_17_out, OP0, OP1, not_83_out, not_84_out, OP5);
  and and_18 (and_18_out, not_85_out, not_86_out, not_87_out, not_88_out, not_89_out, not_90_out, not_91_out, not_92_out, not_93_out, not_94_out, not_95_out);
  and and_19 (and_19_out, not_96_out, not_97_out, not_98_out, not_99_out, not_100_out, not_101_out, not_102_out, not_103_out, not_104_out, not_105_out);
  and and_20 (and_20_out, not_106_out, not_107_out, not_108_out, not_109_out, not_110_out, not_111_out, not_112_out, not_113_out, not_114_out, F5);
  and and_21 (and_21_out, not_115_out, not_116_out, not_117_out, not_118_out, not_119_out, not_120_out, F1, not_121_out, not_122_out, not_123_out, not_124_out);
  and and_22 (and_22_out, not_125_out, not_126_out, not_127_out, not_128_out, not_129_out, not_130_out, F1, not_131_out, F3, not_132_out, F5);
  and and_23 (and_23_out, not_133_out, not_134_out, not_135_out, not_136_out, not_137_out, not_138_out, F0, F2, not_139_out, not_140_out, F5);
  and and_24 (BEQ, not_141_out, not_142_out, OP2, not_143_out, not_144_out, not_145_out);
  and and_25 (BNE, OP0, not_146_out, OP2, not_147_out, not_148_out, not_149_out);
  and and_26 (JR, not_150_out, not_151_out, not_152_out, not_153_out, not_154_out, not_155_out, not_156_out, not_157_out, not_158_out, F3, not_159_out, not_160_out);
  and and_27 (and_27_out, not_161_out, not_162_out, not_163_out, not_164_out, not_165_out, not_166_out, not_167_out, not_168_out, F3, not_169_out, not_170_out);
  and and_28 (and_28_out, OP1, not_171_out, not_172_out, not_173_out, not_174_out);
  and and_29 (JAL, OP0, OP1, not_175_out, not_176_out, not_177_out, not_178_out);
  and and_30 (ERET, not_179_out, OP4, not_180_out, not_181_out, not_182_out, not_183_out, not_184_out, F4, F3, not_185_out, not_186_out, not_187_out);
  or or_3 (RegWrite, and_6_out, and_7_out, and_8_out, and_9_out, and_10_out, and_11_out, and_12_out, and_13_out);
  or or_4 (RegDst, and_18_out, and_19_out, and_20_out, and_21_out, and_22_out, and_23_out);
  or or_5 (JUMP, and_27_out, and_28_out);
endmodule

// ALU
module MIPS_ALU (
  input  [4:0] shamt,
  input  [31:0] X,
  input  [31:0] Y,
  input  [3:0] AluOP,
  output Equal,
  output [31:0] Result,
  output [31:0] Result_2
);

  wire [0:0] comparator_1_lt, comparator_2_lt;
  wire [31:0] adder_1_out, AND_out, divider_1_out, divider_1_rem, multiplier_1_cout, multiplier_1_out,
       NOR_out, OR_out, shifter_1_out, shifter_2_out, shifter_3_out, subtractor_1_out, XOR_out;

  assign AND_out = X & Y;  // AND_Gate AND, 32 bits wide
  assign OR_out = X | Y;  // OR_Gate OR, 32 bits wide
  Shifter #(.width(32), .shift("ll")) shifter_1 (.in(Y), .\dist (shamt), .out(shifter_1_out));
  Shifter #(.width(32), .shift("ar")) shifter_2 (.in(Y), .\dist (shamt), .out(shifter_2_out));
  Shifter #(.width(32), .shift("lr")) shifter_3 (.in(Y), .\dist (shamt), .out(shifter_3_out));
  Multiplier #(.width(32)) multiplier_1 (.a(X), .b(Y), .out(multiplier_1_out), .cout(multiplier_1_cout));  // open: cin
  Divider #(.width(32)) divider_1 (.a(X), .b(Y), .out(divider_1_out), .rem(divider_1_rem));  // open: upper
  Adder #(.width(32)) adder_1 (.a(X), .b(Y), .out(adder_1_out));  // open: cin, cout
  Subtractor #(.width(32)) subtractor_1 (.a(X), .b(Y), .out(subtractor_1_out));  // open: bin, bout
  assign XOR_out = X ^ Y;  // XOR_Gate XOR, 32 bits wide
  assign NOR_out = ~(X | Y);  // NOR_Gate NOR, 32 bits wide
  Comparator #(.width(32), .mode("twosComplement")) comparator_1 (
    .a(X), .b(Y), .eq(Equal), .lt(comparator_1_lt[0]));  // open: gt
  Comparator #(.width(32), .mode("unsigned")) comparator_2 (.a(X), .b(Y), .lt(comparator_2_lt[0]));  // open: gt, eq
  Multiplexer #(.select(4), .width(32), .disabled("Z"), .enable("false")) multiplexer_1 (
    .in0(shifter_1_out), .in1(shifter_2_out), .in2(shifter_3_out), .in3(multiplier_1_out),
    .in4(divider_1_out), .in5(adder_1_out), .in6(subtractor_1_out), .in7(AND_out), .in8(OR_out),
    .in9(XOR_out), .in10(NOR_out), .in11({{31{1'b0}}, comparator_1_lt[0]}),
    .in12({{31{1'b0}}, comparator_2_lt[0]}), .in13({32{1'b0}}), .in14({32{1'b0}}), .in15({32{1'b0}}),
    .out(Result), .sel(AluOP));
  Multiplexer #(.select(4), .width(32), .disabled("Z"), .enable("false")) multiplexer_2 (
    .in0({32{1'b0}}), .in1({32{1'b0}}), .in2({32{1'b0}}), .in3(multiplier_1_cout), .in4(divider_1_rem),
    .in5({32{1'b0}}), .in6({32{1'b0}}), .in7({32{1'b0}}), .in8({32{1'b0}}), .in9({32{1'b0}}),
    .in10({32{1'b0}}), .in11({32{1'b0}}), .in12({32{1'b0}}), .in13({32{1'b0}}), .in14({32{1'b0}}),
    .in15({32{1'b0}}), .out(Result_2), .sel(AluOP));

  // Other names for the same wires on the sheet: Result2[31:0] = Result_2; S[3:0] = AluOP

  // Notes on the sheet:
  //   不要改变此引脚区域内容，也不要改变ALU封装形式
  //   输入引脚
  //   输出引脚
endmodule

module MIPS_Regifile (
  input  [31:0] Din,
  input  Clk,
  input  WE,
  input  [4:0] R1_num,
  input  [4:0] W_num,
  input  [4:0] R2_num,
  output [31:0] R1,
  output [31:0] R2
);

  // RegisterFile registerfile_1: pin names not known; wires that end beside it: Din, Clk, WE, W_num, R1_num, R2_num, R1, R2
endmodule

module \理想流水线  (
  output RegWrite,
  output MemWrite,
  output [31:0] IF_PC,
  output [31:0] ID_PC,
  output [31:0] EX_PC,
  output [31:0] M_PC,
  output [31:0] WB_PC,
  output [31:0] RDin,
  output [31:0] MDin,
  output [31:0] LedData
);

  wire alu_srcb, beq, bne, CLK, clock_1_out, clock_2_out, comparator_1_eq, comparator_1_lt, comparator_2_eq,
       d_ff_1_q, d_ff_1_qn, d_ff_2_q, EX_MEM_out_25, EX_MEM_out_26, Go, Halt, ID_EX_out_24, ID_EX_out_25,
       ID_EX_out_26, ID_EX_out_27, ID_EX_out_28, ID_EX_out_29, \ID_EX_当前传输数据有效_输出 , \IF_ID_输出数据有效 , IR1, IR2,
       IR3, jal, jmp, jr, mem_to_reg, mem_write, nand_1_out, not_1_out, reg_dst, reg_dst_back, reg_write,
       RST, signed_ext, syscall, W1, W2, W3;
  wire [0:0] EX_MEM_out_22;
  wire [3:0] alu_op, ID_EX_out_31;
  wire [4:0] multiplexer_2_out, multiplexer_3_out, multiplexer_4_out;
  wire [5:0] Func;
  wire [12:0] CNT_num;
  wire [15:0] \LoadUse次数 , \总周期数 , \插入气泡数 , \无条件分支数 , \条件分支成功数 ;
  wire [31:0] adder_1_out, adder_2_out, bit_extender_1_out, bit_extender_2_out, EX_IR, \EX_MEM_alurst输出 ,
       \ID_EX_imm输出 , \ID_EX_rd1输出 , \ID_EX_rd2输出 , IF_IR, MEM_IR, mips_alu_1_result, mips_regifile_1_r1,
       mips_regifile_1_r2, multiplexer_1_out, multiplexer_5_out, multiplexer_6_out, multiplexer_7_out,
       ram_1_data, WB_IR;
  wire [31:6] ID_IR;

  Button \u_总复位  (.out(RST));
  Button _1 (.out(IR1));
  Button _2 (.out(IR2));
  Button _3 (.out(IR3));
  // Probe on \总周期数 
  // Probe on \总周期数 
  Button \u_继续运行  (.out(Go));
  LED #(.active("true")) led_1 (.in(W1));
  LED #(.active("true")) led_2 (.in(W2));
  LED #(.active("true")) led_3 (.in(W3));
  Hex_Digit_Display hex_digit_display_1 (.value(LedData[31:28]));  // open: dp
  // Probe on IF_PC[19:0]
  // Mips_Probe mips_probe_1: pin names not known; wires that end beside it: IF_IR
  D_Flip_Flop #(.trigger("rising"), .Pre_Clr_Positions("ABOVE_BELOW"), .NegatePresetClear("false"), .enable("false"), .NewFFLayout("true")) d_ff_1 (
    .clk(Halt), .D(d_ff_1_qn), .Q(d_ff_1_q), .Qn(d_ff_1_qn));  // open: preset, reset
  Hex_Digit_Display hex_digit_display_2 (.value(LedData[23:20]));  // open: dp
  Hex_Digit_Display hex_digit_display_3 (.value(LedData[27:24]));  // open: dp
  // Probe on ID_PC[19:0]
  // Mips_Probe mips_probe_2: pin names not known; wires that end beside it: {ID_IR, Func}
  Multiplexer #(.select(1), .width(32), .disabled("Z"), .enable("false")) multiplexer_1 (
    .in0(adder_1_out), .in1(IF_PC), .out(multiplexer_1_out), .sel(1'b0));
  Hex_Digit_Display hex_digit_display_4 (.value(LedData[19:16]));  // open: dp
  Hex_Digit_Display hex_digit_display_5 (.value(LedData[15:12]));  // open: dp
  Register #(.width(32), .trigger("rising"), .Select("low")) PC (
    .D(multiplexer_1_out), .Q(IF_PC), .clk(CLK));  // open: en, clr
  Hex_Digit_Display hex_digit_display_6 (.value(LedData[7:4]));  // open: dp
  Hex_Digit_Display hex_digit_display_7 (.value(LedData[11:8]));  // open: dp
  Clock #(.highDuration(1), .lowDuration(1)) clock_1 (.out(clock_1_out));
  // Probe on EX_PC[19:0]
  // Mips_Probe mips_probe_3: pin names not known; wires that end beside it: clock_1_out, EX_IR, CLK
  Hex_Digit_Display hex_digit_display_8 (.value(LedData[3:0]));  // open: dp
  Adder #(.width(32)) adder_1 (.a(IF_PC), .b(32'h4), .out(adder_1_out));  // open: cin, cout
  // Probe on \总周期数 
  // Probe on M_PC[19:0]
  // Mips_Probe mips_probe_4: pin names not known; wires that end beside it: MEM_IR, ID_IR[31:26]
  // Probe on \总周期数 
  // Probe on \无条件分支数 
  // Probe on \条件分支成功数 
  // Probe on \插入气泡数 
  // Probe on \LoadUse次数 
  \单周期硬布线控制器  \u_单周期硬布线控制器_1  (
    .Func(Func), .OP(ID_IR[31:26]), .ALU_OP(alu_op), .MemToReg(mem_to_reg), .MemWrite(mem_write),
    .ALU_SRC(alu_srcb), .RegWrite(reg_write), .SysCALL(syscall), .SignedExt(signed_ext), .RegDst(reg_dst),
    .JR(jr), .JMP(jmp), .Beq(beq), .JAL(jal), .Bne(bne));  // open: ERET
  ROM #(.addrWidth(10), .dataWidth(32), .Select("high")) \u_指令存储器  (.addr(IF_PC[11:2]), .data(IF_IR));
  not not_1 (not_1_out, Halt);
  // Probe on IF_PC[11:0]
  // Probe on WB_PC[19:0]
  // Mips_Probe mips_probe_5: pin names not known; wires that end beside it: WB_IR
  Counter #(.width(16), .max('hffff), .ongoal("wrap"), .trigger("rising"), .behavior("new")) counter_1 (
    .count(not_1_out), .Q(\总周期数 ), .clk(CLK));  // open: load, D, carry, clr, preset, down
  // Probe on EX_PC[11:0]
  // Probe on ID_PC[11:0]
  // Probe on M_PC[11:0]
  D_Flip_Flop #(.trigger("high"), .Pre_Clr_Positions("LEGACY"), .NegatePresetClear("false"), .enable("true"), .NewFFLayout("false")) d_ff_2 (.Q(d_ff_2_q));  // open: clk, D, Qn, preset, en, reset
  // Probe on 13'hc
  // Probe on WB_PC[11:0]
  Comparator #(.width(13), .mode("twosComplement")) comparator_1 (
    .a(CNT_num), .b(13'hc), .eq(comparator_1_eq), .lt(comparator_1_lt));  // open: gt
  Clock #(.highDuration(1), .lowDuration(1)) clock_2 (.out(clock_2_out));
  IF_ID IF_ID (
    .\IR输入 (IF_IR), .\IR输出 ({ID_IR, Func}), .\输出数据有效 (\IF_ID_输出数据有效 ), .\PC输入 (IF_PC), .\PC输出 (ID_PC),
    .CLK(CLK));  // open: 输入数据有效, 清零_气泡_高, 使能端
  nand nand_1 (nand_1_out, d_ff_2_q, comparator_1_eq);
  Counter #(.width(13), .max('h1fff), .ongoal("stay"), .trigger("rising"), .behavior("old")) counter_2 (
    .count(comparator_1_lt), .Q(CNT_num), .clk(clock_2_out));  // open: load, D, carry, clr, preset
  assign CLK = nand_1_out ? clock_2_out : 1'bz;  // Controlled_Buffer controlled_buffer_1
  Multiplexer #(.select(1), .width(5), .disabled("Z"), .enable("false")) multiplexer_2 (
    .in0(ID_IR[25:21]), .in1(5'b00010), .out(multiplexer_2_out), .sel(syscall));
  Multiplexer #(.select(1), .width(5), .disabled("Z"), .enable("false")) multiplexer_3 (
    .in0(ID_IR[20:16]), .in1(5'b00100), .out(multiplexer_3_out), .sel(syscall));
  Multiplexer #(.select(1), .width(5), .disabled("Z"), .enable("false")) multiplexer_4 (
    .in0(WB_IR[20:16]), .in1(WB_IR[15:11]), .out(multiplexer_4_out), .sel(reg_dst_back));
  Pull_Resistor #(.pull(1)) pull_resistor_1 (.node(CLK));
  MIPS_Regifile mips_regifile_1 (
    .Din(RDin), .Clk(CLK), .R1(mips_regifile_1_r1), .R2(mips_regifile_1_r2), .WE(RegWrite),
    .W_num(multiplexer_4_out), .R1_num(multiplexer_2_out), .R2_num(multiplexer_3_out));
  assign bit_extender_1_out = {{16{1'b0}}, {ID_IR[15:6], Func}};  // Bit_Extender bit_extender_1
  assign bit_extender_2_out = {{16{ID_IR[15]}}, {ID_IR[15:6], Func}};  // Bit_Extender bit_extender_2
  Multiplexer #(.select(1), .width(32), .disabled("Z"), .enable("false")) multiplexer_5 (
    .in0(bit_extender_1_out), .in1(bit_extender_2_out), .out(multiplexer_5_out), .sel(signed_ext));
  ID_EX ID_EX (
    .\IR输入 ({ID_IR, Func}), .\PC输入 (ID_PC), .\RD1输入 (mips_regifile_1_r1), .\RD2输入 (mips_regifile_1_r2),
    .\Imm输入 (multiplexer_5_out), .\IR输出 (EX_IR), .\PC输出 (EX_PC), .\RD1输出 (\ID_EX_rd1输出 ),
    .\RD2输出 (\ID_EX_rd2输出 ), .\Imm输出 (\ID_EX_imm输出 ), .CLK(CLK), .in_6(signed_ext), .in_7(mem_to_reg),
    .in_8(mem_write), .in_9(alu_srcb), .in_10(reg_write), .in_11(reg_dst), .in_12(syscall),
    .\当前传输数据有效_输入 (\IF_ID_输出数据有效 ), .in_14(alu_op), .out_24(ID_EX_out_24), .out_25(ID_EX_out_25),
    .out_26(ID_EX_out_26), .out_27(ID_EX_out_27), .out_28(ID_EX_out_28), .out_29(ID_EX_out_29),
    .\当前传输数据有效_输出 (\ID_EX_当前传输数据有效_输出 ), .out_31(ID_EX_out_31));  // open: 同步清零_气泡_高, out_23, 使能端
  Comparator #(.width(32), .mode("twosComplement")) comparator_2 (
    .a(\ID_EX_rd1输出 ), .b(32'ha), .eq(comparator_2_eq));  // open: gt, lt
  Multiplexer #(.select(1), .width(32), .disabled("Z"), .enable("false")) multiplexer_6 (
    .in0(\ID_EX_rd2输出 ), .in1(\ID_EX_imm输出 ), .out(multiplexer_6_out), .sel(ID_EX_out_26));
  and and_1 (Halt, comparator_2_eq, ID_EX_out_29);
  MIPS_ALU mips_alu_1 (
    .X(\ID_EX_rd1输出 ), .Y(multiplexer_6_out), .AluOP(ID_EX_out_31), .Result(mips_alu_1_result),
    .shamt(EX_IR[10:6]));  // open: Equal, Result_2
  EX_MEM EX_MEM (
    .\IR输入 (EX_IR), .\PC输入 (EX_PC), .\AluRst输入 (mips_alu_1_result), .\Mem输入 (\ID_EX_rd2输出 ), .\IR输出 (MEM_IR),
    .\PC输出 (M_PC), .\AluRst输出 (\EX_MEM_alurst输出 ), .\Mem输出 (MDin), .in_6(ID_EX_out_24), .in_7(ID_EX_out_25),
    .in_9(ID_EX_out_27), .in_10(ID_EX_out_28), .\当前传输数据有效_输入 (\ID_EX_当前传输数据有效_输出 ),
    .out_22(EX_MEM_out_22[0]), .out_23(MemWrite), .out_25(EX_MEM_out_25), .out_26(EX_MEM_out_26), .CLK(CLK));  // open: in_5, in_8, in_11, RegWrite_in, out_21, out_24, out_27, RegWrite_out, 当前传输数据有效_输出, 清零_气泡_高, 使能端
  Adder #(.width(32)) adder_2 (.a(M_PC), .b(32'h4), .out(adder_2_out));  // open: cin, cout
  RAM #(.addrWidth(10), .dataWidth(32), .bus("separate"), .Select("high")) ram_1 (
    .addr(\EX_MEM_alurst输出 [11:2]), .din(MDin), .data(ram_1_data), .str(MemWrite), .clk(CLK));  // open: sel, ld, clr
  Multiplexer #(.select(2), .width(32), .disabled("Z"), .enable("false")) multiplexer_7 (
    .in0(\EX_MEM_alurst输出 ), .in1(ram_1_data), .in2(adder_2_out), .in3(adder_2_out), .out(multiplexer_7_out),
    .sel({1'b0, EX_MEM_out_22[0]}));
  MEM_WB MEM_WB (
    .\IR输入 (MEM_IR), .\PC输入 (M_PC), .\Reg输入 (multiplexer_7_out), .\IR输出 (WB_IR), .\PC输出 (WB_PC),
    .\Reg输出 (RDin), .in_8(EX_MEM_out_25), .in_9(EX_MEM_out_26), .CLK(CLK), .out_23(RegWrite),
    .out_24(reg_dst_back));  // open: Mem输入, Mem输出, in_5, in_6, in_7, in_10, RegWrite_in, 当前传输数据有效_输入, out_20, out_21, out_22, out_25, RegWrite_out, 当前传输数据有效_输出, 清零_气泡_高, 使能端

  // Other names for the same wires on the sheet: ID_IR[5:0] = Func; OP[5:0] = ID_IR[31:26]; MEM_PC[31:0] = M_PC

  // Notes on the sheet:
  //   中断源
  //   时空图监测，可删除
  //   中断等待指示
  //   数码管输出
  //   contents of 指令存储器 (hex, n*v repeats v):
  //   20100000 20110000 20120000 20130000 36100000 36310001 36520002 36730003 ae100000 ae110004 ae120008
  //   ae13000c 2002000a 20110000 20120000 20130000 c
  //   控制位
  //   流水调试日志用
  //   暂停节拍，不能为0
  //   戳工具置1进入计数暂停模式，ctrl+k时钟自动运行到对应节拍暂停
  //   ctrl+k关闭时钟连续运行，将控制位置零，进入单步调试模式调试
  //   用这个时钟源需要去掉电路中的其他时钟源
  //   rt
  //   rs
  //   可计数暂停的时钟源
  //   为方便自动评测，需要输出流水线各段保存的PC值，注意是PC不是PC+4，另外ID段寄存器写入信息，Mem段内存写入信息也要输出
endmodule

module \气泡流水线  (
  output RegWrite,
  output MemWrite,
  output [31:0] IF_PC,
  output [31:0] ID_PC,
  output [31:0] EX_PC,
  output [31:0] M_PC,
  output [31:0] WB_PC,
  output [31:0] RDin,
  output [31:0] MDin,
  output [31:0] LedData
);

  wire alu_src, alu_src_ex, and_1_out, and_2_out, and_3_out, and_6_out, beq, beq_ex, BLEZ_LESS, bne, bne_ex,
       CLK, clock_2_out, comparator_1_eq, comparator_1_lt, comparator_2_eq, comparator_3_eq, comparator_4_eq,
       controlled_buffer_1_out, d_ff_1_q, equal, eret, eret_ex, EX_RegWrite, Exit, Go, IF_stall, IR1, IR2,
       IR3, jal, jal_ex, jal_mem, jmp, jmp_ex_t, jr, jr_ex, MEM_RegWrite, mem_to_reg, mem_to_reg_ex,
       mem_to_reg_mem, mem_write, mem_write_ex, nand_1_out, not_1_out, not_2_out, or_1_out, or_2_out,
       or_3_out, or_4_out, Pause, reg_dst, reg_dst_ex, reg_write, RST, signed_ext, signed_ext_ex, Stop,
       syscall, syscall_ex, W1, W2, W3, \条件分支成功 , \源寄存器使用_1_r1_used , \源寄存器使用_1_r2_used ;
  wire [1:0] pull_resistor_3_node, \流水线关卡_4__1_3_2 , \流水线关卡_4__32_4_2 ;
  wire [3:0] alu_op, alu_op_ex;
  wire [4:0] EX_RegWrite_num, ID_R1_num, ID_R2_num, MEM_RegWrite_num, multiplexer_4_out, multiplexer_5_out,
       WB_RegWrite_num;
  wire [12:0] CNT_num;
  wire [15:0] \LoadUse次数 , \总周期数 , \插入气泡数 , \无条件分支数 , \条件分支成功数 ;
  wire [31:0] adder_1_out, adder_2_out, adder_3_out, adder_4_out, bit_extender_1_out, bit_extender_2_out,
       bit_extender_3_out, EX_IR, ID_IR, IF_IR, JMP_EX, MEM_IR, mips_regfille_falling_1_r1,
       mips_regfille_falling_1_r2, multiplexer_1_out, multiplexer_6_out, multiplexer_7_out,
       multiplexer_9_out, multiplexer_10_out, pull_resistor_2_node, R1_ex, R2_ex, R_mem, ram_1_data, WB_IR,
       \流水线关卡_2__32_6_2 , \流水线关卡_4__32_3_2 ;
  wire [31:1] mips_alu_1_result;
  wire [31:2] \流水线关卡_4__32_4_2_2 ;
  wire [31:8] pull_resistor_4_node, pull_resistor_5_node, pull_resistor_6_node, pull_resistor_7_node;

  Button \u_总复位  (.out(RST));
  Button _1 (.out(IR1));
  Button _2 (.out(IR2));
  Button _3 (.out(IR3));
  // Probe on \总周期数 
  // Probe on \总周期数 
  Button \u_继续运行  (.out(Go));
  LED #(.active("true")) led_1 (.in(W1));
  LED #(.active("true")) led_2 (.in(W2));
  LED #(.active("true")) led_3 (.in(W3));
  Hex_Digit_Display hex_digit_display_1 (.value(LedData[31:28]));  // open: dp
  // Probe on IF_PC[19:0]
  // Mips_Probe mips_probe_1: pin names not known; wires that end beside it: IF_IR
  Hex_Digit_Display hex_digit_display_2 (.value(LedData[27:24]));  // open: dp
  Hex_Digit_Display hex_digit_display_3 (.value(LedData[23:20]));  // open: dp
  // Probe on ID_PC[19:0]
  // Mips_Probe mips_probe_2: pin names not known; wires that end beside it: ID_IR
  not not_1 (not_1_out, IF_stall);
  Multiplexer #(.select(1), .width(32), .disabled("Z"), .enable("false")) multiplexer_1 (
    .in0(adder_1_out), .in1(JMP_EX), .out(multiplexer_1_out), .sel(or_3_out));
  // Probe on multiplexer_1_out
  Hex_Digit_Display hex_digit_display_4 (.value(LedData[19:16]));  // open: dp
  Hex_Digit_Display hex_digit_display_5 (.value(LedData[15:12]));  // open: dp
  // Probe on IF_PC
  Register #(.width(32), .trigger("rising"), .Select("low")) PC (
    .D(multiplexer_1_out), .en(not_1_out), .Q(IF_PC), .clk(CLK), .clr(RST));
  Adder #(.width(32)) adder_1 (.a(IF_PC), .b(32'h4), .out(adder_1_out));  // open: cin, cout
  Hex_Digit_Display hex_digit_display_6 (.value(LedData[11:8]));  // open: dp
  Hex_Digit_Display hex_digit_display_7 (.value(LedData[7:4]));  // open: dp
  Clock #(.highDuration(1), .lowDuration(1)) clock_1 (.out(CLK));
  // Probe on EX_PC[19:0]
  // Mips_Probe mips_probe_3: pin names not known; wires that end beside it: EX_IR
  Hex_Digit_Display hex_digit_display_8 (.value(LedData[3:0]));  // open: dp
  // Probe on \总周期数 
  // Probe on M_PC[19:0]
  // Mips_Probe mips_probe_4: pin names not known; wires that end beside it: MEM_IR
  ROM #(.addrWidth(10), .dataWidth(32), .Select("high")) rom_1 (.addr(IF_PC[11:2]), .data(IF_IR));
  // Probe on \总周期数 
  // Probe on \无条件分支数 
  // Probe on \条件分支成功数 
  // Probe on \插入气泡数 
  // Probe on \LoadUse次数 
  // Probe on IF_PC[11:0]
  // Probe on WB_PC[19:0]
  // Mips_Probe mips_probe_5: pin names not known; wires that end beside it: WB_IR
  \流水线关卡  \u_流水线关卡_1  (
    ._32_1(IF_PC), ._32_2(IF_IR), ._32_1_2(ID_PC), ._32_2_2(ID_IR), .\同步清零 (or_3_out), .CLK(CLK),
    .\使能 (IF_stall));  // open: _1_1, _1_11, _1_2, _1_12, _1_3, _1_13, _1_4, _1_14, _1_5, _1_15, _1_6, _1_16, _1_7, _1_17, _32_3, _1_8, _1_18, _1_9, _1_19, _32_4, _1_10, _1_20, _2_1, _2_2, _32_5, _3_1, _5_1, _3_2, _5_2, _32_6, _4_1, _4_2, _1_1_2, _1_11_2, _1_2_2, _1_12_2, _1_3_2, _1_13_2, _1_4_2, _1_14_2, _1_5_2, _1_15_2, _1_6_2, _1_16_2, _1_7_2, _1_17_2, _32_3_2, _1_8_2, _1_18_2, _1_9_2, _1_19_2, _32_4_2, _1_10_2, _1_20_2, _2_1_2, _2_2_2, _32_5_2, _3_1_2, _5_1_2, _3_2_2, _5_2_2, _32_6_2, _4_1_2, _4_2_2
  // Probe on EX_PC[11:0]
  // Probe on ID_PC[11:0]
  // Probe on M_PC[11:0]
  D_Flip_Flop #(.trigger("high"), .Pre_Clr_Positions("LEGACY"), .NegatePresetClear("false"), .enable("true"), .NewFFLayout("false")) d_ff_1 (.Q(d_ff_1_q));  // open: clk, D, Qn, preset, en, reset
  // Probe on 13'hc
  // Probe on WB_PC[11:0]
  Comparator #(.width(13), .mode("twosComplement")) comparator_1 (
    .a(CNT_num), .b(13'hc), .eq(comparator_1_eq), .lt(comparator_1_lt));  // open: gt
  Clock #(.highDuration(1), .lowDuration(1)) clock_2 (.out(clock_2_out));
  \单周期硬布线控制器  \u_单周期硬布线控制器_1  (
    .Func(ID_IR[5:0]), .OP(ID_IR[31:26]), .ALU_OP(alu_op), .MemToReg(mem_to_reg), .MemWrite(mem_write),
    .ALU_SRC(alu_src), .RegWrite(reg_write), .SysCALL(syscall), .SignedExt(signed_ext), .RegDst(reg_dst),
    .JR(jr), .JMP(jmp), .Beq(beq), .JAL(jal), .Bne(bne), .ERET(eret));
  nand nand_1 (nand_1_out, d_ff_1_q, comparator_1_eq);
  Counter #(.width(13), .max('h1fff), .ongoal("stay"), .trigger("rising"), .behavior("old")) counter_1 (
    .count(comparator_1_lt), .Q(CNT_num), .clk(clock_2_out));  // open: load, D, carry, clr, preset
  Multiplexer #(.select(1), .width(5), .disabled("Z"), .enable("false")) multiplexer_2 (
    .in0(ID_IR[25:21]), .in1(5'b00010), .out(ID_R1_num), .sel(syscall));
  Multiplexer #(.select(1), .width(5), .disabled("Z"), .enable("false")) multiplexer_3 (
    .in0(ID_IR[20:16]), .in1(5'b00100), .out(ID_R2_num), .sel(syscall));
  and and_1 (and_1_out, ~Exit, Go);  // AND_Gate
  assign controlled_buffer_1_out = nand_1_out ? clock_2_out : 1'bz;  // Controlled_Buffer controlled_buffer_1
  or or_1 (or_1_out, Pause, Exit);
  or or_2 (or_2_out, and_1_out, RST);
  Pull_Resistor #(.pull(1)) pull_resistor_1 (.node(controlled_buffer_1_out));
  or or_3 (or_3_out, jmp_ex_t, \条件分支成功 );
  MIPS_Regfille_falling mips_regfille_falling_1 (
    .Din(RDin), .Clk(CLK), .R1(mips_regfille_falling_1_r1), .R2(mips_regfille_falling_1_r2), .WE(RegWrite),
    .W_num(WB_RegWrite_num), .R1_num(ID_R1_num), .R2_num(ID_R2_num));
  \源寄存器使用  \u_源寄存器使用_1  (
    .OP0(ID_IR[26]), .OP1(ID_IR[27]), .OP2(ID_IR[28]), .OP3(ID_IR[29]), .OP4(ID_IR[30]), .OP5(ID_IR[31]),
    .F0(ID_IR[0]), .F1(ID_IR[1]), .F2(ID_IR[2]), .F3(ID_IR[3]), .F4(ID_IR[4]), .F5(ID_IR[5]),
    .R1_Used(\源寄存器使用_1_r1_used ), .R2_Used(\源寄存器使用_1_r2_used ));
  D_Flip_Flop #(.trigger("rising"), .Pre_Clr_Positions("ABOVE_BELOW"), .NegatePresetClear("false"), .enable("false"), .NewFFLayout("true")) d_ff_2 (
    .D(1'b1), .Qn(Stop), .reset(or_2_out));  // open: clk, Q, preset
  or or_4 (or_4_out, jmp_ex_t, IF_stall, \条件分支成功 );
  Multiplexer #(.select(1), .width(5), .disabled("Z"), .enable("false")) multiplexer_4 (
    .in0(ID_IR[20:16]), .in1(ID_IR[15:11]), .out(multiplexer_4_out), .sel(reg_dst));
  assign bit_extender_1_out = {{16{1'b0}}, ID_IR[15:0]};  // Bit_Extender bit_extender_1
  assign bit_extender_2_out = {{16{ID_IR[15]}}, ID_IR[15:0]};  // Bit_Extender bit_extender_2
  \数据相关检测  \u_数据相关检测_1  (
    .R1_Used(\源寄存器使用_1_r1_used ), .R2_Used(\源寄存器使用_1_r2_used ), .EX_WriteReg_num(EX_RegWrite_num),
    .MEM_WriteReg_num(MEM_RegWrite_num), .WB_WriteReg_num(WB_RegWrite_num), .R1_num(ID_R1_num),
    .R2_num(ID_R2_num), .EX_RegWrite(EX_RegWrite), .MEM_RegWrite(MEM_RegWrite), .\数据相关 (IF_stall),
    .WB_RegWrite(RegWrite));
  Multiplexer #(.select(1), .width(5), .disabled("Z"), .enable("false")) multiplexer_5 (
    .in0(multiplexer_4_out), .in1({5{1'b1}}), .out(multiplexer_5_out), .sel(jal));
  Multiplexer #(.select(1), .width(32), .disabled("Z"), .enable("false")) multiplexer_6 (
    .in0(bit_extender_1_out), .in1(bit_extender_2_out), .out(multiplexer_6_out), .sel(signed_ext));
  Counter #(.width(16), .max('hffff), .ongoal("wrap"), .trigger("rising"), .behavior("new")) counter_2 (
    .count(IF_stall), .Q(\插入气泡数 ), .clk(CLK), .clr(RST));  // open: load, D, carry, preset, down
  or or_5 (\条件分支成功 , and_2_out, and_3_out);
  and and_2 (and_2_out, beq_ex, equal);
  not not_2 (not_2_out, equal);
  Counter #(.width(16), .max('hffff), .ongoal("wrap"), .trigger("rising"), .behavior("new")) counter_3 (
    .count(Stop), .Q(\总周期数 ), .clk(CLK), .clr(RST));  // open: load, D, carry, preset, down
  and and_3 (and_3_out, bne_ex, not_2_out);
  \流水线关卡  \u_流水线关卡_2  (
    ._32_1(ID_PC), ._1_2(beq), ._1_12(bne), ._1_3(mem_to_reg), ._1_13(mem_write), ._1_4(alu_src),
    ._1_14(reg_write), ._32_2(ID_IR), ._1_5(jal), ._1_15(eret), ._1_6(reg_dst), ._1_16(syscall), ._1_7(jmp),
    ._1_17(jr), ._1_8(signed_ext), ._32_4(mips_regfille_falling_1_r1), ._32_5(mips_regfille_falling_1_r2),
    ._5_1(multiplexer_5_out), ._32_6(multiplexer_6_out), ._4_1(alu_op), ._32_1_2(EX_PC), ._1_2_2(beq_ex),
    ._1_12_2(bne_ex), ._1_3_2(mem_to_reg_ex), ._1_13_2(mem_write_ex), ._1_4_2(alu_src_ex),
    ._1_14_2(EX_RegWrite), ._32_2_2(EX_IR), ._1_5_2(jal_ex), ._1_15_2(eret_ex), ._1_6_2(reg_dst_ex),
    ._1_16_2(syscall_ex), ._1_7_2(jmp_ex_t), ._1_17_2(jr_ex), ._1_8_2(signed_ext_ex), ._32_4_2(R1_ex),
    ._32_5_2(R2_ex), ._5_1_2(EX_RegWrite_num), ._32_6_2(\流水线关卡_2__32_6_2 ), ._4_1_2(alu_op_ex),
    .\同步清零 (or_4_out), .CLK(CLK), .\使能 (1'b0));  // open: _1_1, _1_11, _32_3, _1_18, _1_9, _1_19, _1_10, _1_20, _2_1, _2_2, _3_1, _3_2, _5_2, _4_2, _1_1_2, _1_11_2, _32_3_2, _1_18_2, _1_9_2, _1_19_2, _1_10_2, _1_20_2, _2_1_2, _2_2_2, _3_1_2, _3_2_2, _5_2_2, _4_2_2
  Counter #(.width(16), .max('hffff), .ongoal("wrap"), .trigger("rising"), .behavior("new")) \u_条件分支数  (
    .count(\条件分支成功 ), .Q(\条件分支成功数 ), .clk(CLK), .clr(RST));  // open: load, D, carry, preset, down
  Multiplexer #(.select(1), .width(32), .disabled("Z"), .enable("false")) multiplexer_7 (
    .in0(R2_ex), .in1(\流水线关卡_2__32_6_2 ), .out(multiplexer_7_out), .sel(alu_src_ex));
  Counter #(.width(16), .max('hffff), .ongoal("wrap"), .trigger("rising"), .behavior("new")) \u_无条件分支数  (
    .count(jmp_ex_t), .Q(\无条件分支数 ), .clk(CLK), .clr(RST));  // open: load, D, carry, preset, down
  Comparator #(.width(32), .mode("twosComplement")) comparator_2 (
    .a(R1_ex), .b(32'h32), .eq(comparator_2_eq));  // open: gt, lt
  Comparator #(.width(32), .mode("twosComplement")) comparator_3 (
    .a(R1_ex), .b(32'ha), .eq(comparator_3_eq));  // open: gt, lt
  Comparator #(.width(32), .mode("twosComplement")) comparator_4 (
    .a(R1_ex), .b(32'h22), .eq(comparator_4_eq));  // open: gt, lt
  and and_4 (Pause, comparator_2_eq, syscall_ex);
  and and_5 (Exit, comparator_3_eq, syscall_ex);
  and and_6 (and_6_out, comparator_4_eq, syscall_ex);
  Pull_Resistor #(.pull(0)) pull_resistor_2 (.node({pull_resistor_2_node[31:28], EX_IR[25:0], pull_resistor_2_node[1:0]}));
  Pull_Resistor #(.pull(0)) pull_resistor_3 (.node({EX_IR[15:0], pull_resistor_3_node}));
  assign bit_extender_3_out = {{14{EX_IR[15]}}, {EX_IR[15:0], pull_resistor_3_node}};  // Bit_Extender bit_extender_3
  Adder #(.width(32)) adder_2 (.a(32'h4), .b(EX_PC), .out(adder_2_out));  // open: cin, cout
  MIPS_ALU mips_alu_1 (
    .X(R1_ex), .Y(multiplexer_7_out), .AluOP(alu_op_ex), .Equal(equal),
    .Result({mips_alu_1_result, BLEZ_LESS}), .shamt(EX_IR[10:6]));  // open: Result_2
  Register #(.width(32), .trigger("rising"), .Select("low")) register_1 (
    .D(R2_ex), .en(and_6_out), .Q(LedData), .clk(CLK));  // open: clr
  Adder #(.width(32)) adder_3 (.a(bit_extender_3_out), .b(adder_2_out), .out(adder_3_out));  // open: cin, cout
  Multiplexer #(.select(2), .width(32), .disabled("Z"), .enable("false")) multiplexer_8 (
    .in0({pull_resistor_2_node[31:28], EX_IR[25:0], pull_resistor_2_node[1:0]}), .in1(adder_3_out),
    .in2(R1_ex), .in3(adder_3_out), .out(JMP_EX), .sel({jr_ex, \条件分支成功 }));
  \流水线关卡  \u_流水线关卡_3  (
    ._32_1(EX_PC), ._1_3(mem_to_reg_ex), ._1_13(mem_write_ex), ._1_14(EX_RegWrite), ._32_2(EX_IR),
    ._1_5(jal_ex), ._32_3({mips_alu_1_result, BLEZ_LESS}), ._32_4(R2_ex), ._5_1(EX_RegWrite_num),
    ._32_1_2(M_PC), ._1_3_2(mem_to_reg_mem), ._1_13_2(MemWrite), ._1_14_2(MEM_RegWrite), ._32_2_2(MEM_IR),
    ._1_5_2(jal_mem), ._32_3_2(R_mem), ._32_4_2(MDin), ._5_1_2(MEM_RegWrite_num), .CLK(CLK), .\使能 (1'b0));  // open: _1_1, _1_11, _1_2, _1_12, _1_4, _1_15, _1_6, _1_16, _1_7, _1_17, _1_8, _1_18, _1_9, _1_19, _1_10, _1_20, _2_1, _2_2, _32_5, _3_1, _3_2, _5_2, _32_6, _4_1, _4_2, _1_1_2, _1_11_2, _1_2_2, _1_12_2, _1_4_2, _1_15_2, _1_6_2, _1_16_2, _1_7_2, _1_17_2, _1_8_2, _1_18_2, _1_9_2, _1_19_2, _1_10_2, _1_20_2, _2_1_2, _2_2_2, _32_5_2, _3_1_2, _3_2_2, _5_2_2, _32_6_2, _4_1_2, _4_2_2, 同步清零
  RAM #(.addrWidth(10), .dataWidth(32), .bus("separate"), .Select("high")) ram_1 (
    .addr(R_mem[11:2]), .din(MDin), .data(ram_1_data), .str(MemWrite), .clk(CLK));  // open: sel, ld, clr
  \流水线关卡  \u_流水线关卡_4  (
    ._32_1(M_PC), ._1_3(mem_to_reg_mem), ._1_14(MEM_RegWrite), ._32_2(MEM_IR), ._1_5(jal_mem),
    ._32_3(ram_1_data), ._32_4(R_mem), ._5_1(MEM_RegWrite_num), ._32_1_2(WB_PC),
    ._1_3_2(\流水线关卡_4__1_3_2 [0]), ._1_14_2(RegWrite), ._32_2_2(WB_IR), ._1_5_2(\流水线关卡_4__1_3_2 [1]),
    ._32_3_2(\流水线关卡_4__32_3_2 ), ._32_4_2({\流水线关卡_4__32_4_2_2 , \流水线关卡_4__32_4_2 }),
    ._5_1_2(WB_RegWrite_num), .CLK(CLK), .\使能 (1'b0));  // open: _1_1, _1_11, _1_2, _1_12, _1_13, _1_4, _1_15, _1_6, _1_16, _1_7, _1_17, _1_8, _1_18, _1_9, _1_19, _1_10, _1_20, _2_1, _2_2, _32_5, _3_1, _3_2, _5_2, _32_6, _4_1, _4_2, _1_1_2, _1_11_2, _1_2_2, _1_12_2, _1_13_2, _1_4_2, _1_15_2, _1_6_2, _1_16_2, _1_7_2, _1_17_2, _1_8_2, _1_18_2, _1_9_2, _1_19_2, _1_10_2, _1_20_2, _2_1_2, _2_2_2, _32_5_2, _3_1_2, _3_2_2, _5_2_2, _32_6_2, _4_1_2, _4_2_2, 同步清零
  Pull_Resistor #(.pull(0)) pull_resistor_4 (.node({pull_resistor_4_node, \流水线关卡_4__32_3_2 [31:24]}));
  Pull_Resistor #(.pull(0)) pull_resistor_5 (.node({pull_resistor_5_node, \流水线关卡_4__32_3_2 [15:8]}));
  Pull_Resistor #(.pull(0)) pull_resistor_6 (.node({pull_resistor_6_node, \流水线关卡_4__32_3_2 [23:16]}));
  Pull_Resistor #(.pull(0)) pull_resistor_7 (.node({pull_resistor_7_node, \流水线关卡_4__32_3_2 [7:0]}));
  Adder #(.width(32)) adder_4 (.a(WB_PC), .b(32'h4), .out(adder_4_out));  // open: cin, cout
  Multiplexer #(.select(2), .width(32), .disabled("Z"), .enable("false")) multiplexer_9 (
    .in0({pull_resistor_7_node, \流水线关卡_4__32_3_2 [7:0]}),
    .in1({pull_resistor_5_node, \流水线关卡_4__32_3_2 [15:8]}),
    .in2({pull_resistor_6_node, \流水线关卡_4__32_3_2 [23:16]}),
    .in3({pull_resistor_4_node, \流水线关卡_4__32_3_2 [31:24]}), .out(multiplexer_9_out), .sel(\流水线关卡_4__32_4_2 ));
  Multiplexer #(.select(1), .width(32), .disabled("Z"), .enable("false")) multiplexer_10 (
    .in0(\流水线关卡_4__32_3_2 ), .in1(multiplexer_9_out), .out(multiplexer_10_out), .sel(1'b0));
  Multiplexer #(.select(2), .width(32), .disabled("Z"), .enable("false")) multiplexer_11 (
    .in0({\流水线关卡_4__32_4_2_2 , \流水线关卡_4__32_4_2 }), .in1(multiplexer_10_out), .in2(adder_4_out),
    .in3(adder_4_out), .out(RDin), .sel(\流水线关卡_4__1_3_2 ));

  // Other names for the same wires on the sheet: MEM_PC[31:0] = M_PC; mem_write_mem = MemWrite; R2_mem[31:0] = MDin;
  //   reg_write_ex = EX_RegWrite; WB_RegWrite = RegWrite

  // Notes on the sheet:
  //   中断源
  //   时空图监测，可删除
  //   中断等待指示
  //   数码管输出
  //   contents of rom_1 (hex, n*v repeats v):
  //   20110001 8000c05 20110001 20120002 20130003 8000c09 20110001 20120002 20130003 8000c0d 20110001
  //   20120002 20130003 8000c11 20110001 20120002 20130003 c000cb8 20100001 20110001 118fc0 112020
  //   20020022 c 118882 12200001 8000c15 112020 20020022 c 20110001 118880 112020 20020022 c 12200001
  //   8000c1f 20110001 118fc0 112020 20020022 c 1188c3 112020 20020022 c 118903 112020 20020022 c 118903
  //   112020 20020022 c 118903 112020 20020022 c 118903 112020 20020022 c 118903 112020 20020022 c 118903
  //   112020 20020022 c 118903 112020 20020022 c 20100001 109fc0 139fc3 8021 2012000c 24160003 26100001
  //   3210000f 20080008 20090001 139900 2709825 132020 20020022 c 1094022 1500fff9 22100001 2018000f
  //   2188024 108700 20080008 20090001 139902 2709825 132021 20020022 c 1094022 1500fff9 108702 2c9b022
  //   12c00001 8000c50 4020 1084027 84400 3508ffff 82021 20020022 c 2010ffff 20110000 ae300000 22100001
  //   22310004 ae300000 22100001 22310004 ae300000 22100001 22310004 ae300000 22100001 22310004 ae300000
  //   22100001 22310004 ae300000 22100001 22310004 ae300000 22100001 22310004 ae300000 22100001 22310004
  //   ae300000 22100001 22310004 ae300000 22100001 22310004 ae300000 22100001 22310004 ae300000 22100001
  //   22310004 ae300000 22100001 22310004 ae300000 22100001 22310004 ae300000 22100001 22310004 ae300000
  //   22100001 22310004 22100001 8020 2011003c 8e130000 8e340000 274402a 11000002 ae330000 ae140000
  //   2231fffc 1611fff8 102020 20020022 c 22100004 2011003c 1611fff2 20020032 c 20100000 22100001 102020
  //   20020022 c 22100002 102020 20020022 c 22100003 102020 20020022 c 22100004 102020 20020022 c 22100005
  //   102020 20020022 c 22100006 102020 20020022 c 22100007 102020 20020022 c 22100008 102020 20020022
  //   20020022 c 3e00008
  //   控制位
  //   流水调试日志用
  //   暂停节拍，不能为0
  //   OP
  //   FUNC
  //   rs
  //   rt
  //   rd
  //   戳工具置1进入计数暂停模式，ctrl+k时钟自动运行到对应节拍暂停
  //   ctrl+k关闭时钟连续运行，将控制位置零，进入单步调试模式调试
  //   可计数暂停的时钟源
  //   OP
  //   FUNC
  //   rd
  //   为方便自动评测，需要输出流水线各段保存的PC值，注意是PC不是PC+4，另外ID段寄存器写入信息，Mem段内存写入信息也要输出
endmodule

module \重定向流水线  (
  output RegWrite,
  output MemWrite,
  output [31:0] IF_PC,
  output [31:0] ID_PC,
  output [31:0] EX_PC,
  output [31:0] M_PC,
  output [31:0] WB_PC,
  output [31:0] RDin,
  output [31:0] MDin,
  output [31:0] LedData
);

  wire alu_src, alu_src_ex, and_1_out, and_2_out, and_3_out, and_4_out, beq, beq_ex, bne, bne_ex, CLK,
       clock_1_out, clock_2_out, comparator_1_eq, comparator_1_lt, comparator_2_eq, d_ff_1_q, equal, eret,
       eret_ex, EX_RegWrite, Go, if_stall, IR1, IR2, IR3, jal, jal_ex, jal_mem, jal_mem_t, JMP, jmp_t, jr,
       jr_ex, MEM_RegWrite, MEM_RegWrite_t, mem_to_reg, mem_to_reg_ex, mem_to_reg_mem, mem_to_reg_mem_t,
       mem_write, mem_write_ex, mem_write_mem_t, nand_1_out, not_1_out, not_2_out, not_3_out, or_2_out,
       or_3_out, ppn_in_tlb_0, ppn_in_tlb_0__1, \R_权限 , reg_dst, reg_dst_ex, reg_write, RST, signed_ext,
       signed_ext_ex, syscall, syscall_ex, tlb_miss, tlb_miss_wb, \U_权限 , W1, W2, W3, \W_权限 , \X_权限 ,
       \条件分支成功 , \流水线关卡_5__1_12_2 , \流水线关卡_6__1_6_2 , \流水线关卡_6__1_7_2 , \流水线关卡_6__1_12_2 , \流水线关卡_6__1_13_2 ,
       \源寄存器使用_1_r1_used , \源寄存器使用_1_r2_used , \页表模式 ;
  wire [1:0] forward1, forward2, \流水线关卡_2__2_1_2 , \流水线关卡_2__2_2_2 , \流水线关卡_4__1_3_2 ;
  wire [2:0] ppn_1__in_mem, ppn_2__in_mem, vpn_1, vpn_1__1, vpn_2, vpn_2__1, \地址空间参数 ;
  wire [3:0] alu_op, alu_op_ex, offset, offset_1, offset_wb;
  wire [4:0] EX_RegWrite_num, ID_R1_num, ID_R2_num, MEM_RegWrite__t, MEM_RegWrite_num, multiplexer_4_out,
       multiplexer_5_out, ppn_in_tlb_1__5, ppn_in_tlb_1__5__1, WB_RegWrite_num, \流水线关卡_6__5_1_2 ;
  wire [5:0] ppn_in_mem, ppn_in_tlb, \根页表ppn , \解析pte_1_ppn ;
  wire [8:0] \虚拟地址 ;
  wire [9:0] adder_5_out, adder_6_out, bit_extender_5_out, bit_extender_6_out, bit_extender_7_out,
       bit_extender_8_out;
  wire [9:4] pa;
  wire [12:0] CNT_num;
  wire [15:0] \LoadUse次数 , multiplexer_12_out, \总周期数 , \插入气泡数 , \无条件分支数 , \条件分支成功数 ;
  wire [31:0] adder_1_out, adder_2_out, adder_3_out, adder_4_out, bit_extender_1_out, bit_extender_2_out,
       bit_extender_3_out, bit_extender_4_out, EX_IR, ID_IR, IF_IR, JumpAddr, MDin_t, MEM_IR, MEM_IR_t,
       MEM_PC_t, mips_alu_1_result, mips_regfille_falling_1_r1, mips_regfille_falling_1_r2,
       multiplexer_1_out, multiplexer_6_out, multiplexer_7_out, multiplexer_9_out, multiplexer_11_out, R,
       R1_ex, R2_ex, R_mem, R_mem_t, ram_1_data, satp_q, WB_IR, \一级pte , \二级pte , \流水线关卡_2__32_6_2 ,
       \流水线关卡_4__32_3_2 , \流水线关卡_4__32_4_2 , \流水线关卡_6__32_1_2 , \流水线关卡_6__32_2_2 , \流水线关卡_6__32_4_2 ,
       \流水线关卡_6__32_6_2 ;

  Button \u_总复位  (.out(RST));
  Button _1 (.out(IR1));
  Button _2 (.out(IR2));
  Button _3 (.out(IR3));
  // Probe on \总周期数 
  // Probe on \总周期数 
  Button \u_继续运行  (.out(Go));
  LED #(.active("true")) led_1 (.in(W1));
  LED #(.active("true")) led_2 (.in(W2));
  LED #(.active("true")) led_3 (.in(W3));
  Multiplexer #(.select(1), .width(32), .disabled("Z"), .enable("false")) multiplexer_1 (
    .in0(adder_1_out), .in1(JumpAddr), .out(multiplexer_1_out), .sel(or_2_out));
  Hex_Digit_Display hex_digit_display_1 (.value(LedData[31:28]));  // open: dp
  // Probe on IF_PC[19:0]
  // Mips_Probe mips_probe_1: pin names not known; wires that end beside it: IF_IR
  // Probe on multiplexer_1_out
  not not_1 (not_1_out, if_stall);
  Hex_Digit_Display hex_digit_display_2 (.value(LedData[23:20]));  // open: dp
  Hex_Digit_Display hex_digit_display_3 (.value(LedData[27:24]));  // open: dp
  // Probe on ID_PC[19:0]
  // Mips_Probe mips_probe_2: pin names not known; wires that end beside it: ID_IR
  // Probe on IF_PC
  Register #(.width(32), .trigger("rising"), .Select("low")) PC (
    .D(multiplexer_1_out), .en(not_1_out), .Q(IF_PC), .clk(CLK), .clr(RST));
  Hex_Digit_Display hex_digit_display_4 (.value(LedData[19:16]));  // open: dp
  Hex_Digit_Display hex_digit_display_5 (.value(LedData[15:12]));  // open: dp
  // Probe on IF_PC
  Adder #(.width(32)) adder_1 (.a(IF_PC), .b(32'h4), .out(adder_1_out));  // open: cin, cout
  Hex_Digit_Display hex_digit_display_6 (.value(LedData[11:8]));  // open: dp
  Hex_Digit_Display hex_digit_display_7 (.value(LedData[7:4]));  // open: dp
  Clock #(.highDuration(1), .lowDuration(1)) clock_1 (.out(clock_1_out));
  // Probe on EX_PC[19:0]
  // Mips_Probe mips_probe_3: pin names not known; wires that end beside it: clock_1_out, EX_IR, CLK
  // Probe on adder_1_out
  Hex_Digit_Display hex_digit_display_8 (.value(LedData[3:0]));  // open: dp
  // Probe on \总周期数 
  // Probe on M_PC[19:0]
  // Mips_Probe mips_probe_4: pin names not known; wires that end beside it: MEM_IR
  ROM #(.addrWidth(10), .dataWidth(32), .Select("high")) \u_指令存储器  (.addr(IF_PC[11:2]), .data(IF_IR));
  // Probe on \总周期数 
  // Probe on \无条件分支数 
  // Probe on \条件分支成功数 
  // Probe on \插入气泡数 
  // Probe on \LoadUse次数 
  // Probe on IF_PC[11:0]
  // Probe on WB_PC[19:0]
  // Mips_Probe mips_probe_5: pin names not known; wires that end beside it: WB_IR
  \流水线关卡  \u_流水线关卡_1  (
    ._32_1(IF_PC), ._32_2(IF_IR), ._32_1_2(ID_PC), ._32_2_2(ID_IR), .\同步清零 (or_2_out), .CLK(CLK),
    .\使能 (if_stall));  // open: _1_1, _1_11, _1_2, _1_12, _1_3, _1_13, _1_4, _1_14, _1_5, _1_15, _1_6, _1_16, _1_7, _1_17, _32_3, _1_8, _1_18, _1_9, _1_19, _32_4, _1_10, _1_20, _2_1, _2_2, _32_5, _3_1, _5_1, _3_2, _5_2, _32_6, _4_1, _4_2, _1_1_2, _1_11_2, _1_2_2, _1_12_2, _1_3_2, _1_13_2, _1_4_2, _1_14_2, _1_5_2, _1_15_2, _1_6_2, _1_16_2, _1_7_2, _1_17_2, _32_3_2, _1_8_2, _1_18_2, _1_9_2, _1_19_2, _32_4_2, _1_10_2, _1_20_2, _2_1_2, _2_2_2, _32_5_2, _3_1_2, _5_1_2, _3_2_2, _5_2_2, _32_6_2, _4_1_2, _4_2_2
  // Probe on EX_PC[11:0]
  // Probe on ID_PC[11:0]
  // Probe on M_PC[11:0]
  D_Flip_Flop #(.trigger("high"), .Pre_Clr_Positions("LEGACY"), .NegatePresetClear("false"), .enable("true"), .NewFFLayout("false")) d_ff_1 (.Q(d_ff_1_q));  // open: clk, D, Qn, preset, en, reset
  // Probe on 13'hc
  // Probe on WB_PC[11:0]
  Comparator #(.width(13), .mode("twosComplement")) comparator_1 (
    .a(CNT_num), .b(13'hc), .eq(comparator_1_eq), .lt(comparator_1_lt));  // open: gt
  Clock #(.highDuration(1), .lowDuration(1)) clock_2 (.out(clock_2_out));
  \单周期硬布线控制器  \u_单周期硬布线控制器_1  (
    .Func(ID_IR[5:0]), .OP(ID_IR[31:26]), .ALU_OP(alu_op), .MemToReg(mem_to_reg), .MemWrite(mem_write),
    .ALU_SRC(alu_src), .RegWrite(reg_write), .SysCALL(syscall), .SignedExt(signed_ext), .RegDst(reg_dst),
    .JR(jr), .JMP(jmp_t), .Beq(beq), .JAL(jal), .Bne(bne), .ERET(eret));
  \源寄存器使用  \u_源寄存器使用_1  (
    .OP0(ID_IR[26]), .OP1(ID_IR[27]), .OP2(ID_IR[28]), .OP3(ID_IR[29]), .OP4(ID_IR[30]), .OP5(ID_IR[31]),
    .F0(ID_IR[0]), .F1(ID_IR[1]), .F2(ID_IR[2]), .F3(ID_IR[3]), .F4(ID_IR[4]), .F5(ID_IR[5]),
    .R1_Used(\源寄存器使用_1_r1_used ), .R2_Used(\源寄存器使用_1_r2_used ));
  nand nand_1 (nand_1_out, d_ff_1_q, comparator_1_eq);
  Counter #(.width(13), .max('h1fff), .ongoal("stay"), .trigger("rising"), .behavior("old")) counter_1 (
    .count(comparator_1_lt), .Q(CNT_num), .clk(clock_2_out));  // open: load, D, carry, clr, preset
  Multiplexer #(.select(1), .width(5), .disabled("Z"), .enable("false")) multiplexer_2 (
    .in0(ID_IR[25:21]), .in1(5'b00010), .out(ID_R1_num), .sel(syscall));
  Multiplexer #(.select(1), .width(5), .disabled("Z"), .enable("false")) multiplexer_3 (
    .in0(ID_IR[20:16]), .in1(5'b00100), .out(ID_R2_num), .sel(syscall));
  \访存相关  \u_访存相关_1  (
    .R1_num(ID_R1_num), .R1(\源寄存器使用_1_r1_used ), .R2_num(ID_R2_num), .R2(\源寄存器使用_1_r2_used ),
    .EXRegWrite_num(EX_RegWrite_num), .EXRegWrite(mem_to_reg_ex), .\访存相关 (if_stall));
  assign CLK = nand_1_out ? clock_2_out : 1'bz;  // Controlled_Buffer controlled_buffer_1
  Pull_Resistor #(.pull(1)) pull_resistor_1 (.node(CLK));
  MIPS_Regfille_falling mips_regfille_falling_1 (
    .Din(RDin), .Clk(CLK), .R1(mips_regfille_falling_1_r1), .R2(mips_regfille_falling_1_r2), .WE(RegWrite),
    .W_num(WB_RegWrite_num), .R1_num(ID_R1_num), .R2_num(ID_R2_num));
  Counter #(.width(16), .max('hffff), .ongoal("wrap"), .trigger("rising"), .behavior("new")) counter_2 (
    .count(if_stall), .Q(\LoadUse次数 ), .clk(CLK), .clr(RST));  // open: load, D, carry, preset, down
  and and_1 (and_1_out, beq_ex, equal);
  Multiplexer #(.select(1), .width(5), .disabled("Z"), .enable("false")) multiplexer_4 (
    .in0(ID_IR[20:16]), .in1(ID_IR[15:11]), .out(multiplexer_4_out), .sel(reg_dst));
  assign bit_extender_1_out = {{16{1'b0}}, ID_IR[15:0]};  // Bit_Extender bit_extender_1
  assign bit_extender_2_out = {{16{ID_IR[15]}}, ID_IR[15:0]};  // Bit_Extender bit_extender_2
  Forward forward_1 (
    .R1_num(ID_R1_num), .R1(\源寄存器使用_1_r1_used ), .R2_num(ID_R2_num), .R2(\源寄存器使用_1_r2_used ),
    .ExRegWrite_num(EX_RegWrite_num), .ExRegWrite(EX_RegWrite), .MemRegWrite_num(MEM_RegWrite_num),
    .MemRegWrite(MEM_RegWrite), .Forward1(forward1), .Forward2(forward2));
  or or_1 (\条件分支成功 , and_1_out, and_2_out);
  and and_2 (and_2_out, bne_ex, not_2_out);
  not not_2 (not_2_out, equal);
  Multiplexer #(.select(1), .width(5), .disabled("Z"), .enable("false")) multiplexer_5 (
    .in0(multiplexer_4_out), .in1({5{1'b1}}), .out(multiplexer_5_out), .sel(jal));
  Multiplexer #(.select(1), .width(32), .disabled("Z"), .enable("false")) multiplexer_6 (
    .in0(bit_extender_1_out), .in1(bit_extender_2_out), .out(multiplexer_6_out), .sel(signed_ext));
  or or_2 (or_2_out, JMP, \条件分支成功 );
  or or_3 (or_3_out, or_2_out, if_stall);
  \流水线关卡  \u_流水线关卡_2  (
    ._32_1(ID_PC), ._1_2(beq), ._1_12(bne), ._1_3(mem_to_reg), ._1_13(mem_write), ._1_4(alu_src),
    ._1_14(reg_write), ._32_2(ID_IR), ._1_5(jal), ._1_15(eret), ._1_6(reg_dst), ._1_16(syscall),
    ._1_7(jmp_t), ._1_17(jr), ._1_8(signed_ext), ._32_4(mips_regfille_falling_1_r1), ._2_1(forward1),
    ._2_2(forward2), ._32_5(mips_regfille_falling_1_r2), ._5_1(multiplexer_5_out), ._32_6(multiplexer_6_out),
    ._4_1(alu_op), ._32_1_2(EX_PC), ._1_2_2(beq_ex), ._1_12_2(bne_ex), ._1_3_2(mem_to_reg_ex),
    ._1_13_2(mem_write_ex), ._1_4_2(alu_src_ex), ._1_14_2(EX_RegWrite), ._32_2_2(EX_IR), ._1_5_2(jal_ex),
    ._1_15_2(eret_ex), ._1_6_2(reg_dst_ex), ._1_16_2(syscall_ex), ._1_7_2(JMP), ._1_17_2(jr_ex),
    ._1_8_2(signed_ext_ex), ._32_4_2(R1_ex), ._2_1_2(\流水线关卡_2__2_1_2 ), ._2_2_2(\流水线关卡_2__2_2_2 ),
    ._32_5_2(R2_ex), ._5_1_2(EX_RegWrite_num), ._32_6_2(\流水线关卡_2__32_6_2 ), ._4_1_2(alu_op_ex),
    .\同步清零 (or_3_out), .CLK(CLK), .\使能 (1'b0));  // open: _1_1, _1_11, _32_3, _1_18, _1_9, _1_19, _1_10, _1_20, _3_1, _3_2, _5_2, _4_2, _1_1_2, _1_11_2, _32_3_2, _1_18_2, _1_9_2, _1_19_2, _1_10_2, _1_20_2, _3_1_2, _3_2_2, _5_2_2, _4_2_2
  Multiplexer #(.select(2), .width(32), .disabled("Z"), .enable("false")) multiplexer_7 (
    .in0(R2_ex), .in1(RDin), .in2(R_mem), .out(multiplexer_7_out), .sel(\流水线关卡_2__2_2_2 ));  // open: in3
  Multiplexer #(.select(2), .width(32), .disabled("Z"), .enable("false")) multiplexer_8 (
    .in0(R1_ex), .in1(RDin), .in2(R_mem), .out(R), .sel(\流水线关卡_2__2_1_2 ));  // open: in3
  Multiplexer #(.select(1), .width(32), .disabled("Z"), .enable("false")) multiplexer_9 (
    .in0(multiplexer_7_out), .in1(\流水线关卡_2__32_6_2 ), .out(multiplexer_9_out), .sel(alu_src_ex));
  assign bit_extender_3_out = {{14{EX_IR[15]}}, {EX_IR[15:0], 2'b00}};  // Bit_Extender bit_extender_3
  Adder #(.width(32)) adder_2 (.a(EX_PC), .b(32'h4), .out(adder_2_out));  // open: cin, cout
  Adder #(.width(32)) adder_3 (.a(bit_extender_3_out), .b(adder_2_out), .out(adder_3_out));  // open: cin, cout
  MIPS_ALU mips_alu_1 (
    .X(R), .Y(multiplexer_9_out), .AluOP(alu_op_ex), .Equal(equal), .Result(mips_alu_1_result),
    .shamt(EX_IR[10:6]));  // open: Result_2
  Comparator #(.width(32), .mode("twosComplement")) comparator_2 (
    .a(R), .b(32'h22), .eq(comparator_2_eq));  // open: gt, lt
  Multiplexer #(.select(2), .width(32), .disabled("Z"), .enable("false")) multiplexer_10 (
    .in0({4'b0000, EX_IR[25:0], 2'b00}), .in1(adder_3_out), .in2(R), .in3(adder_3_out), .out(JumpAddr),
    .sel({jr_ex, \条件分支成功 }));
  and and_3 (and_3_out, comparator_2_eq, ~syscall_ex);  // AND_Gate
  not not_3 (not_3_out, and_3_out);
  and and_4 (and_4_out, comparator_2_eq, syscall_ex);
  \流水线关卡  \u_流水线关卡_3  (
    ._32_1(EX_PC), ._1_3(mem_to_reg_ex), ._1_13(mem_write_ex), ._1_14(EX_RegWrite), ._32_2(EX_IR),
    ._1_5(jal_ex), ._32_3(mips_alu_1_result), ._32_4(multiplexer_7_out), ._5_1(EX_RegWrite_num),
    ._32_1_2(MEM_PC_t), ._1_3_2(mem_to_reg_mem_t), ._1_13_2(mem_write_mem_t), ._1_14_2(MEM_RegWrite_t),
    ._32_2_2(MEM_IR_t), ._1_5_2(jal_mem_t), ._32_3_2(R_mem_t), ._32_4_2(MDin_t), ._5_1_2(MEM_RegWrite__t),
    .CLK(CLK), .\使能 (1'b0));  // open: _1_1, _1_11, _1_2, _1_12, _1_4, _1_15, _1_6, _1_16, _1_7, _1_17, _1_8, _1_18, _1_9, _1_19, _1_10, _1_20, _2_1, _2_2, _32_5, _3_1, _3_2, _5_2, _32_6, _4_1, _4_2, _1_1_2, _1_11_2, _1_2_2, _1_12_2, _1_4_2, _1_15_2, _1_6_2, _1_16_2, _1_7_2, _1_17_2, _1_8_2, _1_18_2, _1_9_2, _1_19_2, _1_10_2, _1_20_2, _2_1_2, _2_2_2, _32_5_2, _3_1_2, _3_2_2, _5_2_2, _32_6_2, _4_1_2, _4_2_2, 同步清零
  Counter #(.width(16), .max('hffff), .ongoal("wrap"), .trigger("rising"), .behavior("old")) counter_3 (
    .count(not_3_out), .Q(\总周期数 ), .clk(CLK));  // open: load, D, carry, clr, preset
  Register #(.width(32), .trigger("rising"), .Select("low")) register_1 (
    .D(multiplexer_7_out), .en(and_4_out), .Q(LedData), .clk(CLK));  // open: clr
  // Probe on R_mem_t
  Counter #(.width(16), .max('hffff), .ongoal("wrap"), .trigger("rising"), .behavior("new")) counter_4 (
    .count(JMP), .Q(\无条件分支数 ), .clk(CLK), .clr(RST));  // open: load, D, carry, preset, down
  // Probe on vpn_1
  // Probe on vpn_2
  // Probe on offset
  \虚拟地址解析  \u_解析虚拟地址  (.VA(R_mem_t[9:0]), .offset(offset), .vpn_2(vpn_2), .vpn_1(vpn_1));
  Counter #(.width(16), .max('hffff), .ongoal("wrap"), .trigger("rising"), .behavior("new")) counter_5 (
    .count(\条件分支成功 ), .Q(\条件分支成功数 ), .clk(CLK), .clr(RST));  // open: load, D, carry, preset, down
  RAM #(.addrWidth(10), .dataWidth(32), .bus("separate"), .Select("high")) ram_1 (
    .addr({pa, offset_wb}), .din(MDin), .data(ram_1_data), .str(MemWrite), .clk(CLK));  // open: sel, ld, clr
  TLB TLB (
    .PPN({ppn_in_tlb_1__5, ppn_in_tlb_0}), .miss(tlb_miss), .in_2(1'b0), .clk(CLK), .VPN({vpn_1, vpn_2}));  // open: VPN_Missed
  \流水线关卡  \u_流水线关卡_4  (
    ._32_1(M_PC), ._1_3(mem_to_reg_mem), ._1_14(MEM_RegWrite), ._32_2(MEM_IR), ._1_5(jal_mem),
    ._32_3(ram_1_data), ._32_4(R_mem), ._5_1(MEM_RegWrite_num), ._32_1_2(WB_PC),
    ._1_3_2(\流水线关卡_4__1_3_2 [0]), ._1_14_2(RegWrite), ._32_2_2(WB_IR), ._1_5_2(\流水线关卡_4__1_3_2 [1]),
    ._32_3_2(\流水线关卡_4__32_3_2 ), ._32_4_2(\流水线关卡_4__32_4_2 ), ._5_1_2(WB_RegWrite_num), .CLK(CLK), .\使能 (1'b0));  // open: _1_1, _1_11, _1_2, _1_12, _1_13, _1_4, _1_15, _1_6, _1_16, _1_7, _1_17, _1_8, _1_18, _1_9, _1_19, _1_10, _1_20, _2_1, _2_2, _32_5, _3_1, _3_2, _5_2, _32_6, _4_1, _4_2, _1_1_2, _1_11_2, _1_2_2, _1_12_2, _1_13_2, _1_4_2, _1_15_2, _1_6_2, _1_16_2, _1_7_2, _1_17_2, _1_8_2, _1_18_2, _1_9_2, _1_19_2, _1_10_2, _1_20_2, _2_1_2, _2_2_2, _32_5_2, _3_1_2, _3_2_2, _5_2_2, _32_6_2, _4_1_2, _4_2_2, 同步清零
  Adder #(.width(32)) adder_4 (.a(WB_PC), .b(32'h4), .out(adder_4_out));  // open: cin, cout
  Multiplexer #(.select(2), .width(32), .disabled("Z"), .enable("false")) multiplexer_11 (
    .in0(\流水线关卡_4__32_4_2 ), .in1(\流水线关卡_4__32_3_2 ), .in2(adder_4_out), .in3(adder_4_out),
    .out(multiplexer_11_out), .sel(\流水线关卡_4__1_3_2 ));
  Multiplexer #(.select(1), .width(16), .disabled("Z"), .enable("false")) multiplexer_12 (
    .in0(multiplexer_11_out[15:0]), .in1(multiplexer_11_out[31:16]), .out(multiplexer_12_out),
    .sel(\流水线关卡_4__32_4_2 [1]));
  assign bit_extender_4_out = {{16{1'b1}}, multiplexer_12_out};  // Bit_Extender bit_extender_4
  \流水线关卡  \u_流水线关卡_5  (
    ._1_12(tlb_miss), ._1_10(ppn_in_tlb_0), ._3_1(vpn_1), ._3_2(vpn_2), ._5_2(ppn_in_tlb_1__5),
    ._4_1(offset), ._1_12_2(\流水线关卡_5__1_12_2 ), ._1_10_2(ppn_in_tlb_0__1), ._3_1_2(vpn_1__1),
    ._3_2_2(vpn_2__1), ._5_2_2(ppn_in_tlb_1__5__1), ._4_1_2(offset_1), .CLK(CLK), .\使能 (1'b0));  // open: _1_1, _1_11, _32_1, _1_2, _1_3, _1_13, _1_4, _1_14, _32_2, _1_5, _1_15, _1_6, _1_16, _1_7, _1_17, _32_3, _1_8, _1_18, _1_9, _1_19, _32_4, _1_20, _2_1, _2_2, _32_5, _5_1, _32_6, _4_2, _1_1_2, _1_11_2, _32_1_2, _1_2_2, _1_3_2, _1_13_2, _1_4_2, _1_14_2, _32_2_2, _1_5_2, _1_15_2, _1_6_2, _1_16_2, _1_7_2, _1_17_2, _32_3_2, _1_8_2, _1_18_2, _1_9_2, _1_19_2, _32_4_2, _1_20_2, _2_1_2, _2_2_2, _32_5_2, _5_1_2, _32_6_2, _4_2_2, 同步清零
  \流水线关卡  \u_流水线关卡_6  (
    ._32_1(MEM_IR_t), ._1_12(mem_to_reg_mem_t), ._1_13(mem_write_mem_t), ._32_2(MEM_PC_t),
    ._1_6(MEM_RegWrite_t), ._1_7(jal_mem_t), ._32_4(R_mem_t), ._5_1(MEM_RegWrite__t), ._32_6(MDin_t),
    ._32_1_2(\流水线关卡_6__32_1_2 ), ._1_12_2(\流水线关卡_6__1_12_2 ), ._1_13_2(\流水线关卡_6__1_13_2 ),
    ._32_2_2(\流水线关卡_6__32_2_2 ), ._1_6_2(\流水线关卡_6__1_6_2 ), ._1_7_2(\流水线关卡_6__1_7_2 ),
    ._32_4_2(\流水线关卡_6__32_4_2 ), ._5_1_2(\流水线关卡_6__5_1_2 ), ._32_6_2(\流水线关卡_6__32_6_2 ), .CLK(CLK),
    .\使能 (1'b0));  // open: _1_1, _1_11, _1_2, _1_3, _1_4, _1_14, _1_5, _1_15, _1_16, _1_17, _32_3, _1_8, _1_18, _1_9, _1_19, _1_10, _1_20, _2_1, _2_2, _32_5, _3_1, _3_2, _5_2, _4_1, _4_2, _1_1_2, _1_11_2, _1_2_2, _1_3_2, _1_4_2, _1_14_2, _1_5_2, _1_15_2, _1_16_2, _1_17_2, _32_3_2, _1_8_2, _1_18_2, _1_9_2, _1_19_2, _1_10_2, _1_20_2, _2_1_2, _2_2_2, _32_5_2, _3_1_2, _3_2_2, _5_2_2, _4_1_2, _4_2_2, 同步清零
  Multiplexer #(.select(1), .width(32), .disabled("Z"), .enable("false")) multiplexer_13 (
    .in0(multiplexer_11_out), .in1(bit_extender_4_out), .out(RDin), .sel(1'b0));
  \流水线关卡  \u_流水线关卡_7  (
    ._32_1(\流水线关卡_6__32_1_2 ), ._1_12(\流水线关卡_6__1_12_2 ), ._1_13(\流水线关卡_6__1_13_2 ),
    ._32_2(\流水线关卡_6__32_2_2 ), ._1_6(\流水线关卡_6__1_6_2 ), ._1_7(\流水线关卡_6__1_7_2 ), ._32_4(\流水线关卡_6__32_4_2 ),
    ._5_1(\流水线关卡_6__5_1_2 ), ._32_6(\流水线关卡_6__32_6_2 ), ._32_1_2(MEM_IR), ._1_12_2(mem_to_reg_mem),
    ._1_13_2(MemWrite), ._32_2_2(M_PC), ._1_6_2(MEM_RegWrite), ._1_7_2(jal_mem), ._32_4_2(R_mem),
    ._5_1_2(MEM_RegWrite_num), ._32_6_2(MDin), .CLK(CLK), .\使能 (1'b0));  // open: _1_1, _1_11, _1_2, _1_3, _1_4, _1_14, _1_5, _1_15, _1_16, _1_17, _32_3, _1_8, _1_18, _1_9, _1_19, _1_10, _1_20, _2_1, _2_2, _32_5, _3_1, _3_2, _5_2, _4_1, _4_2, _1_1_2, _1_11_2, _1_2_2, _1_3_2, _1_4_2, _1_14_2, _1_5_2, _1_15_2, _1_16_2, _1_17_2, _32_3_2, _1_8_2, _1_18_2, _1_9_2, _1_19_2, _1_10_2, _1_20_2, _2_1_2, _2_2_2, _32_5_2, _3_1_2, _3_2_2, _5_2_2, _4_1_2, _4_2_2, 同步清零
  // Probe on vpn_2__1
  \解析pte  \u_解析pte_1  (.pte(\一级pte ), .R(\R_权限 ), .W(\W_权限 ), .X(\X_权限 ), .U(\U_权限 ), .ppn(\解析pte_1_ppn ));
  // Probe on vpn_1__1
  Register #(.width(32), .trigger("rising"), .Select("low")) satp (
    .D({32{1'b0}}), .en(1'b1), .Q(satp_q));  // open: clk, clr
  assign bit_extender_5_out = {{7{1'b0}}, vpn_2__1};  // Bit_Extender bit_extender_5
  assign bit_extender_6_out = {{4{1'b0}}, \解析pte_1_ppn };  // Bit_Extender bit_extender_6
  assign bit_extender_7_out = {{7{1'b0}}, vpn_1__1};  // Bit_Extender bit_extender_7
  assign bit_extender_8_out = {{4{1'b0}}, \根页表ppn };  // Bit_Extender bit_extender_8
  \satp解析  \satp解析_1  (.pte(satp_q), .mode(\页表模式 ), .\地址空间参数 (\地址空间参数 ), .ppn(\根页表ppn ));
  // Probe on adder_5_out
  Adder #(.width(10)) adder_5 (.a(bit_extender_5_out), .b(bit_extender_6_out), .out(adder_5_out));  // open: cin, cout
  // Probe on adder_6_out
  Adder #(.width(10)) adder_6 (.a(bit_extender_7_out), .b(bit_extender_8_out), .out(adder_6_out));  // open: cin, cout
  ROM #(.addrWidth(10), .dataWidth(32), .Select("high")) \u_二级页表存储器  (.addr(adder_5_out), .data(\二级pte ));
  ROM #(.addrWidth(10), .dataWidth(32), .Select("high")) \u_一级页表存储器  (.addr(adder_6_out), .data(\一级pte ));
  \解析pte  \u_解析pte_2  (.pte(\二级pte ), .ppn({ppn_1__in_mem, ppn_2__in_mem}));  // open: R, W, X, U
  // Probe on {vpn_1__1[2], \虚拟地址 }
  // Probe on {pa, offset_wb}
  \流水线关卡  \u_流水线关卡_8  (
    ._1_12(\流水线关卡_5__1_12_2 ), ._1_16(vpn_1__1[2]), ._1_20(ppn_in_tlb_0__1), ._3_1(ppn_2__in_mem),
    ._5_1({vpn_2__1[0], offset_1}), ._3_2(ppn_1__in_mem), ._5_2(ppn_in_tlb_1__5__1), ._4_1(offset_1),
    ._4_2({vpn_1__1[1:0], vpn_2__1[2:1]}), ._1_12_2(tlb_miss_wb), ._1_16_2(vpn_1__1[2]),
    ._1_20_2(ppn_in_tlb[0]), ._3_1_2(ppn_in_mem[2:0]), ._5_1_2(\虚拟地址 [4:0]), ._3_2_2(ppn_in_mem[5:3]),
    ._5_2_2(ppn_in_tlb[5:1]), ._4_1_2(offset_wb), ._4_2_2(\虚拟地址 [8:5]), .CLK(CLK), .\使能 (1'b0));  // open: _1_1, _1_11, _32_1, _1_2, _1_3, _1_13, _1_4, _1_14, _32_2, _1_5, _1_15, _1_6, _1_7, _1_17, _32_3, _1_8, _1_18, _1_9, _1_19, _32_4, _1_10, _2_1, _2_2, _32_5, _32_6, _1_1_2, _1_11_2, _32_1_2, _1_2_2, _1_3_2, _1_13_2, _1_4_2, _1_14_2, _32_2_2, _1_5_2, _1_15_2, _1_6_2, _1_7_2, _1_17_2, _32_3_2, _1_8_2, _1_18_2, _1_9_2, _1_19_2, _32_4_2, _1_10_2, _2_1_2, _2_2_2, _32_5_2, _32_6_2, 同步清零
  // Probe on offset_wb
  // Probe on {pa, offset_wb}
  Multiplexer #(.select(1), .width(6), .disabled("Z"), .enable("false")) multiplexer_14 (
    .in0(ppn_in_tlb), .in1(ppn_in_mem), .out(pa), .sel(tlb_miss_wb));

  // Other names for the same wires on the sheet: jmp_ex = JMP; MEM_PC[31:0] = M_PC; mem_write_mem = MemWrite;
  //   R2_mem[31:0] = MDin; reg_write_ex = EX_RegWrite; WB_RegWrite = RegWrite; pa[3:0] = offset_wb;
  //   物理地址[9:0] = {pa, offset_wb}; ppn[5:0] = pa; 虚拟地址[9] = vpn_1__1[2]

  // Notes on the sheet:
  //   中断源
  //   时空图监测，可删除
  //   中断等待指示
  //   数码管输出
  //   contents of 指令存储器 (hex, n*v repeats v):
  //   20090000 8d240000 8d240004 8d240008 8d24000c 8d240100 8d240104 8d240108 8d24010c 8100001
  //   控制位
  //   流水调试日志用
  //   暂停节拍，不能为0
  //   OP
  //   FUNC
  //   rs
  //   rt
  //   rd
  //   戳工具置1进入计数暂停模式，ctrl+k时钟自动运行到对应节拍暂停
  //   可计数暂停的时钟源
  //   rd
  //   为方便自动评测，需要输出流水线各段保存的PC值，注意是PC不是PC+4，另外ID段寄存器写入信息，Mem段内存写入信息也要输出
  //   如果 TLB 不命中，从内存中找页表项
  //   比博燃队 团队任务演示
  //   虚拟内存支持
  //   林国平 尹泽源 张泽良 车春池
  //   contents of 二级页表存储器 (hex, n*v repeats v):
  //   0 310 3c0
  //   contents of 一级页表存储器 (hex, n*v repeats v):
  //   301 15*0 3c2
  //   这里为了方便实现，页表和内存分开存
endmodule

module \中断按键参考电路  (
  input  \同步清零信号 ,
  output \与中断屏蔽位与 
);

  wire \_1号中断_out , and_1_out, clock_1_out, d_ff_1_q, or_1_out, or_2_out;

  Clock #(.highDuration(1), .lowDuration(1)) clock_1 (.out(clock_1_out));
  Button \_1号中断  (.out(\_1号中断_out ));
  or or_1 (or_1_out, \与中断屏蔽位与 , d_ff_1_q);
  LED #(.active("true")) \_1号中断等待指示灯  (.in(or_1_out));
  D_Flip_Flop #(.trigger("rising"), .Pre_Clr_Positions("LEGACY"), .NegatePresetClear("false"), .enable("true"), .NewFFLayout("false")) d_ff_1 (
    .clk(\_1号中断_out ), .D(1'b1), .Q(d_ff_1_q), .reset(\与中断屏蔽位与 ));  // open: Qn, preset, en
  or or_2 (or_2_out, d_ff_1_q, \与中断屏蔽位与 );
  and and_1 (and_1_out, or_2_out, ~\同步清零信号 );  // AND_Gate
  D_Flip_Flop #(.trigger("rising"), .Pre_Clr_Positions("LEGACY"), .NegatePresetClear("false"), .enable("true"), .NewFFLayout("false")) IR1 (
    .clk(clock_1_out), .D(and_1_out), .Q(\与中断屏蔽位与 ));  // open: Qn, preset, en, reset

  // Notes on the sheet:
  //   中断信号采样参考电路
  //   Reset 
endmodule
module \单周期MIPS_单级中断  (
  input  IR1,
  input  IR2,
  input  IR3,
  output RegWrite,
  output MemWrite,
  output [31:0] PC,
  output [31:0] IR,
  output [31:0] RDin,
  output [31:0] MDin,
  output [31:0] LedData
);

  wire alu_srcb, and_3_out, and_4_out, and_5_out, and_6_out, and_7_out, and_8_out, beq, bne, CLK, CLR1, CLR2,
       CLR3, comparator_1_eq, comparator_2_eq, comparator_3_eq, comparator_4_eq, comparator_5_eq, d_ff_1_q,
       d_ff_2_q, d_ff_3_q, equal, eret, Go, halt, IE, INT, INT0, INT1, INT2, INT3, IR1_t, IR2_t, IR3_t, IRA,
       IRB, IRC, jal, jmp, jmp_if, jr, led_en, mem_to_reg, not_1_out, not_2_out, not_3_out, not_4_out,
       or_1_out, or_10_out, or_11_out, or_12_out, reg_dst, rst, signed_ext, syscall, W1, W2, W3;
  wire [1:0] priority_encoder_1_out, register_2_q;
  wire [3:0] alu_op;
  wire [4:0] multiplexer_6_out, multiplexer_7_out, multiplexer_8_out, multiplexer_9_out;
  wire [15:0] \总周期数 ;
  wire [31:0] bit_extender_1_out, bit_extender_2_out, epc_in, epc_out, int_addr, mips_alu_1_result,
       multiplexer_1_out, multiplexer_2_out, multiplexer_4_out, multiplexer_5_out, multiplexer_10_out,
       multiplexer_11_out, multiplexer_12_out, pc_4, pc_imm, pc_jr, ram_1_data, shifter_1_out;

  Clock #(.highDuration(1), .lowDuration(1)) clock_1 (.out(CLK));
  Button _1 ();  // open: out
  Button _2 ();  // open: out
  Button _3 ();  // open: out
  Button \u_继续运行  (.out(Go));
  LED #(.active("true")) led_1 (.in(W1));
  LED #(.active("true")) led_2 (.in(W2));
  LED #(.active("true")) led_3 (.in(W3));
  Hex_Digit_Display hex_digit_display_1 (.value(LedData[31:28]));  // open: dp
  Comparator #(.width(16), .mode("twosComplement")) comparator_1 (
    .a(16'h23b), .b(\总周期数 ), .eq(comparator_1_eq));  // open: gt, lt
  Comparator #(.width(16), .mode("twosComplement")) comparator_2 (
    .a(\总周期数 ), .b(16'h1), .eq(comparator_2_eq));  // open: gt, lt
  Comparator #(.width(16), .mode("twosComplement")) comparator_3 (
    .a(\总周期数 ), .b(16'h4), .eq(comparator_3_eq));  // open: gt, lt
  Comparator #(.width(16), .mode("twosComplement")) comparator_4 (
    .a(\总周期数 ), .b(16'h7), .eq(comparator_4_eq));  // open: gt, lt
  Hex_Digit_Display hex_digit_display_2 (.value(LedData[27:24]));  // open: dp
  Hex_Digit_Display hex_digit_display_3 (.value(LedData[23:20]));  // open: dp
  or or_1 (or_1_out, comparator_1_eq, comparator_2_eq);
  assign IRA = or_1_out ? ~CLK : 1'bz;  // Controlled_Inverter controlled_inverter_1
  assign IRB = comparator_3_eq ? ~CLK : 1'bz;  // Controlled_Inverter controlled_inverter_2
  assign IRC = comparator_4_eq ? ~CLK : 1'bz;  // Controlled_Inverter controlled_inverter_3
  Hex_Digit_Display hex_digit_display_4 (.value(LedData[15:12]));  // open: dp
  Hex_Digit_Display hex_digit_display_5 (.value(LedData[19:16]));  // open: dp
  Pull_Resistor #(.pull(0)) pull_resistor_1 (.node(IRA));
  Pull_Resistor #(.pull(0)) pull_resistor_2 (.node(IRB));
  Pull_Resistor #(.pull(0)) pull_resistor_3 (.node(IRC));
  Hex_Digit_Display hex_digit_display_6 (.value(LedData[7:4]));  // open: dp
  Hex_Digit_Display hex_digit_display_7 (.value(LedData[11:8]));  // open: dp
  // Probe on \总周期数 
  Hex_Digit_Display hex_digit_display_8 (.value(LedData[3:0]));  // open: dp
  Button button_1 (.out(rst));
  Multiplexer #(.select(1), .width(32), .disabled("Z"), .enable("false")) multiplexer_1 (
    .in0(pc_4), .in1(pc_imm), .out(multiplexer_1_out), .sel(jmp_if));
  Multiplexer #(.select(1), .width(32), .disabled("Z"), .enable("false")) multiplexer_2 (
    .in0(multiplexer_1_out), .in1({pc_4[31:28], IR[25:0], 2'b00}), .out(multiplexer_2_out), .sel(jmp));
  Multiplexer #(.select(1), .width(32), .disabled("Z"), .enable("false")) multiplexer_3 (
    .in0(multiplexer_2_out), .in1(pc_jr), .out(epc_in), .sel(jr));
  Multiplexer #(.select(1), .width(32), .disabled("Z"), .enable("false")) multiplexer_4 (
    .in0(epc_in), .in1(int_addr), .out(multiplexer_4_out), .sel(INT));
  Multiplexer #(.select(1), .width(32), .disabled("Z"), .enable("false")) multiplexer_5 (
    .in0(multiplexer_4_out), .in1(epc_out), .out(multiplexer_5_out), .sel(eret));
  not not_1 (not_1_out, halt);
  // Mips_Probe mips_probe_1: pin names not known; wires that end beside it: {pc_4[31:28], IR[25:0], 2'b00}
  or or_2 (IR1_t, IR1, IRA);
  Register #(.width(32), .trigger("rising"), .Select("low")) u_PC (
    .D(multiplexer_5_out), .en(not_1_out), .Q(PC), .clk(CLK), .clr(rst));
  or or_3 (IR2_t, IR2, IRB);
  Multiplexer #(.select(1), .width(5), .disabled("Z"), .enable("false")) multiplexer_6 (
    .in0(IR[20:16]), .in1(5'b00100), .out(multiplexer_6_out), .sel(syscall));
  Multiplexer #(.select(1), .width(5), .disabled("Z"), .enable("false")) multiplexer_7 (
    .in0(IR[20:16]), .in1(IR[15:11]), .out(multiplexer_7_out), .sel(reg_dst));
  // Probe on IR[15:0]
  // Probe on PC
  \单周期硬布线控制器  \u_单周期硬布线控制器_1  (
    .Func(IR[5:0]), .OP(IR[31:26]), .ALU_OP(alu_op), .MemToReg(mem_to_reg), .MemWrite(MemWrite),
    .ALU_SRC(alu_srcb), .RegWrite(RegWrite), .SysCALL(syscall), .SignedExt(signed_ext), .RegDst(reg_dst),
    .JR(jr), .JMP(jmp), .Beq(beq), .JAL(jal), .Bne(bne), .ERET(eret));
  Multiplexer #(.select(1), .width(5), .disabled("Z"), .enable("false")) multiplexer_8 (
    .in0(IR[25:21]), .in1(5'b00010), .out(multiplexer_8_out), .sel(syscall));
  Multiplexer #(.select(1), .width(5), .disabled("Z"), .enable("false")) multiplexer_9 (
    .in0(multiplexer_7_out), .in1({5{1'b1}}), .out(multiplexer_9_out), .sel(jal));
  or or_4 (IR3_t, IR3, IRC);
  // Probe on multiplexer_8_out
  // Probe on multiplexer_6_out
  // Probe on multiplexer_9_out
  // Probe on bit_extender_1_out
  ROM #(.addrWidth(10), .dataWidth(32), .Select("high")) rom_1 (.addr(PC[11:2]), .data(IR));
  MIPS_Regifile mips_regifile_1 (
    .Din(RDin), .Clk(CLK), .R1(pc_jr), .R2(MDin), .WE(RegWrite), .W_num(multiplexer_9_out),
    .R1_num(multiplexer_8_out), .R2_num(multiplexer_6_out));
  assign bit_extender_1_out = {{16{1'b0}}, IR[15:0]};  // Bit_Extender bit_extender_1
  assign bit_extender_2_out = {{16{IR[15]}}, IR[15:0]};  // Bit_Extender bit_extender_2
  // Mips_Probe mips_probe_2: pin names not known; wires that end beside it: IR
  Adder #(.width(32)) adder_1 (.a(PC), .b(32'h4), .out(pc_4));  // open: cin, cout
  // Probe on pc_jr
  Multiplexer #(.select(1), .width(32), .disabled("Z"), .enable("false")) multiplexer_10 (
    .in0(bit_extender_1_out), .in1(bit_extender_2_out), .out(multiplexer_10_out), .sel(signed_ext));
  Comparator #(.width(32), .mode("twosComplement")) comparator_5 (
    .a(pc_jr), .b(32'h22), .eq(comparator_5_eq));  // open: gt, lt
  and and_1 (halt, syscall, ~comparator_5_eq);  // AND_Gate
  Multiplexer #(.select(1), .width(32), .disabled("Z"), .enable("false")) multiplexer_11 (
    .in0(MDin), .in1(multiplexer_10_out), .out(multiplexer_11_out), .sel(alu_srcb));
  Shifter #(.width(32), .shift("ll")) shifter_1 (.in(bit_extender_2_out), .\dist (5'b00010), .out(shifter_1_out));
  Register #(.width(32), .trigger("rising"), .Select("low")) EPC (
    .D(epc_in), .en(INT), .Q(epc_out), .clk(CLK));  // open: clr
  and and_2 (led_en, syscall, comparator_5_eq);
  MIPS_ALU mips_alu_1 (
    .X(pc_jr), .Y(multiplexer_11_out), .AluOP(alu_op), .Equal(equal), .Result(mips_alu_1_result),
    .shamt(IR[10:6]));  // open: Result_2
  Adder #(.width(32)) adder_2 (.a(shifter_1_out), .b(pc_4), .out(pc_imm));  // open: cin, cout
  and and_3 (and_3_out, beq, equal);
  and and_4 (and_4_out, bne, ~equal);  // AND_Gate
  Register #(.width(32), .trigger("rising"), .Select("low")) register_1 (
    .D(MDin), .en(led_en), .Q(LedData), .clk(CLK), .clr(rst));
  or or_5 (jmp_if, and_3_out, and_4_out);
  not not_2 (not_2_out, halt);
  RAM #(.addrWidth(10), .dataWidth(32), .bus("separate"), .Select("high")) ram_1 (
    .addr(mips_alu_1_result[11:2]), .din(MDin), .data(ram_1_data), .str(MemWrite), .clk(CLK));  // open: sel, ld, clr
  Counter #(.width(16), .max('hffff), .ongoal("wrap"), .trigger("rising"), .behavior("old")) counter_1 (
    .count(not_2_out), .Q(\总周期数 ), .clk(CLK), .clr(rst));  // open: load, D, carry, preset
  Multiplexer #(.select(1), .width(32), .disabled("Z"), .enable("false")) multiplexer_12 (
    .in0(mips_alu_1_result), .in1(ram_1_data), .out(multiplexer_12_out), .sel(mem_to_reg));
  Multiplexer #(.select(1), .width(32), .disabled("Z"), .enable("false")) multiplexer_13 (
    .in0(multiplexer_12_out), .in1(pc_4), .out(RDin), .sel(jal));
  or or_6 (W1, INT1, d_ff_1_q);
  or or_7 (W2, INT2, d_ff_2_q);
  or or_8 (W3, INT3, d_ff_3_q);
  and and_5 (and_5_out, INT0, not_3_out);
  not not_3 (not_3_out, eret);
  D_Flip_Flop #(.trigger("rising"), .Pre_Clr_Positions("LEGACY"), .NegatePresetClear("false"), .enable("true"), .NewFFLayout("false")) d_ff_1 (
    .clk(IR1_t), .D(1'b1), .Q(d_ff_1_q), .reset(INT1));  // open: Qn, preset, en
  D_Flip_Flop #(.trigger("rising"), .Pre_Clr_Positions("LEGACY"), .NegatePresetClear("false"), .enable("true"), .NewFFLayout("false")) d_ff_2 (
    .clk(IR2_t), .D(1'b1), .Q(d_ff_2_q), .reset(INT2));  // open: Qn, preset, en
  D_Flip_Flop #(.trigger("rising"), .Pre_Clr_Positions("LEGACY"), .NegatePresetClear("false"), .enable("true"), .NewFFLayout("false")) d_ff_3 (
    .clk(IR3_t), .D(1'b1), .Q(d_ff_3_q), .reset(INT3));  // open: Qn, preset, en
  Priority_Encoder #(.select(2), .disabled("Z")) priority_encoder_1 (
    .in0(INT1), .in1(INT2), .in2(INT3), .out(priority_encoder_1_out));  // open: in3, gs, en_out, en_in
  or or_9 (INT0, INT1, INT2, INT3);
  D_Flip_Flop #(.trigger("rising"), .Pre_Clr_Positions("LEGACY"), .NegatePresetClear("false"), .enable("true"), .NewFFLayout("true")) d_ff_4 (
    .clk(CLK), .D(and_5_out), .Q(IE));  // open: Qn, preset, en, reset
  or or_10 (or_10_out, d_ff_1_q, INT1);
  or or_11 (or_11_out, d_ff_2_q, INT2);
  or or_12 (or_12_out, d_ff_3_q, INT3);
  and and_6 (and_6_out, or_10_out, ~CLR1);  // AND_Gate
  and and_7 (and_7_out, or_11_out, ~CLR2);  // AND_Gate
  and and_8 (and_8_out, or_12_out, ~CLR3);  // AND_Gate
  Multiplexer #(.select(2), .width(32), .disabled("Z"), .enable("false")) multiplexer_14 (
    .in0(32'h30ac), .in1(32'h3150), .in2(32'h31f4), .out(int_addr), .sel(priority_encoder_1_out));  // open: in3
  not not_4 (not_4_out, IE);
  D_Flip_Flop #(.trigger("rising"), .Pre_Clr_Positions("LEGACY"), .NegatePresetClear("false"), .enable("true"), .NewFFLayout("false")) u_IR1 (
    .clk(CLK), .D(and_6_out), .Q(INT1));  // open: Qn, preset, en, reset
  D_Flip_Flop #(.trigger("rising"), .Pre_Clr_Positions("LEGACY"), .NegatePresetClear("false"), .enable("true"), .NewFFLayout("false")) u_IR3 (
    .clk(CLK), .D(and_7_out), .Q(INT2));  // open: Qn, preset, en, reset
  D_Flip_Flop #(.trigger("rising"), .Pre_Clr_Positions("LEGACY"), .NegatePresetClear("false"), .enable("true"), .NewFFLayout("false")) IR3_2 (
    .clk(CLK), .D(and_8_out), .Q(INT3));  // open: Qn, preset, en, reset
  Demultiplexer #(.select(2), .width(1), .tristate("false"), .disabled("Z"), .enable("false")) demultiplexer_1 (
    .out0(CLR1), .out1(CLR2), .out2(CLR3), .in(eret), .sel(register_2_q));  // open: out3
  and and_9 (INT, INT0, not_4_out);
  Register #(.width(2), .trigger("rising"), .Select("low")) register_2 (
    .D(priority_encoder_1_out), .en(INT), .Q(register_2_q), .clk(CLK));  // open: clr

  // Other names for the same wires on the sheet: a0[31:0] = MDin; addr[25:0] = IR[25:0]; imm[15:0] = IR[15:0];
  //   mem_write = MemWrite; reg_write = RegWrite

  // Notes on the sheet:
  //   中断源
  //   中断等待指示
  //   总复位信号应将除ROM以外所有存储组件全部清零
  //   单级中断测试信号模拟器
  //   数码管输出
  //   数码管输出应该用寄存器锁存，否则显示数据只能一闪而过
  //   OP
  //   Func
  //   rs
  //   rt
  //   rd
  //   shamt
  //   指令存储器
  //   contents of rom_1 (hex, n*v repeats v):
  //   201d07d0 20100001 109fc0 139fc3 8021 2012000c 24160008 26100001 3210000f 20080008 20090001 139900
  //   2709825 132020 20020022 c 1094022 1500fff9 22100001 2018000f 2188024 108700 20080008 20090001 139902
  //   2709825 132021 20020022 c 1094022 1500fff9 108702 2c9b022 12c00001 8000c07 4020 1084027 84400
  //   3508ffff 82021 20020022 c 8000c01 afa20000 23bd0004 afa40000 23bd0004 afb00000 23bd0004 afb30000
  //   23bd0004 afb40000 23bd0004 afb50000 23bd0004 afb60000 23bd0004 20160001 20140003 20150001 168020
  //   108100 2149825 132020 20020022 c 1600fffa 295a022 1680fff7 23bdfffc 8fb60000 23bdfffc 8fb50000
  //   23bdfffc 8fb40000 23bdfffc 8fb30000 23bdfffc 8fb00000 23bdfffc 8fa40000 23bdfffc 8fa20000 42000018
  //   afa20000 23bd0004 afa40000 23bd0004 afb00000 23bd0004 afb30000 23bd0004 afb40000 23bd0004 afb50000
  //   23bd0004 afb60000 23bd0004 20160002 20140003 20150001 168020 108100 2149825 132020 20020022 c
  //   1600fffa 295a022 1680fff7 23bdfffc 8fb60000 23bdfffc 8fb50000 23bdfffc 8fb40000 23bdfffc 8fb30000
  //   23bdfffc 8fb00000 23bdfffc 8fa40000 23bdfffc 8fa20000 42000018 afa20000 23bd0004 afa40000 23bd0004
  //   afb00000 23bd0004 afb30000 23bd0004 afb40000 23bd0004 afb50000 23bd0004 afb60000 23bd0004 20160003
  //   20140003 20150001 168020 108100 2149825 132020 20020022 c 1600fffa 295a022 1680fff7 23bdfffc
  //   8fb60000 23bdfffc 8fb50000 23bdfffc 8fb40000 23bdfffc 8fb30000 23bdfffc 8fb00000 23bdfffc 8fa40000
  //   23bdfffc 8fa20000 42000018
  //   指令字
  //   为方便自动评测，需要输出PC，IR，寄存器堆写如数据RDin
  //   RAM写使能MemWrite、RAM写入数据MDin等信号
  //   Reset 
  //   Reset 
  //   Reset 
endmodule

module \单周期MIPS_多级中断  (
  input  IR1,
  input  IR2,
  input  IR3,
  output RegWrite,
  output MemWrite,
  output [31:0] PC,
  output [31:0] IR,
  output [31:0] RDin,
  output [31:0] MDin,
  output [31:0] LedData
);

  wire CLK, comparator_1_eq, comparator_2_eq, comparator_3_eq, comparator_4_eq, comparator_5_eq, Go, IR1_t,
       IR2_t, IR3_t, IRA, IRB, IRC, or_1_out, or_2_out, W1, W2, W3;
  wire [15:0] \总周期数 ;

  Clock #(.highDuration(1), .lowDuration(1)) clock_1 (.out(CLK));
  Button _1 ();  // open: out
  Button _2 ();  // open: out
  Button _3 ();  // open: out
  Button \u_继续运行  (.out(Go));
  LED #(.active("true")) led_1 (.in(W1));
  LED #(.active("true")) led_2 (.in(W2));
  LED #(.active("true")) led_3 (.in(W3));
  Hex_Digit_Display hex_digit_display_1 (.value(LedData[31:28]));  // open: dp
  Comparator #(.width(16), .mode("twosComplement")) comparator_1 (
    .a(\总周期数 ), .b(16'h7), .eq(comparator_1_eq));  // open: gt, lt
  Comparator #(.width(16), .mode("twosComplement")) comparator_2 (
    .a(\总周期数 ), .b(16'h241), .eq(comparator_2_eq));  // open: gt, lt
  Hex_Digit_Display hex_digit_display_2 (.value(LedData[27:24]));  // open: dp
  Hex_Digit_Display hex_digit_display_3 (.value(LedData[23:20]));  // open: dp
  Comparator #(.width(16), .mode("twosComplement")) comparator_3 (
    .a(16'h258), .b(\总周期数 ), .eq(comparator_3_eq));  // open: gt, lt
  or or_1 (or_1_out, comparator_3_eq, comparator_4_eq);
  Comparator #(.width(16), .mode("twosComplement")) comparator_4 (
    .a(\总周期数 ), .b(16'h1), .eq(comparator_4_eq));  // open: gt, lt
  Comparator #(.width(16), .mode("twosComplement")) comparator_5 (
    .a(\总周期数 ), .b(16'h4), .eq(comparator_5_eq));  // open: gt, lt
  or or_2 (or_2_out, comparator_1_eq, comparator_2_eq);
  Hex_Digit_Display hex_digit_display_4 (.value(LedData[19:16]));  // open: dp
  Hex_Digit_Display hex_digit_display_5 (.value(LedData[15:12]));  // open: dp
  Pull_Resistor #(.pull(0)) pull_resistor_1 (.node(IRA));
  assign IRA = or_1_out ? ~CLK : 1'bz;  // Controlled_Inverter controlled_inverter_1
  Pull_Resistor #(.pull(0)) pull_resistor_2 (.node(IRB));
  assign IRB = comparator_5_eq ? ~CLK : 1'bz;  // Controlled_Inverter controlled_inverter_2
  Pull_Resistor #(.pull(0)) pull_resistor_3 (.node(IRC));
  assign IRC = or_2_out ? ~CLK : 1'bz;  // Controlled_Inverter controlled_inverter_3
  Hex_Digit_Display hex_digit_display_6 (.value(LedData[11:8]));  // open: dp
  Hex_Digit_Display hex_digit_display_7 (.value(LedData[7:4]));  // open: dp
  // Probe on \总周期数 
  Hex_Digit_Display hex_digit_display_8 (.value(LedData[3:0]));  // open: dp
  or or_3 (IR1_t, IR1, IRA);
  or or_4 (IR2_t, IR2, IRB);
  or or_5 (IR3_t, IR3, IRC);

  // Notes on the sheet:
  //   中断源
  //   中断等待指示
  //   总复位信号应将除ROM以外所有存储组件全部清零
  //   多级中断测试信号模拟器
  //   数码管输出
  //   数码管输出应该用寄存器锁存，否则显示数据只能一闪而过
  //   为方便自动评测，需要输出PC，IR，寄存器堆写如数据RDin
  //   RAM写使能MemWrite、RAM写入数据MDin等信号
endmodule

module \封装正确性测试  (
);

  wire IR1, IR2, IR3, MemW, RegW;
  wire [31:0] EX_PC, ID_PC, IF_PC, IR, LED, MDin, MDinr, MEM_PC, PC, RDin, RDinr, WB_PC;

  \单周期MIPS  \u_单周期mips_1  (
    .RegWrite(RegW), .MemWrite(MemW), .PC(PC), .IR(IR), .RDin(RDin), .MDin(MDin), .LedData(LED));  // open: IR1, IR2, IR3
  \气泡流水线  \u_气泡流水线_1  (
    .RegWrite(RegW), .MemWrite(MemW), .IF_PC(IF_PC), .ID_PC(ID_PC), .EX_PC(EX_PC), .M_PC(MEM_PC),
    .WB_PC(WB_PC), .RDin(RDinr), .MDin(MDinr), .LedData(LED));
  \单周期MIPS_单级中断  \u_单周期mips_单级中断_1  (
    .IR1(IR1), .IR2(IR2), .IR3(IR3), .RegWrite(RegW), .MemWrite(MemW), .PC(PC), .IR(IR), .RDin(RDin),
    .MDin(MDin), .LedData(LED));
  \理想流水线  \u_理想流水线_1  (
    .RegWrite(RegW), .MemWrite(MemW), .IF_PC(IF_PC), .ID_PC(ID_PC), .EX_PC(EX_PC), .M_PC(MEM_PC),
    .WB_PC(WB_PC), .RDin(RDinr), .MDin(MDinr), .LedData(LED));
  \重定向流水线  \u_重定向流水线_1  (
    .RegWrite(RegW), .MemWrite(MemW), .IF_PC(IF_PC), .ID_PC(ID_PC), .EX_PC(EX_PC), .M_PC(MEM_PC),
    .WB_PC(WB_PC), .RDin(RDinr), .MDin(MDinr), .LedData(LED));
  \单周期MIPS_多级中断  \u_单周期mips_多级中断_1  (
    .IR1(IR1), .IR2(IR2), .IR3(IR3), .RegWrite(RegW), .MemWrite(MemW), .PC(PC), .IR(IR), .RDin(RDin),
    .MDin(MDin), .LedData(LED));

  // Notes on the sheet:
  //   单周期封装测试
  //   气泡流水封装测试
  //   单周期+单级中断封装测试
  //   请检查上面封装有无位宽不匹配，引脚标签是否和连接的标签相对应，否则无法在educoder平台上正确测试
  //   理想流水封装测试
  //   重定向流水封装测试
  //   单周期+多级中断封装测试
endmodule

module IF_ID (
  input  [31:0] \IR输入 ,
  input  [31:0] \PC输入 ,
  input  \输入数据有效 ,
  input  CLK,
  input  \清零_气泡_高 ,
  input  \使能端 ,
  output [31:0] \IR输出 ,
  output \输出数据有效 ,
  output [31:0] \PC输出 
);

  wire multiplexer_3_out, pull_resistor_2_node;
  wire [31:0] multiplexer_1_out, multiplexer_2_out;

  Multiplexer #(.select(1), .width(32), .disabled("Z"), .enable("false")) multiplexer_1 (
    .in0(\IR输入 ), .in1({32{1'b0}}), .out(multiplexer_1_out), .sel(\清零_气泡_高 ));
  Multiplexer #(.select(1), .width(32), .disabled("Z"), .enable("false")) multiplexer_2 (
    .in0(\PC输入 ), .in1({32{1'b0}}), .out(multiplexer_2_out), .sel(\清零_气泡_高 ));
  Multiplexer #(.select(1), .width(1), .disabled("Z"), .enable("false")) multiplexer_3 (
    .in0(\输入数据有效 ), .in1(1'b0), .out(multiplexer_3_out), .sel(\清零_气泡_高 ));
  Pull_Resistor #(.pull(0)) pull_resistor_1 (.node(\清零_气泡_高 ));
  Pull_Resistor #(.pull(0)) pull_resistor_2 (.node(pull_resistor_2_node));
  not not_1 (pull_resistor_2_node, \使能端 );
  Register #(.width(32), .trigger("rising"), .Select("low")) register_1 (
    .D(multiplexer_1_out), .en(pull_resistor_2_node), .Q(\IR输出 ), .clk(CLK));  // open: clr
  Register #(.width(32), .trigger("rising"), .Select("low")) register_2 (
    .D(multiplexer_2_out), .en(pull_resistor_2_node), .Q(\PC输出 ), .clk(CLK));  // open: clr
  Register #(.width(1), .trigger("rising"), .Select("low")) register_3 (
    .D(multiplexer_3_out), .en(pull_resistor_2_node), .Q(\输出数据有效 ), .clk(CLK));  // open: clr

  // Other names for the same wires on the sheet: IR_in[31:0] = \IR输入 ; IR_out[31:0] = \IR输出 ; PC_in[31:0] = \PC输入 ;
  //   PC_out[31:0] = \PC输出 
endmodule

module ID_EX (
  input  [31:0] \IR输入 ,
  input  [31:0] \PC输入 ,
  input  [31:0] \RD1输入 ,
  input  [31:0] \RD2输入 ,
  input  [31:0] \Imm输入 ,
  input  in_6,
  input  in_7,
  input  in_8,
  input  in_9,
  input  in_10,
  input  in_11,
  input  in_12,
  input  \当前传输数据有效_输入 ,
  input  [3:0] in_14,
  input  CLK,
  input  \同步清零_气泡_高 ,
  input  \使能端 ,
  output [31:0] \IR输出 ,
  output [31:0] \PC输出 ,
  output [31:0] \RD1输出 ,
  output [31:0] \RD2输出 ,
  output [31:0] \Imm输出 ,
  output out_23,
  output out_24,
  output out_25,
  output out_26,
  output out_27,
  output out_28,
  output out_29,
  output \当前传输数据有效_输出 ,
  output [3:0] out_31
);

  wire multiplexer_6_out, multiplexer_7_out, multiplexer_8_out, multiplexer_9_out, multiplexer_10_out,
       multiplexer_11_out, multiplexer_12_out, multiplexer_13_out, pull_resistor_2_node;
  wire [3:0] multiplexer_14_out;
  wire [31:0] multiplexer_1_out, multiplexer_2_out, multiplexer_3_out, multiplexer_4_out, multiplexer_5_out;

  Multiplexer #(.select(1), .width(32), .disabled("Z"), .enable("false")) multiplexer_1 (
    .in0(\IR输入 ), .in1({32{1'b0}}), .out(multiplexer_1_out), .sel(\同步清零_气泡_高 ));
  Register #(.width(32), .trigger("rising"), .Select("low")) register_1 (
    .D(multiplexer_1_out), .en(pull_resistor_2_node), .Q(\IR输出 ), .clk(CLK));  // open: clr
  Pull_Resistor #(.pull(0)) pull_resistor_1 (.node(\同步清零_气泡_高 ));
  Multiplexer #(.select(1), .width(32), .disabled("Z"), .enable("false")) multiplexer_2 (
    .in0(\PC输入 ), .in1({32{1'b0}}), .out(multiplexer_2_out), .sel(\同步清零_气泡_高 ));
  Register #(.width(32), .trigger("rising"), .Select("low")) register_2 (
    .D(multiplexer_2_out), .en(pull_resistor_2_node), .Q(\PC输出 ), .clk(CLK));  // open: clr
  Multiplexer #(.select(1), .width(32), .disabled("Z"), .enable("false")) multiplexer_3 (
    .in0(\RD1输入 ), .in1({32{1'b0}}), .out(multiplexer_3_out), .sel(\同步清零_气泡_高 ));
  Register #(.width(32), .trigger("rising"), .Select("low")) register_3 (
    .D(multiplexer_3_out), .en(pull_resistor_2_node), .Q(\RD1输出 ), .clk(CLK));  // open: clr
  Multiplexer #(.select(1), .width(32), .disabled("Z"), .enable("false")) multiplexer_4 (
    .in0(\RD2输入 ), .in1({32{1'b0}}), .out(multiplexer_4_out), .sel(\同步清零_气泡_高 ));
  Multiplexer #(.select(1), .width(32), .disabled("Z"), .enable("false")) multiplexer_5 (
    .in0(\Imm输入 ), .in1({32{1'b0}}), .out(multiplexer_5_out), .sel(\同步清零_气泡_高 ));
  Register #(.width(32), .trigger("rising"), .Select("low")) register_4 (
    .D(multiplexer_4_out), .en(pull_resistor_2_node), .Q(\RD2输出 ), .clk(CLK));  // open: clr
  Register #(.width(32), .trigger("rising"), .Select("low")) register_5 (
    .D(multiplexer_5_out), .en(pull_resistor_2_node), .Q(\Imm输出 ), .clk(CLK));  // open: clr
  Multiplexer #(.select(1), .width(1), .disabled("Z"), .enable("false")) multiplexer_6 (
    .in0(in_6), .out(multiplexer_6_out), .sel(\同步清零_气泡_高 ));  // open: in1
  Register #(.width(1), .trigger("rising"), .Select("low")) register_6 (
    .D(multiplexer_6_out), .en(pull_resistor_2_node), .Q(out_23), .clk(CLK));  // open: clr
  Multiplexer #(.select(1), .width(1), .disabled("Z"), .enable("false")) multiplexer_7 (
    .in0(in_7), .out(multiplexer_7_out), .sel(\同步清零_气泡_高 ));  // open: in1
  Register #(.width(1), .trigger("rising"), .Select("low")) register_7 (
    .D(multiplexer_7_out), .en(pull_resistor_2_node), .Q(out_24), .clk(CLK));  // open: clr
  Multiplexer #(.select(1), .width(1), .disabled("Z"), .enable("false")) multiplexer_8 (
    .in0(in_8), .in1(1'b0), .out(multiplexer_8_out), .sel(\同步清零_气泡_高 ));
  Register #(.width(1), .trigger("rising"), .Select("low")) register_8 (
    .D(multiplexer_8_out), .en(pull_resistor_2_node), .Q(out_25), .clk(CLK));  // open: clr
  Multiplexer #(.select(1), .width(1), .disabled("Z"), .enable("false")) multiplexer_9 (
    .in0(in_9), .in1(1'b0), .out(multiplexer_9_out), .sel(\同步清零_气泡_高 ));
  Register #(.width(1), .trigger("rising"), .Select("low")) register_9 (
    .D(multiplexer_9_out), .en(pull_resistor_2_node), .Q(out_26), .clk(CLK));  // open: clr
  Multiplexer #(.select(1), .width(1), .disabled("Z"), .enable("false")) multiplexer_10 (
    .in0(in_10), .in1(1'b0), .out(multiplexer_10_out), .sel(\同步清零_气泡_高 ));
  Register #(.width(1), .trigger("rising"), .Select("low")) register_10 (
    .D(multiplexer_10_out), .en(pull_resistor_2_node), .Q(out_27), .clk(CLK));  // open: clr
  Multiplexer #(.select(1), .width(1), .disabled("Z"), .enable("false")) multiplexer_11 (
    .in0(in_11), .in1(1'b0), .out(multiplexer_11_out), .sel(\同步清零_气泡_高 ));
  Register #(.width(1), .trigger("rising"), .Select("low")) register_11 (
    .D(multiplexer_11_out), .en(pull_resistor_2_node), .Q(out_28), .clk(CLK));  // open: clr
  Multiplexer #(.select(1), .width(1), .disabled("Z"), .enable("false")) multiplexer_12 (
    .in0(in_12), .in1(1'b0), .out(multiplexer_12_out), .sel(\同步清零_气泡_高 ));
  Multiplexer #(.select(1), .width(1), .disabled("Z"), .enable("false")) multiplexer_13 (
    .in0(\当前传输数据有效_输入 ), .in1(1'b0), .out(multiplexer_13_out), .sel(\同步清零_气泡_高 ));
  Register #(.width(1), .trigger("rising"), .Select("low")) register_12 (
    .D(multiplexer_12_out), .en(pull_resistor_2_node), .Q(out_29), .clk(CLK));  // open: clr
  Register #(.width(1), .trigger("rising"), .Select("low")) register_13 (
    .D(multiplexer_13_out), .en(pull_resistor_2_node), .Q(\当前传输数据有效_输出 ), .clk(CLK));  // open: clr
  Multiplexer #(.select(1), .width(4), .disabled("Z"), .enable("false")) multiplexer_14 (
    .in0(in_14), .in1(4'b0000), .out(multiplexer_14_out), .sel(\同步清零_气泡_高 ));
  Register #(.width(4), .trigger("rising"), .Select("low")) register_14 (
    .D(multiplexer_14_out), .en(pull_resistor_2_node), .Q(out_31), .clk(CLK));  // open: clr
  Pull_Resistor #(.pull(0)) pull_resistor_2 (.node(pull_resistor_2_node));
  not not_1 (pull_resistor_2_node, \使能端 );

  // Other names for the same wires on the sheet: Imm_in[31:0] = \Imm输入 ; Imm_out[31:0] = \Imm输出 ;
  //   IR_in[31:0] = \IR输入 ; IR_out[31:0] = \IR输出 ; PC_in[31:0] = \PC输入 ; PC_out[31:0] = \PC输出 ;
  //   RD1_in[31:0] = \RD1输入 ; RD1_out[31:0] = \RD1输出 ; RD2_in[31:0] = \RD2输入 ; RD2_out[31:0] = \RD2输出 
endmodule

module EX_MEM (
  input  [31:0] \IR输入 ,
  input  [31:0] \PC输入 ,
  input  [31:0] \AluRst输入 ,
  input  [31:0] \Mem输入 ,
  input  in_5,
  input  in_6,
  input  in_7,
  input  in_8,
  input  in_9,
  input  in_10,
  input  in_11,
  input  [4:0] RegWrite_in,
  input  \当前传输数据有效_输入 ,
  input  CLK,
  input  \使能端 ,
  input  \清零_气泡_高 ,
  output [31:0] \IR输出 ,
  output [31:0] \PC输出 ,
  output [31:0] \AluRst输出 ,
  output [31:0] \Mem输出 ,
  output out_21,
  output out_22,
  output out_23,
  output out_24,
  output out_25,
  output out_26,
  output out_27,
  output [4:0] RegWrite_out,
  output \当前传输数据有效_输出 
);

  wire multiplexer_5_out, multiplexer_6_out, multiplexer_7_out, multiplexer_8_out, multiplexer_9_out,
       multiplexer_10_out, multiplexer_11_out, multiplexer_13_out, pull_resistor_2_node;
  wire [4:0] multiplexer_12_out;
  wire [31:0] multiplexer_1_out, multiplexer_2_out, multiplexer_3_out, multiplexer_4_out;

  Multiplexer #(.select(1), .width(32), .disabled("Z"), .enable("false")) multiplexer_1 (
    .in0(\IR输入 ), .in1({32{1'b0}}), .out(multiplexer_1_out), .sel(\清零_气泡_高 ));
  Multiplexer #(.select(1), .width(32), .disabled("Z"), .enable("false")) multiplexer_2 (
    .in0(\PC输入 ), .in1({32{1'b0}}), .out(multiplexer_2_out), .sel(\清零_气泡_高 ));
  Multiplexer #(.select(1), .width(32), .disabled("Z"), .enable("false")) multiplexer_3 (
    .in0(\AluRst输入 ), .in1({32{1'b0}}), .out(multiplexer_3_out), .sel(\清零_气泡_高 ));
  Multiplexer #(.select(1), .width(32), .disabled("Z"), .enable("false")) multiplexer_4 (
    .in0(\Mem输入 ), .in1({32{1'b0}}), .out(multiplexer_4_out), .sel(\清零_气泡_高 ));
  Multiplexer #(.select(1), .width(1), .disabled("Z"), .enable("false")) multiplexer_5 (
    .in0(in_5), .in1(1'b0), .out(multiplexer_5_out), .sel(\清零_气泡_高 ));
  Multiplexer #(.select(1), .width(1), .disabled("Z"), .enable("false")) multiplexer_6 (
    .in0(in_6), .in1(1'b0), .out(multiplexer_6_out), .sel(\清零_气泡_高 ));
  Multiplexer #(.select(1), .width(1), .disabled("Z"), .enable("false")) multiplexer_7 (
    .in0(in_7), .in1(1'b0), .out(multiplexer_7_out), .sel(\清零_气泡_高 ));
  Multiplexer #(.select(1), .width(1), .disabled("Z"), .enable("false")) multiplexer_8 (
    .in0(in_8), .in1(1'b0), .out(multiplexer_8_out), .sel(\清零_气泡_高 ));
  Multiplexer #(.select(1), .width(1), .disabled("Z"), .enable("false")) multiplexer_9 (
    .in0(in_9), .in1(1'b0), .out(multiplexer_9_out), .sel(\清零_气泡_高 ));
  Multiplexer #(.select(1), .width(1), .disabled("Z"), .enable("false")) multiplexer_10 (
    .in0(in_10), .in1(1'b0), .out(multiplexer_10_out), .sel(\清零_气泡_高 ));
  Multiplexer #(.select(1), .width(1), .disabled("Z"), .enable("false")) multiplexer_11 (
    .in0(in_11), .in1(1'b0), .out(multiplexer_11_out), .sel(\清零_气泡_高 ));
  Multiplexer #(.select(1), .width(5), .disabled("Z"), .enable("false")) multiplexer_12 (
    .in0(RegWrite_in), .in1({5{1'b0}}), .out(multiplexer_12_out), .sel(\清零_气泡_高 ));
  Multiplexer #(.select(1), .width(1), .disabled("Z"), .enable("false")) multiplexer_13 (
    .in0(\当前传输数据有效_输入 ), .in1(1'b0), .out(multiplexer_13_out), .sel(\清零_气泡_高 ));
  Pull_Resistor #(.pull(0)) pull_resistor_1 (.node(\清零_气泡_高 ));
  Register #(.width(32), .trigger("rising"), .Select("low")) register_1 (
    .D(multiplexer_1_out), .en(pull_resistor_2_node), .Q(\IR输出 ), .clk(CLK));  // open: clr
  Register #(.width(32), .trigger("rising"), .Select("low")) register_2 (
    .D(multiplexer_2_out), .en(pull_resistor_2_node), .Q(\PC输出 ), .clk(CLK));  // open: clr
  Register #(.width(32), .trigger("rising"), .Select("low")) register_3 (
    .D(multiplexer_3_out), .en(pull_resistor_2_node), .Q(\AluRst输出 ), .clk(CLK));  // open: clr
  Register #(.width(32), .trigger("rising"), .Select("low")) register_4 (
    .D(multiplexer_4_out), .en(pull_resistor_2_node), .Q(\Mem输出 ), .clk(CLK));  // open: clr
  Register #(.width(1), .trigger("rising"), .Select("low")) register_5 (
    .D(multiplexer_5_out), .en(pull_resistor_2_node), .Q(out_21), .clk(CLK));  // open: clr
  Register #(.width(1), .trigger("rising"), .Select("low")) register_6 (
    .D(multiplexer_6_out), .en(pull_resistor_2_node), .Q(out_22), .clk(CLK));  // open: clr
  Register #(.width(1), .trigger("rising"), .Select("low")) register_7 (
    .D(multiplexer_7_out), .en(pull_resistor_2_node), .Q(out_23), .clk(CLK));  // open: clr
  Register #(.width(1), .trigger("rising"), .Select("low")) register_8 (
    .D(multiplexer_8_out), .en(pull_resistor_2_node), .Q(out_24), .clk(CLK));  // open: clr
  Register #(.width(1), .trigger("rising"), .Select("low")) register_9 (
    .D(multiplexer_9_out), .en(pull_resistor_2_node), .Q(out_25), .clk(CLK));  // open: clr
  Register #(.width(1), .trigger("rising"), .Select("low")) register_10 (
    .D(multiplexer_10_out), .en(pull_resistor_2_node), .Q(out_26), .clk(CLK));  // open: clr
  Register #(.width(1), .trigger("rising"), .Select("low")) register_11 (
    .D(multiplexer_11_out), .en(pull_resistor_2_node), .Q(out_27), .clk(CLK));  // open: clr
  Register #(.width(5), .trigger("rising"), .Select("low")) register_12 (
    .D(multiplexer_12_out), .en(pull_resistor_2_node), .Q(RegWrite_out), .clk(CLK));  // open: clr
  Register #(.width(1), .trigger("rising"), .Select("low")) register_13 (
    .D(multiplexer_13_out), .en(pull_resistor_2_node), .Q(\当前传输数据有效_输出 ), .clk(CLK));  // open: clr
  Pull_Resistor #(.pull(0)) pull_resistor_2 (.node(pull_resistor_2_node));
  not not_1 (pull_resistor_2_node, \使能端 );

  // Other names for the same wires on the sheet: AluRst_in[31:0] = \AluRst输入 ; AluRst_out[31:0] = \AluRst输出 ;
  //   IR_in[31:0] = \IR输入 ; IR_out[31:0] = \IR输出 ; Mem_in[31:0] = \Mem输入 ; Mem_out[31:0] = \Mem输出 ;
  //   PC_in[31:0] = \PC输入 ; PC_out[31:0] = \PC输出 
endmodule

module MEM_WB (
  input  [31:0] \IR输入 ,
  input  [31:0] \PC输入 ,
  input  [31:0] \Reg输入 ,
  input  [31:0] \Mem输入 ,
  input  in_5,
  input  in_6,
  input  in_7,
  input  in_8,
  input  in_9,
  input  in_10,
  input  [4:0] RegWrite_in,
  input  \当前传输数据有效_输入 ,
  input  CLK,
  input  \使能端 ,
  input  \清零_气泡_高 ,
  output [31:0] \IR输出 ,
  output [31:0] \PC输出 ,
  output [31:0] \Reg输出 ,
  output [31:0] \Mem输出 ,
  output out_20,
  output out_21,
  output out_22,
  output out_23,
  output out_24,
  output out_25,
  output [4:0] RegWrite_out,
  output \当前传输数据有效_输出 
);

  wire multiplexer_5_out, multiplexer_6_out, multiplexer_7_out, multiplexer_8_out, multiplexer_9_out,
       multiplexer_10_out, multiplexer_12_out, pull_resistor_2_node;
  wire [4:0] multiplexer_11_out;
  wire [31:0] multiplexer_1_out, multiplexer_2_out, multiplexer_3_out, multiplexer_4_out;

  Multiplexer #(.select(1), .width(32), .disabled("Z"), .enable("false")) multiplexer_1 (
    .in0(\IR输入 ), .in1({32{1'b0}}), .out(multiplexer_1_out), .sel(\清零_气泡_高 ));
  Multiplexer #(.select(1), .width(32), .disabled("Z"), .enable("false")) multiplexer_2 (
    .in0(\PC输入 ), .in1({32{1'b0}}), .out(multiplexer_2_out), .sel(\清零_气泡_高 ));
  Multiplexer #(.select(1), .width(32), .disabled("Z"), .enable("false")) multiplexer_3 (
    .in0(\Reg输入 ), .in1({32{1'b0}}), .out(multiplexer_3_out), .sel(\清零_气泡_高 ));
  Multiplexer #(.select(1), .width(32), .disabled("Z"), .enable("false")) multiplexer_4 (
    .in0(\Mem输入 ), .in1({32{1'b0}}), .out(multiplexer_4_out), .sel(\清零_气泡_高 ));
  Multiplexer #(.select(1), .width(1), .disabled("Z"), .enable("false")) multiplexer_5 (
    .in0(in_5), .in1(1'b0), .out(multiplexer_5_out), .sel(\清零_气泡_高 ));
  Multiplexer #(.select(1), .width(1), .disabled("Z"), .enable("false")) multiplexer_6 (
    .in0(in_6), .in1(1'b0), .out(multiplexer_6_out), .sel(\清零_气泡_高 ));
  Multiplexer #(.select(1), .width(1), .disabled("Z"), .enable("false")) multiplexer_7 (
    .in0(in_7), .in1(1'b0), .out(multiplexer_7_out), .sel(\清零_气泡_高 ));
  Multiplexer #(.select(1), .width(1), .disabled("Z"), .enable("false")) multiplexer_8 (
    .in0(in_8), .in1(1'b0), .out(multiplexer_8_out), .sel(\清零_气泡_高 ));
  Multiplexer #(.select(1), .width(1), .disabled("Z"), .enable("false")) multiplexer_9 (
    .in0(in_9), .in1(1'b0), .out(multiplexer_9_out), .sel(\清零_气泡_高 ));
  Multiplexer #(.select(1), .width(1), .disabled("Z"), .enable("false")) multiplexer_10 (
    .in0(in_10), .in1(1'b0), .out(multiplexer_10_out), .sel(\清零_气泡_高 ));
  Multiplexer #(.select(1), .width(5), .disabled("Z"), .enable("false")) multiplexer_11 (
    .in0(RegWrite_in), .in1({5{1'b0}}), .out(multiplexer_11_out), .sel(\清零_气泡_高 ));
  Multiplexer #(.select(1), .width(1), .disabled("Z"), .enable("false")) multiplexer_12 (
    .in0(\当前传输数据有效_输入 ), .in1(1'b0), .out(multiplexer_12_out), .sel(\清零_气泡_高 ));
  Pull_Resistor #(.pull(0)) pull_resistor_1 (.node(\清零_气泡_高 ));
  Register #(.width(32), .trigger("rising"), .Select("low")) register_1 (
    .D(multiplexer_1_out), .en(pull_resistor_2_node), .Q(\IR输出 ), .clk(CLK));  // open: clr
  Register #(.width(32), .trigger("rising"), .Select("low")) register_2 (
    .D(multiplexer_2_out), .en(pull_resistor_2_node), .Q(\PC输出 ), .clk(CLK));  // open: clr
  Register #(.width(32), .trigger("rising"), .Select("low")) register_3 (
    .D(multiplexer_3_out), .en(pull_resistor_2_node), .Q(\Reg输出 ), .clk(CLK));  // open: clr
  Register #(.width(32), .trigger("rising"), .Select("low")) register_4 (
    .D(multiplexer_4_out), .en(pull_resistor_2_node), .Q(\Mem输出 ), .clk(CLK));  // open: clr
  Register #(.width(1), .trigger("rising"), .Select("low")) register_5 (
    .D(multiplexer_5_out), .en(pull_resistor_2_node), .Q(out_20), .clk(CLK));  // open: clr
  Register #(.width(1), .trigger("rising"), .Select("low")) register_6 (
    .D(multiplexer_6_out), .en(pull_resistor_2_node), .Q(out_21), .clk(CLK));  // open: clr
  Register #(.width(1), .trigger("rising"), .Select("low")) register_7 (
    .D(multiplexer_7_out), .en(pull_resistor_2_node), .Q(out_22), .clk(CLK));  // open: clr
  Register #(.width(1), .trigger("rising"), .Select("low")) register_8 (
    .D(multiplexer_8_out), .en(pull_resistor_2_node), .Q(out_23), .clk(CLK));  // open: clr
  Register #(.width(1), .trigger("rising"), .Select("low")) register_9 (
    .D(multiplexer_9_out), .en(pull_resistor_2_node), .Q(out_24), .clk(CLK));  // open: clr
  Register #(.width(1), .trigger("rising"), .Select("low")) register_10 (
    .D(multiplexer_10_out), .en(pull_resistor_2_node), .Q(out_25), .clk(CLK));  // open: clr
  Register #(.width(5), .trigger("rising"), .Select("low")) register_11 (
    .D(multiplexer_11_out), .en(pull_resistor_2_node), .Q(RegWrite_out), .clk(CLK));  // open: clr
  Register #(.width(1), .trigger("rising"), .Select("low")) register_12 (
    .D(multiplexer_12_out), .en(pull_resistor_2_node), .Q(\当前传输数据有效_输出 ), .clk(CLK));  // open: clr
  Pull_Resistor #(.pull(0)) pull_resistor_2 (.node(pull_resistor_2_node));
  not not_1 (pull_resistor_2_node, \使能端 );

  // Other names for the same wires on the sheet: IR_in[31:0] = \IR输入 ; IR_out[31:0] = \IR输出 ; Mem_in[31:0] = \Mem输入 ;
  //   Mem_out[31:0] = \Mem输出 ; PC_in[31:0] = \PC输入 ; PC_out[31:0] = \PC输出 ; Reg_in[31:0] = \Reg输入 ;
  //   Reg_out[31:0] = \Reg输出 
endmodule

module \单周期单级中断控制器  (
  input  K1,
  input  K2,
  input  K3,
  input  CLR1,
  input  CLR2,
  input  CLR3,
  output W1,
  output W2,
  output W3
);

  wire and_1_out, and_2_out, and_3_out, CLK, d_ff_1_q, d_ff_2_q, d_ff_3_q, INT1, INT2, INT3, or_4_out,
       or_5_out, or_6_out;

  or or_1 (W1, INT1, d_ff_1_q);
  or or_2 (W2, INT2, d_ff_2_q);
  or or_3 (W3, INT3, d_ff_3_q);
  D_Flip_Flop #(.trigger("rising"), .Pre_Clr_Positions("LEGACY"), .NegatePresetClear("false"), .enable("true"), .NewFFLayout("false")) d_ff_1 (
    .clk(K1), .D(1'b1), .Q(d_ff_1_q), .reset(INT1));  // open: Qn, preset, en
  D_Flip_Flop #(.trigger("rising"), .Pre_Clr_Positions("LEGACY"), .NegatePresetClear("false"), .enable("true"), .NewFFLayout("false")) d_ff_2 (
    .clk(K2), .D(1'b1), .Q(d_ff_2_q), .reset(INT2));  // open: Qn, preset, en
  D_Flip_Flop #(.trigger("rising"), .Pre_Clr_Positions("LEGACY"), .NegatePresetClear("false"), .enable("true"), .NewFFLayout("false")) d_ff_3 (
    .clk(K3), .D(1'b1), .Q(d_ff_3_q), .reset(INT3));  // open: Qn, preset, en
  Priority_Encoder #(.select(2), .disabled("Z")) priority_encoder_1 ();  // open: in0, in1, in2, in3, out, gs, en_out, en_in
  or or_4 (or_4_out, d_ff_1_q, INT1);
  or or_5 (or_5_out, d_ff_2_q, INT2);
  or or_6 (or_6_out, d_ff_3_q, INT3);
  and and_1 (and_1_out, or_4_out, ~CLR1);  // AND_Gate
  and and_2 (and_2_out, or_5_out, ~CLR2);  // AND_Gate
  and and_3 (and_3_out, or_6_out, ~CLR3);  // AND_Gate
  D_Flip_Flop #(.trigger("rising"), .Pre_Clr_Positions("LEGACY"), .NegatePresetClear("false"), .enable("true"), .NewFFLayout("false")) IR1 (
    .clk(CLK), .D(and_1_out), .Q(INT1));  // open: Qn, preset, en, reset
  D_Flip_Flop #(.trigger("rising"), .Pre_Clr_Positions("LEGACY"), .NegatePresetClear("false"), .enable("true"), .NewFFLayout("false")) IR3 (
    .clk(CLK), .D(and_2_out), .Q(INT2));  // open: Qn, preset, en, reset
  D_Flip_Flop #(.trigger("rising"), .Pre_Clr_Positions("LEGACY"), .NegatePresetClear("false"), .enable("true"), .NewFFLayout("false")) IR3_2 (
    .clk(CLK), .D(and_3_out), .Q(INT3));  // open: Qn, preset, en, reset

  // Notes on the sheet:
  //   Reset 
  //   Reset 
  //   Reset 
endmodule

module \流水线关卡  (
  input  _1_1,
  input  _1_11,
  input  [31:0] _32_1,
  input  _1_2,
  input  _1_12,
  input  _1_3,
  input  _1_13,
  input  _1_4,
  input  _1_14,
  input  [31:0] _32_2,
  input  _1_5,
  input  _1_15,
  input  _1_6,
  input  _1_16,
  input  _1_7,
  input  _1_17,
  input  [31:0] _32_3,
  input  _1_8,
  input  _1_18,
  input  _1_9,
  input  _1_19,
  input  [31:0] _32_4,
  input  _1_10,
  input  _1_20,
  input  [1:0] _2_1,
  input  [1:0] _2_2,
  input  [31:0] _32_5,
  input  [2:0] _3_1,
  input  [4:0] _5_1,
  input  [2:0] _3_2,
  input  [4:0] _5_2,
  input  [31:0] _32_6,
  input  [3:0] _4_1,
  input  [3:0] _4_2,
  input  \同步清零 ,
  input  CLK,
  input  \使能 ,
  output _1_1_2,
  output _1_11_2,
  output [31:0] _32_1_2,
  output _1_2_2,
  output _1_12_2,
  output _1_3_2,
  output _1_13_2,
  output _1_4_2,
  output _1_14_2,
  output [31:0] _32_2_2,
  output _1_5_2,
  output _1_15_2,
  output _1_6_2,
  output _1_16_2,
  output _1_7_2,
  output _1_17_2,
  output [31:0] _32_3_2,
  output _1_8_2,
  output _1_18_2,
  output _1_9_2,
  output _1_19_2,
  output [31:0] _32_4_2,
  output _1_10_2,
  output _1_20_2,
  output [1:0] _2_1_2,
  output [1:0] _2_2_2,
  output [31:0] _32_5_2,
  output [2:0] _3_1_2,
  output [4:0] _5_1_2,
  output [2:0] _3_2_2,
  output [4:0] _5_2_2,
  output [31:0] _32_6_2,
  output [3:0] _4_1_2,
  output [3:0] _4_2_2
);

  wire multiplexer_7_out, multiplexer_8_out, multiplexer_9_out, multiplexer_10_out, multiplexer_11_out,
       multiplexer_12_out, multiplexer_13_out, multiplexer_14_out, multiplexer_15_out, multiplexer_16_out,
       multiplexer_17_out, multiplexer_18_out, multiplexer_19_out, multiplexer_20_out, multiplexer_21_out,
       multiplexer_22_out, multiplexer_23_out, multiplexer_24_out, multiplexer_25_out, multiplexer_26_out,
       not_1_out;
  wire [1:0] multiplexer_27_out, multiplexer_28_out;
  wire [2:0] multiplexer_29_out, multiplexer_30_out;
  wire [3:0] multiplexer_31_out, multiplexer_32_out;
  wire [4:0] multiplexer_33_out, multiplexer_34_out;
  wire [31:0] multiplexer_1_out, multiplexer_2_out, multiplexer_3_out, multiplexer_4_out, multiplexer_5_out,
       multiplexer_6_out;

  Multiplexer #(.select(1), .width(32), .disabled("Z"), .enable("false")) multiplexer_1 (
    .in0(_32_1), .in1({32{1'b0}}), .out(multiplexer_1_out), .sel(\同步清零 ));
  Multiplexer #(.select(1), .width(32), .disabled("Z"), .enable("false")) multiplexer_2 (
    .in0(_32_2), .in1({32{1'b0}}), .out(multiplexer_2_out), .sel(\同步清零 ));
  Multiplexer #(.select(1), .width(32), .disabled("Z"), .enable("false")) multiplexer_3 (
    .in0(_32_3), .in1({32{1'b0}}), .out(multiplexer_3_out), .sel(\同步清零 ));
  Multiplexer #(.select(1), .width(32), .disabled("Z"), .enable("false")) multiplexer_4 (
    .in0(_32_4), .in1({32{1'b0}}), .out(multiplexer_4_out), .sel(\同步清零 ));
  Multiplexer #(.select(1), .width(32), .disabled("Z"), .enable("false")) multiplexer_5 (
    .in0(_32_5), .in1({32{1'b0}}), .out(multiplexer_5_out), .sel(\同步清零 ));
  Multiplexer #(.select(1), .width(32), .disabled("Z"), .enable("false")) multiplexer_6 (
    .in0(_32_6), .in1({32{1'b0}}), .out(multiplexer_6_out), .sel(\同步清零 ));
  Multiplexer #(.select(1), .width(1), .disabled("Z"), .enable("false")) multiplexer_7 (
    .in0(_1_1), .in1(1'b0), .out(multiplexer_7_out), .sel(\同步清零 ));
  Multiplexer #(.select(1), .width(1), .disabled("Z"), .enable("false")) multiplexer_8 (
    .in0(_1_2), .in1(1'b0), .out(multiplexer_8_out), .sel(\同步清零 ));
  Multiplexer #(.select(1), .width(1), .disabled("Z"), .enable("false")) multiplexer_9 (
    .in0(_1_3), .in1(1'b0), .out(multiplexer_9_out), .sel(\同步清零 ));
  Multiplexer #(.select(1), .width(1), .disabled("Z"), .enable("false")) multiplexer_10 (
    .in0(_1_4), .in1(1'b0), .out(multiplexer_10_out), .sel(\同步清零 ));
  Multiplexer #(.select(1), .width(1), .disabled("Z"), .enable("false")) multiplexer_11 (
    .in0(_1_5), .in1(1'b0), .out(multiplexer_11_out), .sel(\同步清零 ));
  Multiplexer #(.select(1), .width(1), .disabled("Z"), .enable("false")) multiplexer_12 (
    .in0(_1_6), .in1(1'b0), .out(multiplexer_12_out), .sel(\同步清零 ));
  Multiplexer #(.select(1), .width(1), .disabled("Z"), .enable("false")) multiplexer_13 (
    .in0(_1_7), .in1(1'b0), .out(multiplexer_13_out), .sel(\同步清零 ));
  Multiplexer #(.select(1), .width(1), .disabled("Z"), .enable("false")) multiplexer_14 (
    .in0(_1_8), .in1(1'b0), .out(multiplexer_14_out), .sel(\同步清零 ));
  Multiplexer #(.select(1), .width(1), .disabled("Z"), .enable("false")) multiplexer_15 (
    .in0(_1_9), .in1(1'b0), .out(multiplexer_15_out), .sel(\同步清零 ));
  Multiplexer #(.select(1), .width(1), .disabled("Z"), .enable("false")) multiplexer_16 (
    .in0(_1_10), .in1(1'b0), .out(multiplexer_16_out), .sel(\同步清零 ));
  Multiplexer #(.select(1), .width(1), .disabled("Z"), .enable("false")) multiplexer_17 (
    .in0(_1_11), .in1(1'b0), .out(multiplexer_17_out), .sel(\同步清零 ));
  Multiplexer #(.select(1), .width(1), .disabled("Z"), .enable("false")) multiplexer_18 (
    .in0(_1_12), .in1(1'b0), .out(multiplexer_18_out), .sel(\同步清零 ));
  Multiplexer #(.select(1), .width(1), .disabled("Z"), .enable("false")) multiplexer_19 (
    .in0(_1_13), .in1(1'b0), .out(multiplexer_19_out), .sel(\同步清零 ));
  Multiplexer #(.select(1), .width(1), .disabled("Z"), .enable("false")) multiplexer_20 (
    .in0(_1_14), .in1(1'b0), .out(multiplexer_20_out), .sel(\同步清零 ));
  Multiplexer #(.select(1), .width(1), .disabled("Z"), .enable("false")) multiplexer_21 (
    .in0(_1_15), .in1(1'b0), .out(multiplexer_21_out), .sel(\同步清零 ));
  Multiplexer #(.select(1), .width(1), .disabled("Z"), .enable("false")) multiplexer_22 (
    .in0(_1_16), .in1(1'b0), .out(multiplexer_22_out), .sel(\同步清零 ));
  Multiplexer #(.select(1), .width(1), .disabled("Z"), .enable("false")) multiplexer_23 (
    .in0(_1_17), .in1(1'b0), .out(multiplexer_23_out), .sel(\同步清零 ));
  Multiplexer #(.select(1), .width(1), .disabled("Z"), .enable("false")) multiplexer_24 (
    .in0(_1_18), .in1(1'b0), .out(multiplexer_24_out), .sel(\同步清零 ));
  Multiplexer #(.select(1), .width(1), .disabled("Z"), .enable("false")) multiplexer_25 (
    .in0(_1_19), .in1(1'b0), .out(multiplexer_25_out), .sel(\同步清零 ));
  Multiplexer #(.select(1), .width(1), .disabled("Z"), .enable("false")) multiplexer_26 (
    .in0(_1_20), .in1(1'b0), .out(multiplexer_26_out), .sel(\同步清零 ));
  Multiplexer #(.select(1), .width(2), .disabled("Z"), .enable("false")) multiplexer_27 (
    .in0(_2_1), .in1(2'b00), .out(multiplexer_27_out), .sel(\同步清零 ));
  Multiplexer #(.select(1), .width(2), .disabled("Z"), .enable("false")) multiplexer_28 (
    .in0(_2_2), .in1(2'b00), .out(multiplexer_28_out), .sel(\同步清零 ));
  Multiplexer #(.select(1), .width(3), .disabled("Z"), .enable("false")) multiplexer_29 (
    .in0(_3_1), .in1(3'b000), .out(multiplexer_29_out), .sel(\同步清零 ));
  Multiplexer #(.select(1), .width(3), .disabled("Z"), .enable("false")) multiplexer_30 (
    .in0(_3_2), .in1(3'b000), .out(multiplexer_30_out), .sel(\同步清零 ));
  Multiplexer #(.select(1), .width(4), .disabled("Z"), .enable("false")) multiplexer_31 (
    .in0(_4_1), .in1(4'b0000), .out(multiplexer_31_out), .sel(\同步清零 ));
  Multiplexer #(.select(1), .width(4), .disabled("Z"), .enable("false")) multiplexer_32 (
    .in0(_4_2), .in1(4'b0000), .out(multiplexer_32_out), .sel(\同步清零 ));
  Multiplexer #(.select(1), .width(5), .disabled("Z"), .enable("false")) multiplexer_33 (
    .in0(_5_1), .in1({5{1'b0}}), .out(multiplexer_33_out), .sel(\同步清零 ));
  Multiplexer #(.select(1), .width(5), .disabled("Z"), .enable("false")) multiplexer_34 (
    .in0(_5_2), .in1({5{1'b0}}), .out(multiplexer_34_out), .sel(\同步清零 ));
  Pull_Resistor #(.pull(0)) pull_resistor_1 (.node(\同步清零 ));
  not not_1 (not_1_out, \使能 );
  Register #(.width(32), .trigger("rising"), .Select("low")) register_1 (
    .D(multiplexer_1_out), .en(not_1_out), .Q(_32_1_2), .clk(CLK));  // open: clr
  Register #(.width(32), .trigger("rising"), .Select("low")) register_2 (
    .D(multiplexer_2_out), .en(not_1_out), .Q(_32_2_2), .clk(CLK));  // open: clr
  Register #(.width(32), .trigger("rising"), .Select("low")) register_3 (
    .D(multiplexer_3_out), .en(not_1_out), .Q(_32_3_2), .clk(CLK));  // open: clr
  Register #(.width(32), .trigger("rising"), .Select("low")) register_4 (
    .D(multiplexer_4_out), .en(not_1_out), .Q(_32_4_2), .clk(CLK));  // open: clr
  Register #(.width(32), .trigger("rising"), .Select("low")) register_5 (
    .D(multiplexer_5_out), .en(not_1_out), .Q(_32_5_2), .clk(CLK));  // open: clr
  Register #(.width(32), .trigger("rising"), .Select("low")) register_6 (
    .D(multiplexer_6_out), .en(not_1_out), .Q(_32_6_2), .clk(CLK));  // open: clr
  Register #(.width(1), .trigger("rising"), .Select("low")) register_7 (
    .D(multiplexer_7_out), .en(not_1_out), .Q(_1_1_2), .clk(CLK));  // open: clr
  Register #(.width(1), .trigger("rising"), .Select("low")) register_8 (
    .D(multiplexer_8_out), .en(not_1_out), .Q(_1_2_2), .clk(CLK));  // open: clr
  Register #(.width(1), .trigger("rising"), .Select("low")) register_9 (
    .D(multiplexer_9_out), .en(not_1_out), .Q(_1_3_2), .clk(CLK));  // open: clr
  Register #(.width(1), .trigger("rising"), .Select("low")) register_10 (
    .D(multiplexer_10_out), .en(not_1_out), .Q(_1_4_2), .clk(CLK));  // open: clr
  Register #(.width(1), .trigger("rising"), .Select("low")) register_11 (
    .D(multiplexer_11_out), .en(not_1_out), .Q(_1_5_2), .clk(CLK));  // open: clr
  Register #(.width(1), .trigger("rising"), .Select("low")) register_12 (
    .D(multiplexer_12_out), .en(not_1_out), .Q(_1_6_2), .clk(CLK));  // open: clr
  Register #(.width(1), .trigger("rising"), .Select("low")) register_13 (
    .D(multiplexer_13_out), .en(not_1_out), .Q(_1_7_2), .clk(CLK));  // open: clr
  Register #(.width(1), .trigger("rising"), .Select("low")) register_14 (
    .D(multiplexer_14_out), .en(not_1_out), .Q(_1_8_2), .clk(CLK));  // open: clr
  Register #(.width(1), .trigger("rising"), .Select("low")) register_15 (
    .D(multiplexer_15_out), .en(not_1_out), .Q(_1_9_2), .clk(CLK));  // open: clr
  Register #(.width(1), .trigger("rising"), .Select("low")) register_16 (
    .D(multiplexer_16_out), .en(not_1_out), .Q(_1_10_2), .clk(CLK));  // open: clr
  Register #(.width(1), .trigger("rising"), .Select("low")) register_17 (
    .D(multiplexer_17_out), .en(not_1_out), .Q(_1_11_2), .clk(CLK));  // open: clr
  Register #(.width(1), .trigger("rising"), .Select("low")) register_18 (
    .D(multiplexer_18_out), .en(not_1_out), .Q(_1_12_2), .clk(CLK));  // open: clr
  Register #(.width(1), .trigger("rising"), .Select("low")) register_19 (
    .D(multiplexer_19_out), .en(not_1_out), .Q(_1_13_2), .clk(CLK));  // open: clr
  Register #(.width(1), .trigger("rising"), .Select("low")) register_20 (
    .D(multiplexer_20_out), .en(not_1_out), .Q(_1_14_2), .clk(CLK));  // open: clr
  Register #(.width(1), .trigger("rising"), .Select("low")) register_21 (
    .D(multiplexer_21_out), .en(not_1_out), .Q(_1_15_2), .clk(CLK));  // open: clr
  Register #(.width(1), .trigger("rising"), .Select("low")) register_22 (
    .D(multiplexer_22_out), .en(not_1_out), .Q(_1_16_2), .clk(CLK));  // open: clr
  Register #(.width(1), .trigger("rising"), .Select("low")) register_23 (
    .D(multiplexer_23_out), .en(not_1_out), .Q(_1_17_2), .clk(CLK));  // open: clr
  Register #(.width(1), .trigger("rising"), .Select("low")) register_24 (
    .D(multiplexer_24_out), .en(not_1_out), .Q(_1_18_2), .clk(CLK));  // open: clr
  Register #(.width(1), .trigger("rising"), .Select("low")) register_25 (
    .D(multiplexer_25_out), .en(not_1_out), .Q(_1_19_2), .clk(CLK));  // open: clr
  Register #(.width(1), .trigger("rising"), .Select("low")) register_26 (
    .D(multiplexer_26_out), .en(not_1_out), .Q(_1_20_2), .clk(CLK));  // open: clr
  Register #(.width(2), .trigger("rising"), .Select("low")) register_27 (
    .D(multiplexer_27_out), .en(not_1_out), .Q(_2_1_2), .clk(CLK));  // open: clr
  Register #(.width(2), .trigger("rising"), .Select("low")) register_28 (
    .D(multiplexer_28_out), .en(not_1_out), .Q(_2_2_2), .clk(CLK));  // open: clr
  Register #(.width(3), .trigger("rising"), .Select("low")) register_29 (
    .D(multiplexer_29_out), .en(not_1_out), .Q(_3_1_2), .clk(CLK));  // open: clr
  Register #(.width(3), .trigger("rising"), .Select("low")) register_30 (
    .D(multiplexer_30_out), .en(not_1_out), .Q(_3_2_2), .clk(CLK));  // open: clr
  Register #(.width(4), .trigger("rising"), .Select("low")) register_31 (
    .D(multiplexer_31_out), .en(not_1_out), .Q(_4_1_2), .clk(CLK));  // open: clr
  Register #(.width(4), .trigger("rising"), .Select("low")) register_32 (
    .D(multiplexer_32_out), .en(not_1_out), .Q(_4_2_2), .clk(CLK));  // open: clr
  Register #(.width(5), .trigger("rising"), .Select("low")) register_33 (
    .D(multiplexer_33_out), .en(not_1_out), .Q(_5_1_2), .clk(CLK));  // open: clr
  Register #(.width(5), .trigger("rising"), .Select("low")) register_34 (
    .D(multiplexer_34_out), .en(not_1_out), .Q(_5_2_2), .clk(CLK));  // open: clr
  Pull_Resistor #(.pull(0)) pull_resistor_2 (.node(not_1_out));

  // Other names for the same wires on the sheet: _1_1_o = _1_1_2; _1_2_o = _1_2_2; _1_3_o = _1_3_2; _1_4_o = _1_4_2;
  //   _1_5_o = _1_5_2; _1_6_o = _1_6_2; _1_7_o = _1_7_2; _1_8_o = _1_8_2; _1_9_o = _1_9_2; _1_10_o = _1_10_2;
  //   _1_11_o = _1_11_2; _1_12_o = _1_12_2; _1_13_o = _1_13_2; _1_14_o = _1_14_2; _1_15_o = _1_15_2;
  //   _1_16_o = _1_16_2; _1_17_o = _1_17_2; _1_18_o = _1_18_2; _1_19_o = _1_19_2; _1_20_o = _1_20_2;
  //   _2_1_o[1:0] = _2_1_2; _2_2_o[1:0] = _2_2_2; _3_1_o[2:0] = _3_1_2; _3_2_o[2:0] = _3_2_2; _4_1_o[3:0] = _4_1_2;
  //   _4_2_o[3:0] = _4_2_2; _5_1_o[4:0] = _5_1_2; _5_2_o[4:0] = _5_2_2; _32_1_o[31:0] = _32_1_2;
  //   _32_2_o[31:0] = _32_2_2; _32_3_o[31:0] = _32_3_2; _32_4_o[31:0] = _32_4_2; _32_5_o[31:0] = _32_5_2;
  //   _32_6_o[31:0] = _32_6_2
endmodule

module \源寄存器使用  (
  input  OP0,
  input  OP1,
  input  OP2,
  input  OP3,
  input  OP4,
  input  OP5,
  input  F0,
  input  F1,
  input  F2,
  input  F3,
  input  F4,
  input  F5,
  output R1_Used,
  output R2_Used
);

  wire and_1_out, and_2_out, and_3_out, and_4_out, and_5_out, and_6_out, and_7_out, and_8_out, and_9_out,
       and_10_out, and_11_out, and_12_out, and_13_out, and_14_out, and_15_out, and_16_out, and_17_out,
       and_18_out, and_19_out, and_20_out, and_21_out, and_22_out, and_23_out, and_24_out, and_25_out,
       and_26_out, and_27_out, and_28_out, and_29_out, and_30_out, and_31_out, and_32_out, and_33_out,
       and_34_out, and_35_out, and_36_out, and_37_out, and_38_out, and_39_out, and_40_out, not_1_out,
       not_2_out, not_3_out, not_4_out, not_5_out, not_6_out, not_7_out, not_8_out, not_9_out, not_10_out,
       not_11_out, not_12_out, not_13_out, not_14_out, not_15_out, not_16_out, not_17_out, not_18_out,
       not_19_out, not_20_out, not_21_out, not_22_out, not_23_out, not_24_out, not_25_out, not_26_out,
       not_27_out, not_28_out, not_29_out, not_30_out, not_31_out, not_32_out, not_33_out, not_34_out,
       not_35_out, not_36_out, not_37_out, not_38_out, not_39_out, not_40_out, not_41_out, not_42_out,
       not_43_out, not_44_out, not_45_out, not_46_out, not_47_out, not_48_out, not_49_out, not_50_out,
       not_51_out, not_52_out, not_53_out, not_54_out, not_55_out, not_56_out, not_57_out, not_58_out,
       not_59_out, not_60_out, not_61_out, not_62_out, not_63_out, not_64_out, not_65_out, not_66_out,
       not_67_out, not_68_out, not_69_out, not_70_out, not_71_out, not_72_out, not_73_out, not_74_out,
       not_75_out, not_76_out, not_77_out, not_78_out, not_79_out, not_80_out, not_81_out, not_82_out,
       not_83_out, not_84_out, not_85_out, not_86_out, not_87_out, not_88_out, not_89_out, not_90_out,
       not_91_out, not_92_out, not_93_out, not_94_out, not_95_out, not_96_out, not_97_out, not_98_out,
       not_99_out, not_100_out, not_101_out, not_102_out, not_103_out, not_104_out, not_105_out, not_106_out,
       not_107_out, not_108_out, not_109_out, not_110_out, not_111_out, not_112_out, not_113_out,
       not_114_out, not_115_out, not_116_out, not_117_out, not_118_out, not_119_out, not_120_out,
       not_121_out, not_122_out, not_123_out, not_124_out, not_125_out, not_126_out, not_127_out,
       not_128_out, not_129_out, not_130_out, not_131_out, not_132_out, not_133_out, not_134_out,
       not_135_out, not_136_out, not_137_out, not_138_out, not_139_out, not_140_out, not_141_out,
       not_142_out, not_143_out, not_144_out, not_145_out, not_146_out, not_147_out, not_148_out,
       not_149_out, not_150_out, not_151_out, not_152_out, not_153_out, not_154_out, not_155_out,
       not_156_out, not_157_out, not_158_out, not_159_out, not_160_out, not_161_out, not_162_out,
       not_163_out, not_164_out, not_165_out, not_166_out, not_167_out, not_168_out, not_169_out,
       not_170_out, not_171_out, not_172_out, not_173_out, not_174_out, not_175_out, not_176_out,
       not_177_out, not_178_out, not_179_out, not_180_out, not_181_out, not_182_out, not_183_out,
       not_184_out, not_185_out, not_186_out, not_187_out, not_188_out, not_189_out, not_190_out,
       not_191_out, not_192_out, not_193_out, not_194_out, not_195_out, not_196_out, not_197_out,
       not_198_out, not_199_out, not_200_out, not_201_out, not_202_out, not_203_out, not_204_out,
       not_205_out, not_206_out, not_207_out, not_208_out, not_209_out, not_210_out, not_211_out,
       not_212_out, not_213_out, not_214_out, not_215_out, not_216_out, not_217_out, not_218_out,
       not_219_out, not_220_out, not_221_out, not_222_out, not_223_out, not_224_out, not_225_out,
       not_226_out, not_227_out, not_228_out, not_229_out, not_230_out, not_231_out, not_232_out,
       not_233_out, not_234_out, not_235_out, not_236_out, not_237_out, not_238_out, not_239_out,
       not_240_out, not_241_out, not_242_out, not_243_out, not_244_out, not_245_out, not_246_out,
       not_247_out, not_248_out, not_249_out, not_250_out, not_251_out, not_252_out, not_253_out,
       not_254_out, not_255_out, not_256_out, not_257_out, not_258_out, not_259_out, not_260_out,
       not_261_out, not_262_out, not_263_out, not_264_out, not_265_out, not_266_out, not_267_out,
       not_268_out, not_269_out, not_270_out, not_271_out, not_272_out, not_273_out, not_274_out,
       not_275_out, not_276_out, not_277_out, not_278_out, not_279_out, not_280_out, not_281_out,
       not_282_out, not_283_out, not_284_out, not_285_out, not_286_out, not_287_out, not_288_out,
       not_289_out, not_290_out, not_291_out, not_292_out;

  not not_1 (not_1_out, OP5);
  not not_2 (not_2_out, OP4);
  not not_3 (not_3_out, OP3);
  not not_4 (not_4_out, OP2);
  not not_5 (not_5_out, OP1);
  not not_6 (not_6_out, OP0);
  not not_7 (not_7_out, F4);
  not not_8 (not_8_out, F3);
  not not_9 (not_9_out, F2);
  not not_10 (not_10_out, F1);
  not not_11 (not_11_out, F0);
  not not_12 (not_12_out, OP5);
  not not_13 (not_13_out, OP4);
  not not_14 (not_14_out, OP3);
  not not_15 (not_15_out, OP2);
  not not_16 (not_16_out, OP1);
  not not_17 (not_17_out, OP0);
  not not_18 (not_18_out, F4);
  not not_19 (not_19_out, F3);
  not not_20 (not_20_out, F2);
  not not_21 (not_21_out, F1);
  not not_22 (not_22_out, OP5);
  not not_23 (not_23_out, OP4);
  not not_24 (not_24_out, OP3);
  not not_25 (not_25_out, OP2);
  not not_26 (not_26_out, OP1);
  not not_27 (not_27_out, OP0);
  not not_28 (not_28_out, F4);
  not not_29 (not_29_out, F3);
  not not_30 (not_30_out, F2);
  not not_31 (not_31_out, F0);
  not not_32 (not_32_out, OP5);
  not not_33 (not_33_out, OP4);
  not not_34 (not_34_out, OP3);
  not not_35 (not_35_out, OP2);
  not not_36 (not_36_out, OP1);
  not not_37 (not_37_out, OP0);
  not not_38 (not_38_out, F4);
  not not_39 (not_39_out, F3);
  not not_40 (not_40_out, F1);
  not not_41 (not_41_out, F0);
  not not_42 (not_42_out, OP5);
  not not_43 (not_43_out, OP4);
  not not_44 (not_44_out, OP3);
  not not_45 (not_45_out, OP2);
  not not_46 (not_46_out, OP1);
  not not_47 (not_47_out, OP0);
  not not_48 (not_48_out, F4);
  not not_49 (not_49_out, F3);
  not not_50 (not_50_out, F1);
  not not_51 (not_51_out, OP5);
  not not_52 (not_52_out, OP4);
  not not_53 (not_53_out, OP3);
  not not_54 (not_54_out, OP2);
  not not_55 (not_55_out, OP1);
  not not_56 (not_56_out, OP0);
  not not_57 (not_57_out, F4);
  not not_58 (not_58_out, F3);
  not not_59 (not_59_out, OP5);
  not not_60 (not_60_out, OP4);
  not not_61 (not_61_out, OP3);
  not not_62 (not_62_out, OP2);
  not not_63 (not_63_out, OP1);
  not not_64 (not_64_out, OP0);
  not not_65 (not_65_out, F4);
  not not_66 (not_66_out, F2);
  not not_67 (not_67_out, F0);
  not not_68 (not_68_out, OP5);
  not not_69 (not_69_out, OP4);
  not not_70 (not_70_out, OP3);
  not not_71 (not_71_out, OP2);
  not not_72 (not_72_out, OP1);
  not not_73 (not_73_out, OP0);
  not not_74 (not_74_out, F4);
  not not_75 (not_75_out, F2);
  not not_76 (not_76_out, OP5);
  not not_77 (not_77_out, OP4);
  not not_78 (not_78_out, OP3);
  not not_79 (not_79_out, OP2);
  not not_80 (not_80_out, OP1);
  not not_81 (not_81_out, OP0);
  not not_82 (not_82_out, F5);
  not not_83 (not_83_out, F4);
  not not_84 (not_84_out, F2);
  not not_85 (not_85_out, F1);
  not not_86 (not_86_out, F0);
  not not_87 (not_87_out, OP5);
  not not_88 (not_88_out, OP4);
  not not_89 (not_89_out, OP3);
  not not_90 (not_90_out, OP2);
  not not_91 (not_91_out, OP1);
  not not_92 (not_92_out, OP0);
  not not_93 (not_93_out, F5);
  not not_94 (not_94_out, F4);
  not not_95 (not_95_out, F1);
  not not_96 (not_96_out, F0);
  not not_97 (not_97_out, OP5);
  not not_98 (not_98_out, OP4);
  not not_99 (not_99_out, OP3);
  not not_100 (not_100_out, OP1);
  not not_101 (not_101_out, OP0);
  not not_102 (not_102_out, OP5);
  not not_103 (not_103_out, OP4);
  not not_104 (not_104_out, OP3);
  not not_105 (not_105_out, OP1);
  not not_106 (not_106_out, OP5);
  not not_107 (not_107_out, OP4);
  not not_108 (not_108_out, OP2);
  not not_109 (not_109_out, OP1);
  not not_110 (not_110_out, OP0);
  not not_111 (not_111_out, OP5);
  not not_112 (not_112_out, OP4);
  not not_113 (not_113_out, OP1);
  not not_114 (not_114_out, OP0);
  not not_115 (not_115_out, OP5);
  not not_116 (not_116_out, OP4);
  not not_117 (not_117_out, OP2);
  not not_118 (not_118_out, OP1);
  not not_119 (not_119_out, OP5);
  not not_120 (not_120_out, OP4);
  not not_121 (not_121_out, OP2);
  not not_122 (not_122_out, OP0);
  not not_123 (not_123_out, OP5);
  not not_124 (not_124_out, OP4);
  not not_125 (not_125_out, OP1);
  not not_126 (not_126_out, OP4);
  not not_127 (not_127_out, OP3);
  not not_128 (not_128_out, OP2);
  not not_129 (not_129_out, OP4);
  not not_130 (not_130_out, OP2);
  not not_131 (not_131_out, OP5);
  not not_132 (not_132_out, OP4);
  not not_133 (not_133_out, OP3);
  not not_134 (not_134_out, OP2);
  not not_135 (not_135_out, OP1);
  not not_136 (not_136_out, OP0);
  not not_137 (not_137_out, F4);
  not not_138 (not_138_out, F3);
  not not_139 (not_139_out, F0);
  not not_140 (not_140_out, OP5);
  not not_141 (not_141_out, OP4);
  not not_142 (not_142_out, OP2);
  not not_143 (not_143_out, OP4);
  not not_144 (not_144_out, OP3);
  not not_145 (not_145_out, OP1);
  not not_146 (not_146_out, OP0);
  not not_147 (not_147_out, OP5);
  not not_148 (not_148_out, OP4);
  not not_149 (not_149_out, OP3);
  not not_150 (not_150_out, OP0);
  not not_151 (not_151_out, OP5);
  not not_152 (not_152_out, OP4);
  not not_153 (not_153_out, OP3);
  not not_154 (not_154_out, OP2);
  not not_155 (not_155_out, OP1);
  not not_156 (not_156_out, OP0);
  not not_157 (not_157_out, F5);
  not not_158 (not_158_out, F4);
  not not_159 (not_159_out, F3);
  not not_160 (not_160_out, F2);
  not not_161 (not_161_out, F1);
  not not_162 (not_162_out, F0);
  not not_163 (not_163_out, OP5);
  not not_164 (not_164_out, OP4);
  not not_165 (not_165_out, OP3);
  not not_166 (not_166_out, OP2);
  not not_167 (not_167_out, OP1);
  not not_168 (not_168_out, OP0);
  not not_169 (not_169_out, F5);
  not not_170 (not_170_out, F4);
  not not_171 (not_171_out, F3);
  not not_172 (not_172_out, F2);
  not not_173 (not_173_out, OP5);
  not not_174 (not_174_out, OP4);
  not not_175 (not_175_out, OP3);
  not not_176 (not_176_out, OP2);
  not not_177 (not_177_out, OP1);
  not not_178 (not_178_out, OP0);
  not not_179 (not_179_out, F5);
  not not_180 (not_180_out, F4);
  not not_181 (not_181_out, F3);
  not not_182 (not_182_out, F2);
  not not_183 (not_183_out, F0);
  not not_184 (not_184_out, OP5);
  not not_185 (not_185_out, OP4);
  not not_186 (not_186_out, OP3);
  not not_187 (not_187_out, OP2);
  not not_188 (not_188_out, OP1);
  not not_189 (not_189_out, OP0);
  not not_190 (not_190_out, F4);
  not not_191 (not_191_out, F3);
  not not_192 (not_192_out, F2);
  not not_193 (not_193_out, F1);
  not not_194 (not_194_out, F0);
  not not_195 (not_195_out, OP5);
  not not_196 (not_196_out, OP4);
  not not_197 (not_197_out, OP3);
  not not_198 (not_198_out, OP2);
  not not_199 (not_199_out, OP1);
  not not_200 (not_200_out, OP0);
  not not_201 (not_201_out, F4);
  not not_202 (not_202_out, F3);
  not not_203 (not_203_out, F2);
  not not_204 (not_204_out, F1);
  not not_205 (not_205_out, OP5);
  not not_206 (not_206_out, OP4);
  not not_207 (not_207_out, OP3);
  not not_208 (not_208_out, OP2);
  not not_209 (not_209_out, OP1);
  not not_210 (not_210_out, OP0);
  not not_211 (not_211_out, F4);
  not not_212 (not_212_out, F3);
  not not_213 (not_213_out, F2);
  not not_214 (not_214_out, F0);
  not not_215 (not_215_out, OP5);
  not not_216 (not_216_out, OP4);
  not not_217 (not_217_out, OP3);
  not not_218 (not_218_out, OP2);
  not not_219 (not_219_out, OP1);
  not not_220 (not_220_out, OP0);
  not not_221 (not_221_out, F4);
  not not_222 (not_222_out, F3);
  not not_223 (not_223_out, F1);
  not not_224 (not_224_out, F0);
  not not_225 (not_225_out, OP5);
  not not_226 (not_226_out, OP4);
  not not_227 (not_227_out, OP3);
  not not_228 (not_228_out, OP2);
  not not_229 (not_229_out, OP1);
  not not_230 (not_230_out, OP0);
  not not_231 (not_231_out, F4);
  not not_232 (not_232_out, F3);
  not not_233 (not_233_out, F1);
  not not_234 (not_234_out, OP5);
  not not_235 (not_235_out, OP4);
  not not_236 (not_236_out, OP3);
  not not_237 (not_237_out, OP2);
  not not_238 (not_238_out, OP1);
  not not_239 (not_239_out, OP0);
  not not_240 (not_240_out, F4);
  not not_241 (not_241_out, F3);
  not not_242 (not_242_out, OP5);
  not not_243 (not_243_out, OP4);
  not not_244 (not_244_out, OP3);
  not not_245 (not_245_out, OP2);
  not not_246 (not_246_out, OP1);
  not not_247 (not_247_out, OP0);
  not not_248 (not_248_out, F4);
  not not_249 (not_249_out, F2);
  not not_250 (not_250_out, F0);
  not not_251 (not_251_out, OP5);
  not not_252 (not_252_out, OP4);
  not not_253 (not_253_out, OP3);
  not not_254 (not_254_out, OP2);
  not not_255 (not_255_out, OP1);
  not not_256 (not_256_out, OP0);
  not not_257 (not_257_out, F4);
  not not_258 (not_258_out, F2);
  not not_259 (not_259_out, OP5);
  not not_260 (not_260_out, OP4);
  not not_261 (not_261_out, OP3);
  not not_262 (not_262_out, OP2);
  not not_263 (not_263_out, OP1);
  not not_264 (not_264_out, OP0);
  not not_265 (not_265_out, F5);
  not not_266 (not_266_out, F4);
  not not_267 (not_267_out, F1);
  not not_268 (not_268_out, F0);
  not not_269 (not_269_out, OP5);
  not not_270 (not_270_out, OP4);
  not not_271 (not_271_out, OP3);
  not not_272 (not_272_out, OP1);
  not not_273 (not_273_out, OP0);
  not not_274 (not_274_out, OP5);
  not not_275 (not_275_out, OP4);
  not not_276 (not_276_out, OP3);
  not not_277 (not_277_out, OP1);
  not not_278 (not_278_out, OP4);
  not not_279 (not_279_out, OP2);
  not not_280 (not_280_out, OP5);
  not not_281 (not_281_out, OP4);
  not not_282 (not_282_out, OP3);
  not not_283 (not_283_out, OP2);
  not not_284 (not_284_out, OP1);
  not not_285 (not_285_out, OP0);
  not not_286 (not_286_out, F4);
  not not_287 (not_287_out, F3);
  not not_288 (not_288_out, F0);
  not not_289 (not_289_out, OP5);
  not not_290 (not_290_out, OP4);
  not not_291 (not_291_out, OP3);
  not not_292 (not_292_out, OP0);
  and and_1 (and_1_out, not_1_out, not_2_out, not_3_out, not_4_out, not_5_out, not_6_out, F5, not_7_out, not_8_out, not_9_out, not_10_out, not_11_out);
  and and_2 (and_2_out, not_12_out, not_13_out, not_14_out, not_15_out, not_16_out, not_17_out, F5, not_18_out, not_19_out, not_20_out, not_21_out, F0);
  and and_3 (and_3_out, not_22_out, not_23_out, not_24_out, not_25_out, not_26_out, not_27_out, F5, not_28_out, not_29_out, not_30_out, F1, not_31_out);
  and and_4 (and_4_out, not_32_out, not_33_out, not_34_out, not_35_out, not_36_out, not_37_out, F5, not_38_out, not_39_out, F2, not_40_out, not_41_out);
  and and_5 (and_5_out, not_42_out, not_43_out, not_44_out, not_45_out, not_46_out, not_47_out, F5, not_48_out, not_49_out, F2, not_50_out, F0);
  and and_6 (and_6_out, not_51_out, not_52_out, not_53_out, not_54_out, not_55_out, not_56_out, F5, not_57_out, not_58_out, F2, F1, F0);
  and and_7 (and_7_out, not_59_out, not_60_out, not_61_out, not_62_out, not_63_out, not_64_out, F5, not_65_out, F3, not_66_out, F1, not_67_out);
  and and_8 (and_8_out, not_68_out, not_69_out, not_70_out, not_71_out, not_72_out, not_73_out, F5, not_74_out, F3, not_75_out, F1, F0);
  and and_9 (and_9_out, not_76_out, not_77_out, not_78_out, not_79_out, not_80_out, not_81_out, not_82_out, not_83_out, F3, not_84_out, not_85_out, not_86_out);
  and and_10 (and_10_out, not_87_out, not_88_out, not_89_out, not_90_out, not_91_out, not_92_out, not_93_out, not_94_out, F3, F2, not_95_out, not_96_out);
  and and_11 (and_11_out, not_97_out, not_98_out, not_99_out, OP2, not_100_out, not_101_out);
  and and_12 (and_12_out, not_102_out, not_103_out, not_104_out, OP2, not_105_out, OP0);
  and and_13 (and_13_out, not_106_out, not_107_out, OP3, not_108_out, not_109_out, not_110_out);
  and and_14 (and_14_out, not_111_out, not_112_out, OP3, OP2, not_113_out, not_114_out);
  and and_15 (and_15_out, not_115_out, not_116_out, OP3, not_117_out, not_118_out, OP0);
  and and_16 (and_16_out, not_119_out, not_120_out, OP3, not_121_out, OP1, not_122_out);
  and and_17 (and_17_out, not_123_out, not_124_out, OP3, OP2, not_125_out, OP0);
  and and_18 (and_18_out, OP5, not_126_out, not_127_out, not_128_out, OP1, OP0);
  and and_19 (and_19_out, OP5, not_129_out, OP3, not_130_out, OP1, OP0);
  and and_20 (and_20_out, not_131_out, not_132_out, not_133_out, not_134_out, not_135_out, not_136_out, F5, not_137_out, not_138_out, F2, F1, not_139_out);
  and and_21 (and_21_out, not_140_out, not_141_out, OP3, not_142_out, OP1, OP0);
  and and_22 (and_22_out, OP5, not_143_out, not_144_out, OP2, not_145_out, not_146_out);
  and and_23 (and_23_out, not_147_out, not_148_out, not_149_out, OP2, OP1, not_150_out);
  and and_24 (and_24_out, not_151_out, not_152_out, not_153_out, not_154_out, not_155_out, not_156_out, not_157_out, not_158_out, not_159_out, not_160_out, not_161_out, not_162_out);
  and and_25 (and_25_out, not_163_out, not_164_out, not_165_out, not_166_out, not_167_out, not_168_out, not_169_out, not_170_out, not_171_out, not_172_out, F1, F0);
  and and_26 (and_26_out, not_173_out, not_174_out, not_175_out, not_176_out, not_177_out, not_178_out, not_179_out, not_180_out, not_181_out, not_182_out, F1, not_183_out);
  and and_27 (and_27_out, not_184_out, not_185_out, not_186_out, not_187_out, not_188_out, not_189_out, F5, not_190_out, not_191_out, not_192_out, not_193_out, not_194_out);
  and and_28 (and_28_out, not_195_out, not_196_out, not_197_out, not_198_out, not_199_out, not_200_out, F5, not_201_out, not_202_out, not_203_out, not_204_out, F0);
  and and_29 (and_29_out, not_205_out, not_206_out, not_207_out, not_208_out, not_209_out, not_210_out, F5, not_211_out, not_212_out, not_213_out, F1, not_214_out);
  and and_30 (and_30_out, not_215_out, not_216_out, not_217_out, not_218_out, not_219_out, not_220_out, F5, not_221_out, not_222_out, F2, not_223_out, not_224_out);
  and and_31 (and_31_out, not_225_out, not_226_out, not_227_out, not_228_out, not_229_out, not_230_out, F5, not_231_out, not_232_out, F2, not_233_out, F0);
  and and_32 (and_32_out, not_234_out, not_235_out, not_236_out, not_237_out, not_238_out, not_239_out, F5, not_240_out, not_241_out, F2, F1, F0);
  and and_33 (and_33_out, not_242_out, not_243_out, not_244_out, not_245_out, not_246_out, not_247_out, F5, not_248_out, F3, not_249_out, F1, not_250_out);
  and and_34 (and_34_out, not_251_out, not_252_out, not_253_out, not_254_out, not_255_out, not_256_out, F5, not_257_out, F3, not_258_out, F1, F0);
  and and_35 (and_35_out, not_259_out, not_260_out, not_261_out, not_262_out, not_263_out, not_264_out, not_265_out, not_266_out, F3, F2, not_267_out, not_268_out);
  and and_36 (and_36_out, not_269_out, not_270_out, not_271_out, OP2, not_272_out, not_273_out);
  and and_37 (and_37_out, not_274_out, not_275_out, not_276_out, OP2, not_277_out, OP0);
  and and_38 (and_38_out, OP5, not_278_out, OP3, not_279_out, OP1, OP0);
  and and_39 (and_39_out, not_280_out, not_281_out, not_282_out, not_283_out, not_284_out, not_285_out, F5, not_286_out, not_287_out, F2, F1, not_288_out);
  and and_40 (and_40_out, not_289_out, not_290_out, not_291_out, OP2, OP1, not_292_out);
  or or_1 (R1_Used, and_1_out, and_2_out, and_3_out, and_4_out, and_5_out, and_6_out, and_7_out, and_8_out, and_9_out, and_10_out, and_11_out, and_12_out, and_13_out, and_14_out, and_15_out, and_16_out, and_17_out, and_18_out, and_19_out, and_20_out, and_21_out, and_22_out, and_23_out);
  or or_2 (R2_Used, and_24_out, and_25_out, and_26_out, and_27_out, and_28_out, and_29_out, and_30_out, and_31_out, and_32_out, and_33_out, and_34_out, and_35_out, and_36_out, and_37_out, and_38_out, and_39_out, and_40_out);
endmodule

module \数据相关检测  (
  input  [4:0] R1_num,
  input  [4:0] R2_num,
  input  R1_Used,
  input  R2_Used,
  input  [4:0] EX_WriteReg_num,
  input  EX_RegWrite,
  input  [4:0] MEM_WriteReg_num,
  input  [4:0] WB_WriteReg_num,
  input  MEM_RegWrite,
  input  WB_RegWrite,
  output \数据相关 
);

  wire comparator_3_eq, comparator_5_eq, comparator_6_eq, or_1_out, or_3_out, pull_resistor_1_node,
       pull_resistor_2_node, pull_resistor_4_node;
  wire [4:0] \数据相关条件_1_out_3 , \数据相关条件_2_out_3 , \数据相关条件_3_out_3 , \数据相关条件_4_out_3 , \数据相关条件_5_out_3 ;

  \数据相关条件  \u_数据相关条件_1  (.R(EX_RegWrite), .R_num(EX_WriteReg_num), .out_3(\数据相关条件_1_out_3 ));
  \数据相关条件  \u_数据相关条件_2  (.R(MEM_RegWrite), .R_num(MEM_WriteReg_num), .out_3(\数据相关条件_2_out_3 ));
  \数据相关条件  \u_数据相关条件_3  (.R(R1_Used), .R_num(R1_num), .out_3(\数据相关条件_3_out_3 ));
  Pull_Resistor #(.pull(0)) pull_resistor_1 (.node(pull_resistor_1_node));
  Comparator #(.width(5), .mode("twosComplement")) comparator_1 (
    .a(\数据相关条件_3_out_3 ), .b(\数据相关条件_1_out_3 ), .eq(pull_resistor_1_node));  // open: gt, lt
  Pull_Resistor #(.pull(0)) pull_resistor_2 (.node(pull_resistor_2_node));
  Comparator #(.width(5), .mode("twosComplement")) comparator_2 (
    .a(\数据相关条件_3_out_3 ), .b(\数据相关条件_2_out_3 ), .eq(pull_resistor_2_node));  // open: gt, lt
  or or_1 (or_1_out, pull_resistor_2_node, pull_resistor_1_node);
  \数据相关条件  \u_数据相关条件_4  (.R(R2_Used), .R_num(R2_num), .out_3(\数据相关条件_4_out_3 ));
  or or_2 (\数据相关 , or_1_out, or_3_out);
  Comparator #(.width(5), .mode("twosComplement")) comparator_3 (
    .a(\数据相关条件_4_out_3 ), .b(\数据相关条件_1_out_3 ), .eq(comparator_3_eq));  // open: gt, lt
  Pull_Resistor #(.pull(0)) pull_resistor_3 (.node(comparator_3_eq));
  Pull_Resistor #(.pull(0)) pull_resistor_4 (.node(pull_resistor_4_node));
  Comparator #(.width(5), .mode("twosComplement")) comparator_4 (
    .a(\数据相关条件_4_out_3 ), .b(\数据相关条件_2_out_3 ), .eq(pull_resistor_4_node));  // open: gt, lt
  or or_3 (or_3_out, pull_resistor_4_node, comparator_3_eq);
  \数据相关条件  \u_数据相关条件_5  (.R(WB_RegWrite), .R_num(WB_WriteReg_num), .out_3(\数据相关条件_5_out_3 ));
  Comparator #(.width(5), .mode("twosComplement")) comparator_5 (
    .b(\数据相关条件_5_out_3 ), .eq(comparator_5_eq));  // open: a, gt, lt
  Pull_Resistor #(.pull(0)) pull_resistor_5 (.node(comparator_5_eq));
  Comparator #(.width(5), .mode("twosComplement")) comparator_6 (
    .b(\数据相关条件_5_out_3 ), .eq(comparator_6_eq));  // open: a, gt, lt
  Pull_Resistor #(.pull(0)) pull_resistor_6 (.node(comparator_6_eq));
endmodule

module \数据相关条件  (
  input  [4:0] R_num,
  input  R,
  output [4:0] out_3
);

  wire and_1_out, comparator_1_eq;

  and and_1 (and_1_out, R, ~comparator_1_eq);  // AND_Gate
  assign out_3 = and_1_out ? R_num : 5'bz;  // Controlled_Buffer controlled_buffer_1
  Comparator #(.width(5), .mode("twosComplement")) comparator_1 (
    .a(R_num), .b({5{1'b0}}), .eq(comparator_1_eq));  // open: gt, lt
endmodule

module MIPS_Regfille_falling (
  input  [31:0] Din,
  input  Clk,
  input  WE,
  input  [4:0] R1_num,
  input  [4:0] W_num,
  input  [4:0] R2_num,
  output [31:0] R1,
  output [31:0] R2
);

  // RegisterFile registerfile_1: pin names not known; wires that end beside it: Din, Clk, WE, W_num, R1_num, R2_num, R1, R2
endmodule

module \访存相关  (
  input  [4:0] R1_num,
  input  R1,
  input  [4:0] R2_num,
  input  R2,
  input  [4:0] EXRegWrite_num,
  input  EXRegWrite,
  output \访存相关 
);

  wire comparator_1_eq, comparator_2_eq;
  wire [4:0] \数据相关条件_1_out_3 , \数据相关条件_2_out_3 , \数据相关条件_3_out_3 ;

  \数据相关条件  \u_数据相关条件_1  (.R(R1), .R_num(R1_num), .out_3(\数据相关条件_1_out_3 ));
  \数据相关条件  \u_数据相关条件_2  (.R(R2), .R_num(R2_num), .out_3(\数据相关条件_2_out_3 ));
  \数据相关条件  \u_数据相关条件_3  (.R(EXRegWrite), .R_num(EXRegWrite_num), .out_3(\数据相关条件_3_out_3 ));
  Comparator #(.width(5), .mode("twosComplement")) comparator_1 (
    .a(\数据相关条件_1_out_3 ), .b(\数据相关条件_3_out_3 ), .eq(comparator_1_eq));  // open: gt, lt
  Comparator #(.width(5), .mode("twosComplement")) comparator_2 (
    .a(\数据相关条件_2_out_3 ), .b(\数据相关条件_3_out_3 ), .eq(comparator_2_eq));  // open: gt, lt
  Pull_Resistor #(.pull(0)) pull_resistor_1 (.node(comparator_1_eq));
  Pull_Resistor #(.pull(0)) pull_resistor_2 (.node(comparator_2_eq));
  or or_1 (\访存相关 , comparator_1_eq, comparator_2_eq);
endmodule

module Forward (
  input  [4:0] R1_num,
  input  R1,
  input  [4:0] R2_num,
  input  R2,
  input  [4:0] ExRegWrite_num,
  input  ExRegWrite,
  input  [4:0] MemRegWrite_num,
  input  MemRegWrite,
  output [1:0] Forward1,
  output [1:0] Forward2
);

  wire comparator_3_eq, comparator_4_eq, pull_resistor_1_node, pull_resistor_2_node;
  wire [4:0] \数据相关条件_1_out_3 , \数据相关条件_2_out_3 , \数据相关条件_3_out_3 , \数据相关条件_4_out_3 ;

  \数据相关条件  \u_数据相关条件_1  (.R(R1), .R_num(R1_num), .out_3(\数据相关条件_1_out_3 ));
  \数据相关条件  \u_数据相关条件_2  (.R(R2), .R_num(R2_num), .out_3(\数据相关条件_2_out_3 ));
  \数据相关条件  \u_数据相关条件_3  (.R(ExRegWrite), .R_num(ExRegWrite_num), .out_3(\数据相关条件_3_out_3 ));
  \数据相关条件  \u_数据相关条件_4  (.R(MemRegWrite), .R_num(MemRegWrite_num), .out_3(\数据相关条件_4_out_3 ));
  Pull_Resistor #(.pull(0)) pull_resistor_1 (.node(pull_resistor_1_node));
  Comparator #(.width(5), .mode("twosComplement")) comparator_1 (
    .a(\数据相关条件_1_out_3 ), .b(\数据相关条件_3_out_3 ), .eq(pull_resistor_1_node));  // open: gt, lt
  Pull_Resistor #(.pull(0)) pull_resistor_2 (.node(pull_resistor_2_node));
  Comparator #(.width(5), .mode("twosComplement")) comparator_2 (
    .a(\数据相关条件_1_out_3 ), .b(\数据相关条件_4_out_3 ), .eq(pull_resistor_2_node));  // open: gt, lt
  Comparator #(.width(5), .mode("twosComplement")) comparator_3 (
    .a(\数据相关条件_2_out_3 ), .b(\数据相关条件_3_out_3 ), .eq(comparator_3_eq));  // open: gt, lt
  Comparator #(.width(5), .mode("twosComplement")) comparator_4 (
    .a(\数据相关条件_2_out_3 ), .b(\数据相关条件_4_out_3 ), .eq(comparator_4_eq));  // open: gt, lt
  Pull_Resistor #(.pull(0)) pull_resistor_3 (.node(comparator_3_eq));
  Pull_Resistor #(.pull(0)) pull_resistor_4 (.node(comparator_4_eq));
  Priority_Encoder #(.select(2), .disabled("Z")) priority_encoder_1 (
    .in0(1'b1), .in1(pull_resistor_2_node), .in2(pull_resistor_1_node), .out(Forward1));  // open: in3, gs, en_out, en_in
  Priority_Encoder #(.select(2), .disabled("Z")) priority_encoder_2 (
    .in0(1'b1), .in1(comparator_4_eq), .in2(comparator_3_eq), .out(Forward2));  // open: in3, gs, en_out, en_in
endmodule

module \解析pte  (
  input  [31:0] pte,
  output R,
  output W,
  output X,
  output U,
  output [5:0] ppn
);


  assign ppn = pte[5:0];
  assign R = pte[9];
  assign U = pte[6];
  assign W = pte[8];
  assign X = pte[7];

  // Notes on the sheet:
  //   PTE定义：0..5 ppn, 6 U, 7 X, 8 W, 9 R
endmodule

module \satp解析  (
  input  [31:0] pte,
  output [2:0] \地址空间参数 ,
  output mode,
  output [5:0] ppn
);


  assign mode = pte[9];
  assign ppn = pte[5:0];
  assign \地址空间参数  = pte[8:6];

  // Notes on the sheet:
  //   satp定义：0..5 ppn, 6..8 地址空间参数, 9 模式
endmodule

module \虚拟地址解析  (
  input  [9:0] VA,
  output [3:0] offset,
  output [2:0] vpn_2,
  output [2:0] vpn_1
);


  assign offset = VA[3:0];
  assign vpn_1 = VA[9:7];
  assign vpn_2 = VA[6:4];

  // Notes on the sheet:
  //   低 4 位为偏移量
  //   虚拟地址
  //   高 6 位为虚拟页号
endmodule

module TLB (
  input  [31:0] VPN_Missed,
  input  in_2,
  input  clk,
  input  [5:0] VPN,
  output [5:0] PPN,
  output miss
);

  wire and_1_out, and_2_out, and_3_out, and_4_out, comparator_1_eq, comparator_2_eq, comparator_3_eq,
       comparator_4_eq, demultiplexer_1_out0, demultiplexer_1_out1, demultiplexer_1_out2,
       demultiplexer_1_out3, or_1_out, \有效位_1_out_2 , \有效位_2_out_2 , \有效位_3_out_2 , \有效位_4_out_2 ;
  wire [1:0] Addr, counter_1_q;
  wire [31:0] ram_1_data, ram_2_data, ram_3_data, ram_4_data;

  Demultiplexer #(.select(2), .width(1), .tristate("false"), .disabled("Z"), .enable("true")) demultiplexer_1 (
    .out0(demultiplexer_1_out0), .out1(demultiplexer_1_out1), .out2(demultiplexer_1_out2),
    .out3(demultiplexer_1_out3), .in(in_2), .sel(counter_1_q), .en(1'b1));
  Counter #(.width(2), .max('h3), .ongoal("wrap"), .trigger("rising"), .behavior("new")) counter_1 (
    .Q(counter_1_q), .clk(clk));  // open: load, D, count, carry, clr, preset, down
  RAM #(.addrWidth(2), .dataWidth(32), .bus("separate"), .Select("high")) ram_1 (
    .addr(2'b00), .din(VPN_Missed), .data(ram_1_data), .str(demultiplexer_1_out0), .clk(clk));  // open: sel, ld, clr
  RAM #(.addrWidth(2), .dataWidth(32), .bus("separate"), .Select("high")) ram_2 (
    .addr(2'b01), .din(VPN_Missed), .data(ram_2_data), .str(demultiplexer_1_out1), .clk(clk));  // open: sel, ld, clr
  RAM #(.addrWidth(2), .dataWidth(32), .bus("separate"), .Select("high")) ram_3 (
    .addr(2'b10), .din(VPN_Missed), .data(ram_3_data), .str(demultiplexer_1_out2), .clk(clk));  // open: sel, ld, clr
  RAM #(.addrWidth(2), .dataWidth(32), .bus("separate"), .Select("high")) ram_4 (
    .addr(2'b11), .din(VPN_Missed), .data(ram_4_data), .str(demultiplexer_1_out3), .clk(clk));  // open: sel, ld, clr
  \有效位  \u_有效位_1  (.in_1(demultiplexer_1_out0), .out_2(\有效位_1_out_2 ));
  \有效位  \u_有效位_2  (.in_1(demultiplexer_1_out1), .out_2(\有效位_2_out_2 ));
  \有效位  \u_有效位_3  (.in_1(demultiplexer_1_out2), .out_2(\有效位_3_out_2 ));
  \有效位  \u_有效位_4  (.in_1(demultiplexer_1_out3), .out_2(\有效位_4_out_2 ));
  Comparator #(.width(6), .mode("twosComplement")) comparator_1 (
    .a(ram_1_data[11:6]), .b(VPN), .eq(comparator_1_eq));  // open: gt, lt
  and and_1 (and_1_out, comparator_1_eq, \有效位_1_out_2 );
  Comparator #(.width(6), .mode("twosComplement")) comparator_2 (
    .a(ram_2_data[11:6]), .b(VPN), .eq(comparator_2_eq));  // open: gt, lt
  and and_2 (and_2_out, comparator_2_eq, \有效位_2_out_2 );
  Comparator #(.width(6), .mode("twosComplement")) comparator_3 (
    .a(ram_3_data[11:6]), .b(VPN), .eq(comparator_3_eq));  // open: gt, lt
  and and_3 (and_3_out, comparator_3_eq, \有效位_3_out_2 );
  Comparator #(.width(6), .mode("twosComplement")) comparator_4 (
    .a(ram_4_data[11:6]), .b(VPN), .eq(comparator_4_eq));  // open: gt, lt
  Multiplexer #(.select(2), .width(6), .disabled("Z"), .enable("true")) multiplexer_1 (
    .in0(ram_1_data[5:0]), .in1(ram_2_data[5:0]), .in2(ram_3_data[5:0]), .in3(ram_4_data[5:0]), .out(PPN),
    .sel(Addr));  // open: en
  and and_4 (and_4_out, comparator_4_eq, \有效位_4_out_2 );
  or or_1 (or_1_out, and_1_out, and_2_out, and_3_out, and_4_out);
  \编码器  \u_编码器_1  (.a(and_1_out), .b(and_2_out), .c(and_3_out), .d(and_4_out), .x(Addr[0]), .y(Addr[1]));
  not not_1 (miss, or_1_out);
endmodule

module \编码器  (
  input  a,
  input  b,
  input  c,
  input  d,
  output x,
  output y
);

  or or_1 (x, d, c);
  or or_2 (y, d, b, a);
endmodule

module \有效位  (
  input  in_1,
  output out_2
);

  wire d_ff_1_qn;

  D_Flip_Flop #(.trigger("rising"), .Pre_Clr_Positions("ABOVE_BELOW"), .NegatePresetClear("false"), .enable("false"), .NewFFLayout("true")) d_ff_1 (
    .clk(in_1), .D(d_ff_1_qn), .Q(out_2), .Qn(d_ff_1_qn), .preset(out_2));  // open: reset
endmodule
